// Logisim project barrel shift.circ as structural Verilog: 1 circuit, main circuit main
module main (
  input  [31:0] in_1,
  input  in_2,
  input  b2,
  input  b1,
  input  b0,
  output [31:0] out_6
);

  wire multiplexer_1_out, multiplexer_2_out, multiplexer_3_out, multiplexer_4_out, multiplexer_7_out,
       multiplexer_8_out, multiplexer_10_out, multiplexer_11_out, multiplexer_12_out, multiplexer_13_out,
       multiplexer_16_out, multiplexer_17_out, multiplexer_18_out, multiplexer_19_out, multiplexer_21_out,
       multiplexer_22_out, multiplexer_25_out, multiplexer_26_out, multiplexer_27_out, multiplexer_28_out,
       multiplexer_31_out, multiplexer_32_out, multiplexer_34_out, multiplexer_35_out, multiplexer_36_out,
       multiplexer_37_out, multiplexer_40_out, multiplexer_41_out, multiplexer_42_out, multiplexer_43_out,
       multiplexer_45_out, multiplexer_46_out, multiplexer_49_out, multiplexer_50_out, multiplexer_51_out,
       multiplexer_52_out, multiplexer_55_out, multiplexer_56_out, multiplexer_58_out, multiplexer_59_out,
       multiplexer_60_out, multiplexer_61_out, multiplexer_64_out, multiplexer_65_out, multiplexer_66_out,
       multiplexer_67_out, multiplexer_69_out, multiplexer_70_out, multiplexer_73_out, multiplexer_74_out,
       multiplexer_75_out, multiplexer_76_out, multiplexer_79_out, multiplexer_80_out, multiplexer_82_out,
       multiplexer_83_out, multiplexer_84_out, multiplexer_85_out, multiplexer_88_out, multiplexer_89_out,
       multiplexer_90_out, multiplexer_91_out, multiplexer_93_out, multiplexer_94_out;

  Multiplexer #(.enable("false")) multiplexer_1 (.in0(in_1[30]), .in1(in_2), .out(multiplexer_1_out), .sel(b2));
  Multiplexer #(.enable("false")) multiplexer_2 (.in0(in_1[31]), .in1(in_2), .out(multiplexer_2_out), .sel(b2));
  Multiplexer #(.enable("false")) multiplexer_3 (
    .in0(multiplexer_2_out), .in1(in_2), .out(multiplexer_3_out), .sel(b1));
  Multiplexer #(.enable("false")) multiplexer_4 (
    .in0(multiplexer_1_out), .in1(in_2), .out(multiplexer_4_out), .sel(b1));
  Multiplexer #(.enable("false")) multiplexer_5 (
    .in0(multiplexer_4_out), .in1(multiplexer_3_out), .out(out_6[30]), .sel(b0));
  Multiplexer #(.enable("false")) multiplexer_6 (.in0(multiplexer_3_out), .in1(in_2), .out(out_6[31]), .sel(b0));
  Multiplexer #(.enable("false")) multiplexer_7 (.in0(in_1[29]), .in1(in_2), .out(multiplexer_7_out), .sel(b2));
  Multiplexer #(.enable("false")) multiplexer_8 (
    .in0(multiplexer_7_out), .in1(multiplexer_2_out), .out(multiplexer_8_out), .sel(b1));
  Multiplexer #(.enable("false")) multiplexer_9 (
    .in0(multiplexer_8_out), .in1(multiplexer_4_out), .out(out_6[29]), .sel(b0));
  Multiplexer #(.enable("false")) multiplexer_10 (.in0(in_1[27]), .in1(in_1[31]), .out(multiplexer_10_out), .sel(b2));
  Multiplexer #(.enable("false")) multiplexer_11 (.in0(in_1[28]), .in1(in_2), .out(multiplexer_11_out), .sel(b2));
  Multiplexer #(.enable("false")) multiplexer_12 (
    .in0(multiplexer_10_out), .in1(multiplexer_7_out), .out(multiplexer_12_out), .sel(b1));
  Multiplexer #(.enable("false")) multiplexer_13 (
    .in0(multiplexer_11_out), .in1(multiplexer_1_out), .out(multiplexer_13_out), .sel(b1));
  Multiplexer #(.enable("false")) multiplexer_14 (
    .in0(multiplexer_12_out), .in1(multiplexer_13_out), .out(out_6[27]), .sel(b0));
  Multiplexer #(.enable("false")) multiplexer_15 (
    .in0(multiplexer_13_out), .in1(multiplexer_8_out), .out(out_6[28]), .sel(b0));
  Multiplexer #(.enable("false")) multiplexer_16 (.in0(in_1[26]), .in1(in_1[30]), .out(multiplexer_16_out), .sel(b2));
  Multiplexer #(.enable("false")) multiplexer_17 (.in0(in_1[25]), .in1(in_1[29]), .out(multiplexer_17_out), .sel(b2));
  Multiplexer #(.enable("false")) multiplexer_18 (
    .in0(multiplexer_17_out), .in1(multiplexer_10_out), .out(multiplexer_18_out), .sel(b1));
  Multiplexer #(.enable("false")) multiplexer_19 (
    .in0(multiplexer_16_out), .in1(multiplexer_11_out), .out(multiplexer_19_out), .sel(b1));
  Multiplexer #(.enable("false")) multiplexer_20 (
    .in0(multiplexer_19_out), .in1(multiplexer_12_out), .out(out_6[26]), .sel(b0));
  Multiplexer #(.enable("false")) multiplexer_21 (.in0(in_1[24]), .in1(in_1[28]), .out(multiplexer_21_out), .sel(b2));
  Multiplexer #(.enable("false")) multiplexer_22 (
    .in0(multiplexer_21_out), .in1(multiplexer_16_out), .out(multiplexer_22_out), .sel(b1));
  Multiplexer #(.enable("false")) multiplexer_23 (
    .in0(multiplexer_22_out), .in1(multiplexer_18_out), .out(out_6[24]), .sel(b0));
  Multiplexer #(.enable("false")) multiplexer_24 (
    .in0(multiplexer_18_out), .in1(multiplexer_19_out), .out(out_6[25]), .sel(b0));
  Multiplexer #(.enable("false")) multiplexer_25 (.in0(in_1[22]), .in1(in_1[26]), .out(multiplexer_25_out), .sel(b2));
  Multiplexer #(.enable("false")) multiplexer_26 (.in0(in_1[23]), .in1(in_1[27]), .out(multiplexer_26_out), .sel(b2));
  Multiplexer #(.enable("false")) multiplexer_27 (
    .in0(multiplexer_25_out), .in1(multiplexer_21_out), .out(multiplexer_27_out), .sel(b1));
  Multiplexer #(.enable("false")) multiplexer_28 (
    .in0(multiplexer_26_out), .in1(multiplexer_17_out), .out(multiplexer_28_out), .sel(b1));
  Multiplexer #(.enable("false")) multiplexer_29 (
    .in0(multiplexer_27_out), .in1(multiplexer_28_out), .out(out_6[22]), .sel(b0));
  Multiplexer #(.enable("false")) multiplexer_30 (
    .in0(multiplexer_28_out), .in1(multiplexer_22_out), .out(out_6[23]), .sel(b0));
  Multiplexer #(.enable("false")) multiplexer_31 (.in0(in_1[21]), .in1(in_1[25]), .out(multiplexer_31_out), .sel(b2));
  Multiplexer #(.enable("false")) multiplexer_32 (
    .in0(multiplexer_31_out), .in1(multiplexer_26_out), .out(multiplexer_32_out), .sel(b1));
  Multiplexer #(.enable("false")) multiplexer_33 (
    .in0(multiplexer_32_out), .in1(multiplexer_27_out), .out(out_6[21]), .sel(b0));
  Multiplexer #(.enable("false")) multiplexer_34 (.in0(in_1[20]), .in1(in_1[24]), .out(multiplexer_34_out), .sel(b2));
  Multiplexer #(.enable("false")) multiplexer_35 (.in0(in_1[19]), .in1(in_1[23]), .out(multiplexer_35_out), .sel(b2));
  Multiplexer #(.enable("false")) multiplexer_36 (
    .in0(multiplexer_34_out), .in1(multiplexer_25_out), .out(multiplexer_36_out), .sel(b1));
  Multiplexer #(.enable("false")) multiplexer_37 (
    .in0(multiplexer_35_out), .in1(multiplexer_31_out), .out(multiplexer_37_out), .sel(b1));
  Multiplexer #(.enable("false")) multiplexer_38 (
    .in0(multiplexer_36_out), .in1(multiplexer_32_out), .out(out_6[20]), .sel(b0));
  Multiplexer #(.enable("false")) multiplexer_39 (
    .in0(multiplexer_37_out), .in1(multiplexer_36_out), .out(out_6[19]), .sel(b0));
  Multiplexer #(.enable("false")) multiplexer_40 (.in0(in_1[17]), .in1(in_1[21]), .out(multiplexer_40_out), .sel(b2));
  Multiplexer #(.enable("false")) multiplexer_41 (.in0(in_1[18]), .in1(in_1[22]), .out(multiplexer_41_out), .sel(b2));
  Multiplexer #(.enable("false")) multiplexer_42 (
    .in0(multiplexer_41_out), .in1(multiplexer_34_out), .out(multiplexer_42_out), .sel(b1));
  Multiplexer #(.enable("false")) multiplexer_43 (
    .in0(multiplexer_40_out), .in1(multiplexer_35_out), .out(multiplexer_43_out), .sel(b1));
  Multiplexer #(.enable("false")) multiplexer_44 (
    .in0(multiplexer_42_out), .in1(multiplexer_37_out), .out(out_6[18]), .sel(b0));
  Multiplexer #(.enable("false")) multiplexer_45 (.in0(in_1[16]), .in1(in_1[20]), .out(multiplexer_45_out), .sel(b2));
  Multiplexer #(.enable("false")) multiplexer_46 (
    .in0(multiplexer_45_out), .in1(multiplexer_41_out), .out(multiplexer_46_out), .sel(b1));
  Multiplexer #(.enable("false")) multiplexer_47 (
    .in0(multiplexer_43_out), .in1(multiplexer_42_out), .out(out_6[17]), .sel(b0));
  Multiplexer #(.enable("false")) multiplexer_48 (
    .in0(multiplexer_46_out), .in1(multiplexer_43_out), .out(out_6[16]), .sel(b0));
  Multiplexer #(.enable("false")) multiplexer_49 (.in0(in_1[15]), .in1(in_1[19]), .out(multiplexer_49_out), .sel(b2));
  Multiplexer #(.enable("false")) multiplexer_50 (.in0(in_1[14]), .in1(in_1[18]), .out(multiplexer_50_out), .sel(b2));
  Multiplexer #(.enable("false")) multiplexer_51 (
    .in0(multiplexer_50_out), .in1(multiplexer_45_out), .out(multiplexer_51_out), .sel(b1));
  Multiplexer #(.enable("false")) multiplexer_52 (
    .in0(multiplexer_49_out), .in1(multiplexer_40_out), .out(multiplexer_52_out), .sel(b1));
  Multiplexer #(.enable("false")) multiplexer_53 (
    .in0(multiplexer_51_out), .in1(multiplexer_52_out), .out(out_6[14]), .sel(b0));
  Multiplexer #(.enable("false")) multiplexer_54 (
    .in0(multiplexer_52_out), .in1(multiplexer_46_out), .out(out_6[15]), .sel(b0));
  Multiplexer #(.enable("false")) multiplexer_55 (.in0(in_1[13]), .in1(in_1[17]), .out(multiplexer_55_out), .sel(b2));
  Multiplexer #(.enable("false")) multiplexer_56 (
    .in0(multiplexer_55_out), .in1(multiplexer_49_out), .out(multiplexer_56_out), .sel(b1));
  Multiplexer #(.enable("false")) multiplexer_57 (
    .in0(multiplexer_56_out), .in1(multiplexer_51_out), .out(out_6[13]), .sel(b0));
  Multiplexer #(.enable("false")) multiplexer_58 (.in0(in_1[11]), .in1(in_1[15]), .out(multiplexer_58_out), .sel(b2));
  Multiplexer #(.enable("false")) multiplexer_59 (.in0(in_1[12]), .in1(in_1[16]), .out(multiplexer_59_out), .sel(b2));
  Multiplexer #(.enable("false")) multiplexer_60 (
    .in0(multiplexer_58_out), .in1(multiplexer_55_out), .out(multiplexer_60_out), .sel(b1));
  Multiplexer #(.enable("false")) multiplexer_61 (
    .in0(multiplexer_59_out), .in1(multiplexer_50_out), .out(multiplexer_61_out), .sel(b1));
  Multiplexer #(.enable("false")) multiplexer_62 (
    .in0(multiplexer_61_out), .in1(multiplexer_56_out), .out(out_6[12]), .sel(b0));
  Multiplexer #(.enable("false")) multiplexer_63 (
    .in0(multiplexer_60_out), .in1(multiplexer_61_out), .out(out_6[11]), .sel(b0));
  Multiplexer #(.enable("false")) multiplexer_64 (.in0(in_1[9]), .in1(in_1[13]), .out(multiplexer_64_out), .sel(b2));
  Multiplexer #(.enable("false")) multiplexer_65 (.in0(in_1[10]), .in1(in_1[14]), .out(multiplexer_65_out), .sel(b2));
  Multiplexer #(.enable("false")) multiplexer_66 (
    .in0(multiplexer_65_out), .in1(multiplexer_59_out), .out(multiplexer_66_out), .sel(b1));
  Multiplexer #(.enable("false")) multiplexer_67 (
    .in0(multiplexer_64_out), .in1(multiplexer_58_out), .out(multiplexer_67_out), .sel(b1));
  Multiplexer #(.enable("false")) multiplexer_68 (
    .in0(multiplexer_66_out), .in1(multiplexer_60_out), .out(out_6[10]), .sel(b0));
  Multiplexer #(.enable("false")) multiplexer_69 (.in0(in_1[8]), .in1(in_1[12]), .out(multiplexer_69_out), .sel(b2));
  Multiplexer #(.enable("false")) multiplexer_70 (
    .in0(multiplexer_69_out), .in1(multiplexer_65_out), .out(multiplexer_70_out), .sel(b1));
  Multiplexer #(.enable("false")) multiplexer_71 (
    .in0(multiplexer_67_out), .in1(multiplexer_66_out), .out(out_6[9]), .sel(b0));
  Multiplexer #(.enable("false")) multiplexer_72 (
    .in0(multiplexer_70_out), .in1(multiplexer_67_out), .out(out_6[8]), .sel(b0));
  Multiplexer #(.enable("false")) multiplexer_73 (.in0(in_1[6]), .in1(in_1[10]), .out(multiplexer_73_out), .sel(b2));
  Multiplexer #(.enable("false")) multiplexer_74 (.in0(in_1[7]), .in1(in_1[11]), .out(multiplexer_74_out), .sel(b2));
  Multiplexer #(.enable("false")) multiplexer_75 (
    .in0(multiplexer_73_out), .in1(multiplexer_69_out), .out(multiplexer_75_out), .sel(b1));
  Multiplexer #(.enable("false")) multiplexer_76 (
    .in0(multiplexer_74_out), .in1(multiplexer_64_out), .out(multiplexer_76_out), .sel(b1));
  Multiplexer #(.enable("false")) multiplexer_77 (
    .in0(multiplexer_76_out), .in1(multiplexer_70_out), .out(out_6[7]), .sel(b0));
  Multiplexer #(.enable("false")) multiplexer_78 (
    .in0(multiplexer_75_out), .in1(multiplexer_76_out), .out(out_6[6]), .sel(b0));
  Multiplexer #(.enable("false")) multiplexer_79 (.in0(in_1[5]), .in1(in_1[9]), .out(multiplexer_79_out), .sel(b2));
  Multiplexer #(.enable("false")) multiplexer_80 (
    .in0(multiplexer_79_out), .in1(multiplexer_74_out), .out(multiplexer_80_out), .sel(b1));
  Multiplexer #(.enable("false")) multiplexer_81 (
    .in0(multiplexer_80_out), .in1(multiplexer_75_out), .out(out_6[5]), .sel(b0));
  Multiplexer #(.enable("false")) multiplexer_82 (.in0(in_1[4]), .in1(in_1[8]), .out(multiplexer_82_out), .sel(b2));
  Multiplexer #(.enable("false")) multiplexer_83 (.in0(in_1[3]), .in1(in_1[7]), .out(multiplexer_83_out), .sel(b2));
  Multiplexer #(.enable("false")) multiplexer_84 (
    .in0(multiplexer_82_out), .in1(multiplexer_73_out), .out(multiplexer_84_out), .sel(b1));
  Multiplexer #(.enable("false")) multiplexer_85 (
    .in0(multiplexer_83_out), .in1(multiplexer_79_out), .out(multiplexer_85_out), .sel(b1));
  Multiplexer #(.enable("false")) multiplexer_86 (
    .in0(multiplexer_85_out), .in1(multiplexer_84_out), .out(out_6[3]), .sel(b0));
  Multiplexer #(.enable("false")) multiplexer_87 (
    .in0(multiplexer_84_out), .in1(multiplexer_80_out), .out(out_6[4]), .sel(b0));
  Multiplexer #(.enable("false")) multiplexer_88 (.in0(in_1[2]), .in1(in_1[6]), .out(multiplexer_88_out), .sel(b2));
  Multiplexer #(.enable("false")) multiplexer_89 (.in0(in_1[1]), .in1(in_1[5]), .out(multiplexer_89_out), .sel(b2));
  Multiplexer #(.enable("false")) multiplexer_90 (
    .in0(multiplexer_88_out), .in1(multiplexer_82_out), .out(multiplexer_90_out), .sel(b1));
  Multiplexer #(.enable("false")) multiplexer_91 (
    .in0(multiplexer_89_out), .in1(multiplexer_83_out), .out(multiplexer_91_out), .sel(b1));
  Multiplexer #(.enable("false")) multiplexer_92 (
    .in0(multiplexer_90_out), .in1(multiplexer_85_out), .out(out_6[2]), .sel(b0));
  Multiplexer #(.enable("false")) multiplexer_93 (.in0(in_1[0]), .in1(in_1[4]), .out(multiplexer_93_out), .sel(b2));
  Multiplexer #(.enable("false")) multiplexer_94 (
    .in0(multiplexer_93_out), .in1(multiplexer_88_out), .out(multiplexer_94_out), .sel(b1));
  Multiplexer #(.enable("false")) multiplexer_95 (
    .in0(multiplexer_91_out), .in1(multiplexer_90_out), .out(out_6[1]), .sel(b0));
  Multiplexer #(.enable("false")) multiplexer_96 (
    .in0(multiplexer_94_out), .in1(multiplexer_91_out), .out(out_6[0]), .sel(b0));
endmodule
