// Logisim project processador_32bits.circ as structural Verilog: 13 circuits, main circuit celula operacoes
module via_de_dados (
  input  reset_banco,
  input  RESET,
  output [3:0] seletor_de_operacoes,
  output [4:0] \endereço_write ,
  output [4:0] op_reg_A,
  output overflow,
  output [4:0] op_reg_B
);

  wire and_1_out, and_2_out, and_3_out, clock_1_out, demultiplexer_1_out6, not_1_out, ULA_sao_iguais;
  wire [4:0] demultiplexer_1_out1, demultiplexer_2_out0, demultiplexer_2_out1, demultiplexer_2_out2,
       multiplexer_1_out;
  wire [9:0] IR_q_2;
  wire [21:19] IR_q;
  wire [31:0] banco_registrador_1_datareg_a, banco_registrador_1_datareg_b, barrel_shift_left_1_out_7,
       circular_shift_right_1_out_7, circular_shift_right__bit_sinal_1_out_7, multiplexer_2_out,
       multiplexer_3_out, pc_mem_1_memout, ULA_saida;

  not not_1 (not_1_out, clock_1_out);
  Clock clock_1 (.out(clock_1_out));
  Demultiplexer #(.select(3), .enable("false")) demultiplexer_1 (
    .out1(demultiplexer_1_out1[0]), .out2(demultiplexer_1_out1[1]), .out3(demultiplexer_1_out1[2]),
    .out4(demultiplexer_1_out1[3]), .out5(demultiplexer_1_out1[4]), .out6(demultiplexer_1_out6), .in(1'b1),
    .sel(op_reg_A[2:0]));  // open: out0, out7
  PC_MEM pc_mem_1 (
    .RESET(RESET), .MEMout(pc_mem_1_memout), .PC_CLK(clock_1_out), .estado_do_salto(IR_q_2),
    .saltar(and_3_out));
  Multiplexer #(.width(5), .enable("false")) multiplexer_1 (
    .in0(demultiplexer_1_out1), .in1({5{1'b1}}), .out(multiplexer_1_out), .sel(demultiplexer_1_out6));
  Register #(.width(32)) IR (
    .D(pc_mem_1_memout), .Q({IR_q_2, IR_q, op_reg_B, op_reg_A, \endereço_write , seletor_de_operacoes}),
    .clk(clock_1_out), .clr(RESET));  // open: en
  banco_registrador banco_registrador_1 (
    .DATA_IN(ULA_saida), .registrador_A(op_reg_A), .write(not_1_out), .\endereço_write (\endereço_write ),
    .registrador_B(op_reg_B), .DATAreg_A(banco_registrador_1_datareg_a),
    .DATAreg_B(banco_registrador_1_datareg_b), .clear(reset_banco));
  Demultiplexer #(.select(2), .width(5), .enable("false")) demultiplexer_2 (
    .out0(demultiplexer_2_out0), .out1(demultiplexer_2_out1), .out2(demultiplexer_2_out2),
    .in(multiplexer_1_out), .sel(op_reg_A[4:3]));  // open: out3
  Multiplexer #(.width(32), .enable("false")) multiplexer_2 (
    .in0(banco_registrador_1_datareg_b), .in1(barrel_shift_left_1_out_7), .out(multiplexer_2_out),
    .sel(and_1_out));
  barrel_shift_left barrel_shift_left_1 (
    .out_7(barrel_shift_left_1_out_7), .b2_desloca_16(demultiplexer_2_out0[0]),
    .b2_desloca_8(demultiplexer_2_out0[1]), .b2_desloca_4(demultiplexer_2_out0[2]),
    .b1_desloca_2(demultiplexer_2_out0[3]), .b0_desloca_1(demultiplexer_2_out0[4]),
    .in_1(circular_shift_right_1_out_7));
  and and_1 (and_1_out, ~seletor_de_operacoes[0], ~seletor_de_operacoes[1], seletor_de_operacoes[2], ~seletor_de_operacoes[3]);  // AND_Gate
  Circular_shift_right circular_shift_right_1 (
    .out_7(circular_shift_right_1_out_7), .b2_desloca_16(demultiplexer_2_out1[0]),
    .b2_desloca_8(demultiplexer_2_out1[1]), .b2_desloca_4(demultiplexer_2_out1[2]),
    .b1_desloca_2(demultiplexer_2_out1[3]), .b0_desloca_1(demultiplexer_2_out1[4]),
    .in_1(circular_shift_right__bit_sinal_1_out_7));
  circular_shift_right__bit_sinal circular_shift_right__bit_sinal_1 (
    .out_7(circular_shift_right__bit_sinal_1_out_7), .b2_desloca_16(demultiplexer_2_out2[0]),
    .b2_desloca_8(demultiplexer_2_out2[1]), .b2_desloca_4(demultiplexer_2_out2[2]),
    .b1_desloca_2(demultiplexer_2_out2[3]), .b0_desloca_1(demultiplexer_2_out2[4]),
    .in_1({{15{IR_q_2[9]}}, IR_q_2[8:0], IR_q, op_reg_B}));
  Multiplexer #(.width(32), .enable("false")) multiplexer_3 (
    .in0(banco_registrador_1_datareg_a), .in1({32{1'b0}}), .out(multiplexer_3_out), .sel(and_1_out));
  ULA ULA (
    .B(multiplexer_2_out), .saida(ULA_saida), .operador(seletor_de_operacoes), .overflow(overflow),
    .sao_iguais(ULA_sao_iguais), .A(multiplexer_3_out));
  and and_2 (and_2_out, ~seletor_de_operacoes[0], ~seletor_de_operacoes[1], ~seletor_de_operacoes[2], ~seletor_de_operacoes[3]);  // AND_Gate
  and and_3 (and_3_out, ULA_sao_iguais, and_2_out);

  // Notes on the sheet:
  //   op all Shift ->>
  //   write ->>
  //   Entrada de Dados externo ->>
  //   Banco
  //   ||
  //   <--Seleciona endereço da memoria ram
  //   <<-Barrel Shift
  //   <<-Circular Shift right
  //   endereco write
  //   op reg A
  //   op reg B
  //   _______________________________
  //   E
  //   _______________________________
  //   <<-Circular Shift right preservando sinal
  //   ||
  //   ||
  //   D
  //   ||
  //   ||
  //   B
  //   C
  //   ||
  //   A
  //   0 = and
  //   1 = or
  //   2 = xor
  //   3 = nand
  //   6 = subtrair
  //   7 = xnor
  //   Sistemas Digitais
  //   Aluno: Renato F. Soares
  //   TADS 2014.1
  //   4 = somar com valor externo
  //   5 = soma comp_2
  //   8 = desloca
  //   9 = compara A < B
  //   10 = somar com valor interno
  //   A: operador ula
  //   E: insere valor externo
  //   B: endereço da memoria para gravação no banco
  //   C: seleciona um valor do banco para o registrador A
  //   D: seleciona um valor do banco para o registrador B
endmodule

module celula_operacoes (
  input  transporte_entrada_____C_IN,
  input  transporte_entrada_____B_IN,
  input  entrada_desloca,
  input  [3:0] operador_MUX,
  input  A,
  input  B,
  input  b_in,
  input  C_in___compara,
  output C_out___compara,
  output saida,
  output transporte_saida_____C_OUT,
  output transporte_saida_____B_OUT,
  output saida_desloca,
  output [3:0] \Saída_operador 
);

  wire adder_1_out, adder_2_out, and_1_out, comparador_novo_1_a___b, nand_1_out, or_1_out, subtractor_1_out,
       xnor_1_out, xor_1_out;

  xnor xnor_1 (xnor_1_out, A, B);
  and and_1 (and_1_out, A, B);
  or or_1 (or_1_out, A, B);
  xor xor_1 (xor_1_out, A, B);
  nand nand_1 (nand_1_out, A, B);
  Adder #(.width(1)) adder_1 (
    .a(A), .b(B), .out(adder_1_out), .cin(transporte_entrada_____C_IN), .cout(transporte_saida_____C_OUT));
  comparador_novo comparador_novo_1 (
    .C_in(C_in___compara), .B(B), .A(A), .C_out(C_out___compara), .A___B(comparador_novo_1_a___b));
  Subtractor #(.width(1)) subtractor_1 (
    .a(A), .b(B), .out(subtractor_1_out), .bin(transporte_entrada_____B_IN), .bout(transporte_saida_____B_OUT));
  Multiplexer #(.select(4), .enable("false")) multiplexer_1 (
    .in0(and_1_out), .in1(or_1_out), .in2(xor_1_out), .in3(nand_1_out), .in4(adder_1_out), .in5(adder_1_out),
    .in6(subtractor_1_out), .in7(xnor_1_out), .in8(adder_2_out), .in9(comparador_novo_1_a___b),
    .in10(adder_1_out), .out(saida), .sel(operador_MUX));  // open: in11, in12, in13, in14, in15
  Adder #(.width(1)) adder_2 (.a(B), .b(b_in), .out(adder_2_out), .cin(entrada_desloca), .cout(saida_desloca));

  assign \Saída_operador  = operador_MUX;

  // Notes on the sheet:
  //   TADS 2014.1
  //   Celula de operações
  //   Sistemas Digitais
  //   Aluno: Renato Soares
  //   comparador
endmodule

module ULA (
  input  [3:0] operador,
  input  [31:0] A,
  input  [31:0] B,
  output overflow,
  output sao_iguais,
  output [31:0] saida
);

  wire and_1_out, celula_operacoes_1_saida_desloca, celula_operacoes_1_transporte_saida_____b_out,
       celula_operacoes_1_transporte_saida_____c_out, celula_operacoes_2_c_out___compara,
       celula_operacoes_2_saida_desloca, celula_operacoes_2_transporte_saida_____b_out,
       celula_operacoes_2_transporte_saida_____c_out, celula_operacoes_3_c_out___compara,
       celula_operacoes_3_saida_desloca, celula_operacoes_3_transporte_saida_____b_out,
       celula_operacoes_3_transporte_saida_____c_out, celula_operacoes_4_c_out___compara,
       celula_operacoes_4_saida_desloca, celula_operacoes_4_transporte_saida_____b_out,
       celula_operacoes_4_transporte_saida_____c_out, celula_operacoes_5_c_out___compara,
       celula_operacoes_5_saida_desloca, celula_operacoes_5_transporte_saida_____b_out,
       celula_operacoes_5_transporte_saida_____c_out, celula_operacoes_6_c_out___compara,
       celula_operacoes_6_saida_desloca, celula_operacoes_6_transporte_saida_____b_out,
       celula_operacoes_6_transporte_saida_____c_out, celula_operacoes_7_c_out___compara,
       celula_operacoes_7_saida_desloca, celula_operacoes_7_transporte_saida_____b_out,
       celula_operacoes_7_transporte_saida_____c_out, celula_operacoes_8_c_out___compara,
       celula_operacoes_8_saida_desloca, celula_operacoes_8_transporte_saida_____b_out,
       celula_operacoes_8_transporte_saida_____c_out, celula_operacoes_9_c_out___compara,
       celula_operacoes_9_saida_desloca, celula_operacoes_9_transporte_saida_____b_out,
       celula_operacoes_9_transporte_saida_____c_out, celula_operacoes_10_c_out___compara,
       celula_operacoes_10_saida_desloca, celula_operacoes_10_transporte_saida_____b_out,
       celula_operacoes_10_transporte_saida_____c_out, celula_operacoes_11_c_out___compara,
       celula_operacoes_11_saida_desloca, celula_operacoes_11_transporte_saida_____b_out,
       celula_operacoes_11_transporte_saida_____c_out, celula_operacoes_12_c_out___compara,
       celula_operacoes_12_saida_desloca, celula_operacoes_12_transporte_saida_____b_out,
       celula_operacoes_12_transporte_saida_____c_out, celula_operacoes_13_c_out___compara,
       celula_operacoes_13_saida_desloca, celula_operacoes_13_transporte_saida_____b_out,
       celula_operacoes_13_transporte_saida_____c_out, celula_operacoes_14_c_out___compara,
       celula_operacoes_14_saida_desloca, celula_operacoes_14_transporte_saida_____b_out,
       celula_operacoes_14_transporte_saida_____c_out, celula_operacoes_15_c_out___compara,
       celula_operacoes_15_saida_desloca, celula_operacoes_15_transporte_saida_____b_out,
       celula_operacoes_15_transporte_saida_____c_out, celula_operacoes_16_c_out___compara,
       celula_operacoes_16_saida_desloca, celula_operacoes_16_transporte_saida_____b_out,
       celula_operacoes_16_transporte_saida_____c_out, celula_operacoes_17_c_out___compara,
       celula_operacoes_17_saida_desloca, celula_operacoes_17_transporte_saida_____b_out,
       celula_operacoes_17_transporte_saida_____c_out, celula_operacoes_18_c_out___compara,
       celula_operacoes_18_saida_desloca, celula_operacoes_18_transporte_saida_____b_out,
       celula_operacoes_18_transporte_saida_____c_out, celula_operacoes_19_c_out___compara,
       celula_operacoes_19_saida_desloca, celula_operacoes_19_transporte_saida_____b_out,
       celula_operacoes_19_transporte_saida_____c_out, celula_operacoes_20_c_out___compara,
       celula_operacoes_20_saida_desloca, celula_operacoes_20_transporte_saida_____b_out,
       celula_operacoes_20_transporte_saida_____c_out, celula_operacoes_21_c_out___compara,
       celula_operacoes_21_saida_desloca, celula_operacoes_21_transporte_saida_____b_out,
       celula_operacoes_21_transporte_saida_____c_out, celula_operacoes_22_c_out___compara,
       celula_operacoes_22_saida_desloca, celula_operacoes_22_transporte_saida_____b_out,
       celula_operacoes_22_transporte_saida_____c_out, celula_operacoes_23_c_out___compara,
       celula_operacoes_23_saida_desloca, celula_operacoes_23_transporte_saida_____b_out,
       celula_operacoes_23_transporte_saida_____c_out, celula_operacoes_24_c_out___compara,
       celula_operacoes_24_saida_desloca, celula_operacoes_24_transporte_saida_____b_out,
       celula_operacoes_24_transporte_saida_____c_out, celula_operacoes_25_c_out___compara,
       celula_operacoes_25_saida_desloca, celula_operacoes_25_transporte_saida_____b_out,
       celula_operacoes_25_transporte_saida_____c_out, celula_operacoes_26_c_out___compara,
       celula_operacoes_26_saida_desloca, celula_operacoes_26_transporte_saida_____b_out,
       celula_operacoes_26_transporte_saida_____c_out, celula_operacoes_27_c_out___compara,
       celula_operacoes_27_saida_desloca, celula_operacoes_27_transporte_saida_____b_out,
       celula_operacoes_27_transporte_saida_____c_out, celula_operacoes_28_c_out___compara,
       celula_operacoes_28_saida_desloca, celula_operacoes_28_transporte_saida_____b_out,
       celula_operacoes_28_transporte_saida_____c_out, celula_operacoes_29_c_out___compara,
       celula_operacoes_29_saida_desloca, celula_operacoes_29_transporte_saida_____b_out,
       celula_operacoes_29_transporte_saida_____c_out, celula_operacoes_30_c_out___compara,
       celula_operacoes_30_saida_desloca, celula_operacoes_30_transporte_saida_____b_out,
       celula_operacoes_30_transporte_saida_____c_out, celula_operacoes_31_c_out___compara,
       celula_operacoes_31_saida_desloca, celula_operacoes_31_transporte_saida_____b_out,
       celula_operacoes_31_transporte_saida_____c_out, celula_operacoes_32_c_out___compara,
       celula_operacoes_32_saida_desloca, celula_operacoes_32_transporte_saida_____b_out,
       celula_operacoes_32_transporte_saida_____c_out, xnor_1_out, xor_1_out;
  wire [3:0] \celula_operacoes_1_saída_operador , \celula_operacoes_2_saída_operador ,
       \celula_operacoes_3_saída_operador , \celula_operacoes_4_saída_operador ,
       \celula_operacoes_5_saída_operador , \celula_operacoes_6_saída_operador ,
       \celula_operacoes_7_saída_operador , \celula_operacoes_8_saída_operador ,
       \celula_operacoes_9_saída_operador , \celula_operacoes_10_saída_operador ,
       \celula_operacoes_11_saída_operador , \celula_operacoes_12_saída_operador ,
       \celula_operacoes_13_saída_operador , \celula_operacoes_14_saída_operador ,
       \celula_operacoes_15_saída_operador , \celula_operacoes_16_saída_operador ,
       \celula_operacoes_18_saída_operador , \celula_operacoes_19_saída_operador ,
       \celula_operacoes_20_saída_operador , \celula_operacoes_21_saída_operador ,
       \celula_operacoes_22_saída_operador , \celula_operacoes_23_saída_operador ,
       \celula_operacoes_24_saída_operador , \celula_operacoes_25_saída_operador ,
       \celula_operacoes_26_saída_operador , \celula_operacoes_27_saída_operador ,
       \celula_operacoes_28_saída_operador , \celula_operacoes_29_saída_operador ,
       \celula_operacoes_30_saída_operador , \celula_operacoes_31_saída_operador ,
       \celula_operacoes_32_saída_operador ;

  celula_operacoes celula_operacoes_1 (
    .A(A[0]), .B(B[0]), .b_in(B[0]), .saida(saida[0]), .entrada_desloca(1'b0),
    .transporte_entrada_____C_IN(1'b0), .transporte_entrada_____B_IN(1'b0), .operador_MUX(operador),
    .transporte_saida_____C_OUT(celula_operacoes_1_transporte_saida_____c_out),
    .saida_desloca(celula_operacoes_1_saida_desloca),
    .transporte_saida_____B_OUT(celula_operacoes_1_transporte_saida_____b_out),
    .\Saída_operador (\celula_operacoes_1_saída_operador ),
    .C_in___compara(celula_operacoes_2_c_out___compara));  // open: C_out___compara
  celula_operacoes celula_operacoes_2 (
    .A(A[1]), .B(B[1]), .b_in(B[1]), .saida(saida[1]), .entrada_desloca(celula_operacoes_1_saida_desloca),
    .transporte_entrada_____C_IN(celula_operacoes_1_transporte_saida_____c_out),
    .transporte_entrada_____B_IN(celula_operacoes_1_transporte_saida_____b_out),
    .operador_MUX(\celula_operacoes_1_saída_operador ),
    .transporte_saida_____C_OUT(celula_operacoes_2_transporte_saida_____c_out),
    .saida_desloca(celula_operacoes_2_saida_desloca),
    .transporte_saida_____B_OUT(celula_operacoes_2_transporte_saida_____b_out),
    .\Saída_operador (\celula_operacoes_2_saída_operador ),
    .C_in___compara(celula_operacoes_3_c_out___compara), .C_out___compara(celula_operacoes_2_c_out___compara));
  celula_operacoes celula_operacoes_3 (
    .A(A[2]), .B(B[2]), .b_in(B[2]), .saida(saida[2]), .entrada_desloca(celula_operacoes_2_saida_desloca),
    .transporte_entrada_____C_IN(celula_operacoes_2_transporte_saida_____c_out),
    .transporte_entrada_____B_IN(celula_operacoes_2_transporte_saida_____b_out),
    .operador_MUX(\celula_operacoes_2_saída_operador ),
    .transporte_saida_____C_OUT(celula_operacoes_3_transporte_saida_____c_out),
    .saida_desloca(celula_operacoes_3_saida_desloca),
    .transporte_saida_____B_OUT(celula_operacoes_3_transporte_saida_____b_out),
    .\Saída_operador (\celula_operacoes_3_saída_operador ),
    .C_in___compara(celula_operacoes_4_c_out___compara), .C_out___compara(celula_operacoes_3_c_out___compara));
  celula_operacoes celula_operacoes_4 (
    .A(A[3]), .B(B[3]), .b_in(B[3]), .saida(saida[3]), .entrada_desloca(celula_operacoes_3_saida_desloca),
    .transporte_entrada_____C_IN(celula_operacoes_3_transporte_saida_____c_out),
    .transporte_entrada_____B_IN(celula_operacoes_3_transporte_saida_____b_out),
    .operador_MUX(\celula_operacoes_3_saída_operador ),
    .transporte_saida_____C_OUT(celula_operacoes_4_transporte_saida_____c_out),
    .saida_desloca(celula_operacoes_4_saida_desloca),
    .transporte_saida_____B_OUT(celula_operacoes_4_transporte_saida_____b_out),
    .\Saída_operador (\celula_operacoes_4_saída_operador ),
    .C_in___compara(celula_operacoes_5_c_out___compara), .C_out___compara(celula_operacoes_4_c_out___compara));
  celula_operacoes celula_operacoes_5 (
    .A(A[4]), .B(B[4]), .b_in(B[4]), .saida(saida[4]), .entrada_desloca(celula_operacoes_4_saida_desloca),
    .transporte_entrada_____C_IN(celula_operacoes_4_transporte_saida_____c_out),
    .transporte_entrada_____B_IN(celula_operacoes_4_transporte_saida_____b_out),
    .operador_MUX(\celula_operacoes_4_saída_operador ),
    .transporte_saida_____C_OUT(celula_operacoes_5_transporte_saida_____c_out),
    .saida_desloca(celula_operacoes_5_saida_desloca),
    .transporte_saida_____B_OUT(celula_operacoes_5_transporte_saida_____b_out),
    .\Saída_operador (\celula_operacoes_5_saída_operador ),
    .C_in___compara(celula_operacoes_6_c_out___compara), .C_out___compara(celula_operacoes_5_c_out___compara));
  celula_operacoes celula_operacoes_6 (
    .A(A[5]), .B(B[5]), .b_in(B[5]), .saida(saida[5]), .entrada_desloca(celula_operacoes_5_saida_desloca),
    .transporte_entrada_____C_IN(celula_operacoes_5_transporte_saida_____c_out),
    .transporte_entrada_____B_IN(celula_operacoes_5_transporte_saida_____b_out),
    .operador_MUX(\celula_operacoes_5_saída_operador ),
    .transporte_saida_____C_OUT(celula_operacoes_6_transporte_saida_____c_out),
    .saida_desloca(celula_operacoes_6_saida_desloca),
    .transporte_saida_____B_OUT(celula_operacoes_6_transporte_saida_____b_out),
    .\Saída_operador (\celula_operacoes_6_saída_operador ),
    .C_in___compara(celula_operacoes_7_c_out___compara), .C_out___compara(celula_operacoes_6_c_out___compara));
  celula_operacoes celula_operacoes_7 (
    .A(A[6]), .B(B[6]), .b_in(B[6]), .saida(saida[6]), .entrada_desloca(celula_operacoes_6_saida_desloca),
    .transporte_entrada_____C_IN(celula_operacoes_6_transporte_saida_____c_out),
    .transporte_entrada_____B_IN(celula_operacoes_6_transporte_saida_____b_out),
    .operador_MUX(\celula_operacoes_6_saída_operador ),
    .transporte_saida_____C_OUT(celula_operacoes_7_transporte_saida_____c_out),
    .saida_desloca(celula_operacoes_7_saida_desloca),
    .transporte_saida_____B_OUT(celula_operacoes_7_transporte_saida_____b_out),
    .\Saída_operador (\celula_operacoes_7_saída_operador ),
    .C_in___compara(celula_operacoes_8_c_out___compara), .C_out___compara(celula_operacoes_7_c_out___compara));
  celula_operacoes celula_operacoes_8 (
    .A(A[7]), .B(B[7]), .b_in(B[7]), .saida(saida[7]), .entrada_desloca(celula_operacoes_7_saida_desloca),
    .transporte_entrada_____C_IN(celula_operacoes_7_transporte_saida_____c_out),
    .transporte_entrada_____B_IN(celula_operacoes_7_transporte_saida_____b_out),
    .operador_MUX(\celula_operacoes_7_saída_operador ),
    .transporte_saida_____C_OUT(celula_operacoes_8_transporte_saida_____c_out),
    .saida_desloca(celula_operacoes_8_saida_desloca),
    .transporte_saida_____B_OUT(celula_operacoes_8_transporte_saida_____b_out),
    .\Saída_operador (\celula_operacoes_8_saída_operador ),
    .C_in___compara(celula_operacoes_9_c_out___compara), .C_out___compara(celula_operacoes_8_c_out___compara));
  celula_operacoes celula_operacoes_9 (
    .A(A[8]), .B(B[8]), .b_in(B[8]), .saida(saida[8]), .entrada_desloca(celula_operacoes_8_saida_desloca),
    .transporte_entrada_____C_IN(celula_operacoes_8_transporte_saida_____c_out),
    .transporte_entrada_____B_IN(celula_operacoes_8_transporte_saida_____b_out),
    .operador_MUX(\celula_operacoes_8_saída_operador ),
    .transporte_saida_____C_OUT(celula_operacoes_9_transporte_saida_____c_out),
    .saida_desloca(celula_operacoes_9_saida_desloca),
    .transporte_saida_____B_OUT(celula_operacoes_9_transporte_saida_____b_out),
    .\Saída_operador (\celula_operacoes_9_saída_operador ),
    .C_in___compara(celula_operacoes_10_c_out___compara), .C_out___compara(celula_operacoes_9_c_out___compara));
  celula_operacoes celula_operacoes_10 (
    .A(A[9]), .B(B[9]), .b_in(B[9]), .saida(saida[9]), .entrada_desloca(celula_operacoes_9_saida_desloca),
    .transporte_entrada_____C_IN(celula_operacoes_9_transporte_saida_____c_out),
    .transporte_entrada_____B_IN(celula_operacoes_9_transporte_saida_____b_out),
    .operador_MUX(\celula_operacoes_9_saída_operador ),
    .transporte_saida_____C_OUT(celula_operacoes_10_transporte_saida_____c_out),
    .saida_desloca(celula_operacoes_10_saida_desloca),
    .transporte_saida_____B_OUT(celula_operacoes_10_transporte_saida_____b_out),
    .\Saída_operador (\celula_operacoes_10_saída_operador ),
    .C_in___compara(celula_operacoes_11_c_out___compara),
    .C_out___compara(celula_operacoes_10_c_out___compara));
  celula_operacoes celula_operacoes_11 (
    .A(A[10]), .B(B[10]), .b_in(B[10]), .saida(saida[10]),
    .entrada_desloca(celula_operacoes_10_saida_desloca),
    .transporte_entrada_____C_IN(celula_operacoes_10_transporte_saida_____c_out),
    .transporte_entrada_____B_IN(celula_operacoes_10_transporte_saida_____b_out),
    .operador_MUX(\celula_operacoes_10_saída_operador ),
    .transporte_saida_____C_OUT(celula_operacoes_11_transporte_saida_____c_out),
    .saida_desloca(celula_operacoes_11_saida_desloca),
    .transporte_saida_____B_OUT(celula_operacoes_11_transporte_saida_____b_out),
    .\Saída_operador (\celula_operacoes_11_saída_operador ),
    .C_in___compara(celula_operacoes_12_c_out___compara),
    .C_out___compara(celula_operacoes_11_c_out___compara));
  celula_operacoes celula_operacoes_12 (
    .A(A[11]), .B(B[11]), .b_in(B[11]), .saida(saida[11]),
    .entrada_desloca(celula_operacoes_11_saida_desloca),
    .transporte_entrada_____C_IN(celula_operacoes_11_transporte_saida_____c_out),
    .transporte_entrada_____B_IN(celula_operacoes_11_transporte_saida_____b_out),
    .operador_MUX(\celula_operacoes_11_saída_operador ),
    .transporte_saida_____C_OUT(celula_operacoes_12_transporte_saida_____c_out),
    .saida_desloca(celula_operacoes_12_saida_desloca),
    .transporte_saida_____B_OUT(celula_operacoes_12_transporte_saida_____b_out),
    .\Saída_operador (\celula_operacoes_12_saída_operador ),
    .C_in___compara(celula_operacoes_13_c_out___compara),
    .C_out___compara(celula_operacoes_12_c_out___compara));
  celula_operacoes celula_operacoes_13 (
    .A(A[12]), .B(B[12]), .b_in(B[12]), .saida(saida[12]),
    .entrada_desloca(celula_operacoes_12_saida_desloca),
    .transporte_entrada_____C_IN(celula_operacoes_12_transporte_saida_____c_out),
    .transporte_entrada_____B_IN(celula_operacoes_12_transporte_saida_____b_out),
    .operador_MUX(\celula_operacoes_12_saída_operador ),
    .transporte_saida_____C_OUT(celula_operacoes_13_transporte_saida_____c_out),
    .saida_desloca(celula_operacoes_13_saida_desloca),
    .transporte_saida_____B_OUT(celula_operacoes_13_transporte_saida_____b_out),
    .\Saída_operador (\celula_operacoes_13_saída_operador ),
    .C_in___compara(celula_operacoes_14_c_out___compara),
    .C_out___compara(celula_operacoes_13_c_out___compara));
  celula_operacoes celula_operacoes_14 (
    .A(A[13]), .B(B[13]), .b_in(B[13]), .saida(saida[13]),
    .entrada_desloca(celula_operacoes_13_saida_desloca),
    .transporte_entrada_____C_IN(celula_operacoes_13_transporte_saida_____c_out),
    .transporte_entrada_____B_IN(celula_operacoes_13_transporte_saida_____b_out),
    .operador_MUX(\celula_operacoes_13_saída_operador ),
    .transporte_saida_____C_OUT(celula_operacoes_14_transporte_saida_____c_out),
    .saida_desloca(celula_operacoes_14_saida_desloca),
    .transporte_saida_____B_OUT(celula_operacoes_14_transporte_saida_____b_out),
    .\Saída_operador (\celula_operacoes_14_saída_operador ),
    .C_in___compara(celula_operacoes_15_c_out___compara),
    .C_out___compara(celula_operacoes_14_c_out___compara));
  celula_operacoes celula_operacoes_15 (
    .A(A[14]), .B(B[14]), .b_in(B[14]), .saida(saida[14]),
    .entrada_desloca(celula_operacoes_14_saida_desloca),
    .transporte_entrada_____C_IN(celula_operacoes_14_transporte_saida_____c_out),
    .transporte_entrada_____B_IN(celula_operacoes_14_transporte_saida_____b_out),
    .operador_MUX(\celula_operacoes_14_saída_operador ),
    .transporte_saida_____C_OUT(celula_operacoes_15_transporte_saida_____c_out),
    .saida_desloca(celula_operacoes_15_saida_desloca),
    .transporte_saida_____B_OUT(celula_operacoes_15_transporte_saida_____b_out),
    .\Saída_operador (\celula_operacoes_15_saída_operador ),
    .C_in___compara(celula_operacoes_16_c_out___compara),
    .C_out___compara(celula_operacoes_15_c_out___compara));
  celula_operacoes celula_operacoes_16 (
    .A(A[15]), .B(B[15]), .b_in(B[15]), .saida(saida[15]),
    .entrada_desloca(celula_operacoes_15_saida_desloca),
    .transporte_entrada_____C_IN(celula_operacoes_15_transporte_saida_____c_out),
    .transporte_entrada_____B_IN(celula_operacoes_15_transporte_saida_____b_out),
    .operador_MUX(\celula_operacoes_15_saída_operador ),
    .transporte_saida_____C_OUT(celula_operacoes_16_transporte_saida_____c_out),
    .saida_desloca(celula_operacoes_16_saida_desloca),
    .transporte_saida_____B_OUT(celula_operacoes_16_transporte_saida_____b_out),
    .\Saída_operador (\celula_operacoes_16_saída_operador ),
    .C_in___compara(celula_operacoes_32_c_out___compara),
    .C_out___compara(celula_operacoes_16_c_out___compara));
  celula_operacoes celula_operacoes_17 (
    .A(A[31]), .B(B[31]), .b_in(B[31]), .saida(saida[31]),
    .entrada_desloca(celula_operacoes_18_saida_desloca),
    .transporte_entrada_____C_IN(celula_operacoes_18_transporte_saida_____c_out),
    .transporte_entrada_____B_IN(celula_operacoes_18_transporte_saida_____b_out),
    .operador_MUX(\celula_operacoes_18_saída_operador ),
    .transporte_saida_____C_OUT(celula_operacoes_17_transporte_saida_____c_out),
    .saida_desloca(celula_operacoes_17_saida_desloca),
    .transporte_saida_____B_OUT(celula_operacoes_17_transporte_saida_____b_out), .C_in___compara(1'b1),
    .C_out___compara(celula_operacoes_17_c_out___compara));  // open: Saída_operador
  celula_operacoes celula_operacoes_18 (
    .A(A[30]), .B(B[30]), .b_in(B[30]), .saida(saida[30]),
    .entrada_desloca(celula_operacoes_19_saida_desloca),
    .transporte_entrada_____C_IN(celula_operacoes_19_transporte_saida_____c_out),
    .transporte_entrada_____B_IN(celula_operacoes_19_transporte_saida_____b_out),
    .operador_MUX(\celula_operacoes_19_saída_operador ),
    .transporte_saida_____C_OUT(celula_operacoes_18_transporte_saida_____c_out),
    .saida_desloca(celula_operacoes_18_saida_desloca),
    .transporte_saida_____B_OUT(celula_operacoes_18_transporte_saida_____b_out),
    .\Saída_operador (\celula_operacoes_18_saída_operador ),
    .C_in___compara(celula_operacoes_17_c_out___compara),
    .C_out___compara(celula_operacoes_18_c_out___compara));
  celula_operacoes celula_operacoes_19 (
    .A(A[29]), .B(B[29]), .b_in(B[29]), .saida(saida[29]),
    .entrada_desloca(celula_operacoes_20_saida_desloca),
    .transporte_entrada_____C_IN(celula_operacoes_20_transporte_saida_____c_out),
    .transporte_entrada_____B_IN(celula_operacoes_20_transporte_saida_____b_out),
    .operador_MUX(\celula_operacoes_20_saída_operador ),
    .transporte_saida_____C_OUT(celula_operacoes_19_transporte_saida_____c_out),
    .saida_desloca(celula_operacoes_19_saida_desloca),
    .transporte_saida_____B_OUT(celula_operacoes_19_transporte_saida_____b_out),
    .\Saída_operador (\celula_operacoes_19_saída_operador ),
    .C_in___compara(celula_operacoes_18_c_out___compara),
    .C_out___compara(celula_operacoes_19_c_out___compara));
  celula_operacoes celula_operacoes_20 (
    .A(A[28]), .B(B[28]), .b_in(B[28]), .saida(saida[28]),
    .entrada_desloca(celula_operacoes_21_saida_desloca),
    .transporte_entrada_____C_IN(celula_operacoes_21_transporte_saida_____c_out),
    .transporte_entrada_____B_IN(celula_operacoes_21_transporte_saida_____b_out),
    .operador_MUX(\celula_operacoes_21_saída_operador ),
    .transporte_saida_____C_OUT(celula_operacoes_20_transporte_saida_____c_out),
    .saida_desloca(celula_operacoes_20_saida_desloca),
    .transporte_saida_____B_OUT(celula_operacoes_20_transporte_saida_____b_out),
    .\Saída_operador (\celula_operacoes_20_saída_operador ),
    .C_in___compara(celula_operacoes_19_c_out___compara),
    .C_out___compara(celula_operacoes_20_c_out___compara));
  celula_operacoes celula_operacoes_21 (
    .A(A[27]), .B(B[27]), .b_in(B[27]), .saida(saida[27]),
    .entrada_desloca(celula_operacoes_22_saida_desloca),
    .transporte_entrada_____C_IN(celula_operacoes_22_transporte_saida_____c_out),
    .transporte_entrada_____B_IN(celula_operacoes_22_transporte_saida_____b_out),
    .operador_MUX(\celula_operacoes_22_saída_operador ),
    .transporte_saida_____C_OUT(celula_operacoes_21_transporte_saida_____c_out),
    .saida_desloca(celula_operacoes_21_saida_desloca),
    .transporte_saida_____B_OUT(celula_operacoes_21_transporte_saida_____b_out),
    .\Saída_operador (\celula_operacoes_21_saída_operador ),
    .C_in___compara(celula_operacoes_20_c_out___compara),
    .C_out___compara(celula_operacoes_21_c_out___compara));
  celula_operacoes celula_operacoes_22 (
    .A(A[26]), .B(B[26]), .b_in(B[26]), .saida(saida[26]),
    .entrada_desloca(celula_operacoes_23_saida_desloca),
    .transporte_entrada_____C_IN(celula_operacoes_23_transporte_saida_____c_out),
    .transporte_entrada_____B_IN(celula_operacoes_23_transporte_saida_____b_out),
    .operador_MUX(\celula_operacoes_23_saída_operador ),
    .transporte_saida_____C_OUT(celula_operacoes_22_transporte_saida_____c_out),
    .saida_desloca(celula_operacoes_22_saida_desloca),
    .transporte_saida_____B_OUT(celula_operacoes_22_transporte_saida_____b_out),
    .\Saída_operador (\celula_operacoes_22_saída_operador ),
    .C_in___compara(celula_operacoes_21_c_out___compara),
    .C_out___compara(celula_operacoes_22_c_out___compara));
  celula_operacoes celula_operacoes_23 (
    .A(A[25]), .B(B[25]), .b_in(B[25]), .saida(saida[25]),
    .entrada_desloca(celula_operacoes_24_saida_desloca),
    .transporte_entrada_____C_IN(celula_operacoes_24_transporte_saida_____c_out),
    .transporte_entrada_____B_IN(celula_operacoes_24_transporte_saida_____b_out),
    .operador_MUX(\celula_operacoes_24_saída_operador ),
    .transporte_saida_____C_OUT(celula_operacoes_23_transporte_saida_____c_out),
    .saida_desloca(celula_operacoes_23_saida_desloca),
    .transporte_saida_____B_OUT(celula_operacoes_23_transporte_saida_____b_out),
    .\Saída_operador (\celula_operacoes_23_saída_operador ),
    .C_in___compara(celula_operacoes_22_c_out___compara),
    .C_out___compara(celula_operacoes_23_c_out___compara));
  celula_operacoes celula_operacoes_24 (
    .A(A[24]), .B(B[24]), .b_in(B[24]), .saida(saida[24]),
    .entrada_desloca(celula_operacoes_25_saida_desloca),
    .transporte_entrada_____C_IN(celula_operacoes_25_transporte_saida_____c_out),
    .transporte_entrada_____B_IN(celula_operacoes_25_transporte_saida_____b_out),
    .operador_MUX(\celula_operacoes_25_saída_operador ),
    .transporte_saida_____C_OUT(celula_operacoes_24_transporte_saida_____c_out),
    .saida_desloca(celula_operacoes_24_saida_desloca),
    .transporte_saida_____B_OUT(celula_operacoes_24_transporte_saida_____b_out),
    .\Saída_operador (\celula_operacoes_24_saída_operador ),
    .C_in___compara(celula_operacoes_23_c_out___compara),
    .C_out___compara(celula_operacoes_24_c_out___compara));
  celula_operacoes celula_operacoes_25 (
    .A(A[23]), .B(B[23]), .b_in(B[23]), .saida(saida[23]),
    .entrada_desloca(celula_operacoes_26_saida_desloca),
    .transporte_entrada_____C_IN(celula_operacoes_26_transporte_saida_____c_out),
    .transporte_entrada_____B_IN(celula_operacoes_26_transporte_saida_____b_out),
    .operador_MUX(\celula_operacoes_26_saída_operador ),
    .transporte_saida_____C_OUT(celula_operacoes_25_transporte_saida_____c_out),
    .saida_desloca(celula_operacoes_25_saida_desloca),
    .transporte_saida_____B_OUT(celula_operacoes_25_transporte_saida_____b_out),
    .\Saída_operador (\celula_operacoes_25_saída_operador ),
    .C_in___compara(celula_operacoes_24_c_out___compara),
    .C_out___compara(celula_operacoes_25_c_out___compara));
  celula_operacoes celula_operacoes_26 (
    .A(A[22]), .B(B[22]), .b_in(B[22]), .saida(saida[22]),
    .entrada_desloca(celula_operacoes_27_saida_desloca),
    .transporte_entrada_____C_IN(celula_operacoes_27_transporte_saida_____c_out),
    .transporte_entrada_____B_IN(celula_operacoes_27_transporte_saida_____b_out),
    .operador_MUX(\celula_operacoes_27_saída_operador ),
    .transporte_saida_____C_OUT(celula_operacoes_26_transporte_saida_____c_out),
    .saida_desloca(celula_operacoes_26_saida_desloca),
    .transporte_saida_____B_OUT(celula_operacoes_26_transporte_saida_____b_out),
    .\Saída_operador (\celula_operacoes_26_saída_operador ),
    .C_in___compara(celula_operacoes_25_c_out___compara),
    .C_out___compara(celula_operacoes_26_c_out___compara));
  celula_operacoes celula_operacoes_27 (
    .A(A[21]), .B(B[21]), .b_in(B[21]), .saida(saida[21]),
    .entrada_desloca(celula_operacoes_28_saida_desloca),
    .transporte_entrada_____C_IN(celula_operacoes_28_transporte_saida_____c_out),
    .transporte_entrada_____B_IN(celula_operacoes_28_transporte_saida_____b_out),
    .operador_MUX(\celula_operacoes_28_saída_operador ),
    .transporte_saida_____C_OUT(celula_operacoes_27_transporte_saida_____c_out),
    .saida_desloca(celula_operacoes_27_saida_desloca),
    .transporte_saida_____B_OUT(celula_operacoes_27_transporte_saida_____b_out),
    .\Saída_operador (\celula_operacoes_27_saída_operador ),
    .C_in___compara(celula_operacoes_26_c_out___compara),
    .C_out___compara(celula_operacoes_27_c_out___compara));
  celula_operacoes celula_operacoes_28 (
    .A(A[20]), .B(B[20]), .b_in(B[20]), .saida(saida[20]),
    .entrada_desloca(celula_operacoes_29_saida_desloca),
    .transporte_entrada_____C_IN(celula_operacoes_29_transporte_saida_____c_out),
    .transporte_entrada_____B_IN(celula_operacoes_29_transporte_saida_____b_out),
    .operador_MUX(\celula_operacoes_29_saída_operador ),
    .transporte_saida_____C_OUT(celula_operacoes_28_transporte_saida_____c_out),
    .saida_desloca(celula_operacoes_28_saida_desloca),
    .transporte_saida_____B_OUT(celula_operacoes_28_transporte_saida_____b_out),
    .\Saída_operador (\celula_operacoes_28_saída_operador ),
    .C_in___compara(celula_operacoes_27_c_out___compara),
    .C_out___compara(celula_operacoes_28_c_out___compara));
  celula_operacoes celula_operacoes_29 (
    .A(A[19]), .B(B[19]), .b_in(B[19]), .saida(saida[19]),
    .entrada_desloca(celula_operacoes_30_saida_desloca),
    .transporte_entrada_____C_IN(celula_operacoes_30_transporte_saida_____c_out),
    .transporte_entrada_____B_IN(celula_operacoes_30_transporte_saida_____b_out),
    .operador_MUX(\celula_operacoes_30_saída_operador ),
    .transporte_saida_____C_OUT(celula_operacoes_29_transporte_saida_____c_out),
    .saida_desloca(celula_operacoes_29_saida_desloca),
    .transporte_saida_____B_OUT(celula_operacoes_29_transporte_saida_____b_out),
    .\Saída_operador (\celula_operacoes_29_saída_operador ),
    .C_in___compara(celula_operacoes_28_c_out___compara),
    .C_out___compara(celula_operacoes_29_c_out___compara));
  celula_operacoes celula_operacoes_30 (
    .A(A[18]), .B(B[18]), .b_in(B[18]), .saida(saida[18]),
    .entrada_desloca(celula_operacoes_31_saida_desloca),
    .transporte_entrada_____C_IN(celula_operacoes_31_transporte_saida_____c_out),
    .transporte_entrada_____B_IN(celula_operacoes_31_transporte_saida_____b_out),
    .operador_MUX(\celula_operacoes_31_saída_operador ),
    .transporte_saida_____C_OUT(celula_operacoes_30_transporte_saida_____c_out),
    .saida_desloca(celula_operacoes_30_saida_desloca),
    .transporte_saida_____B_OUT(celula_operacoes_30_transporte_saida_____b_out),
    .\Saída_operador (\celula_operacoes_30_saída_operador ),
    .C_in___compara(celula_operacoes_29_c_out___compara),
    .C_out___compara(celula_operacoes_30_c_out___compara));
  celula_operacoes celula_operacoes_31 (
    .A(A[17]), .B(B[17]), .b_in(B[17]), .saida(saida[17]),
    .entrada_desloca(celula_operacoes_32_saida_desloca),
    .transporte_entrada_____C_IN(celula_operacoes_32_transporte_saida_____c_out),
    .transporte_entrada_____B_IN(celula_operacoes_32_transporte_saida_____b_out),
    .operador_MUX(\celula_operacoes_32_saída_operador ),
    .transporte_saida_____C_OUT(celula_operacoes_31_transporte_saida_____c_out),
    .saida_desloca(celula_operacoes_31_saida_desloca),
    .transporte_saida_____B_OUT(celula_operacoes_31_transporte_saida_____b_out),
    .\Saída_operador (\celula_operacoes_31_saída_operador ),
    .C_in___compara(celula_operacoes_30_c_out___compara),
    .C_out___compara(celula_operacoes_31_c_out___compara));
  celula_operacoes celula_operacoes_32 (
    .A(A[16]), .B(B[16]), .b_in(B[16]), .saida(saida[16]),
    .entrada_desloca(celula_operacoes_16_saida_desloca),
    .transporte_entrada_____C_IN(celula_operacoes_16_transporte_saida_____c_out),
    .transporte_entrada_____B_IN(celula_operacoes_16_transporte_saida_____b_out),
    .operador_MUX(\celula_operacoes_16_saída_operador ),
    .transporte_saida_____C_OUT(celula_operacoes_32_transporte_saida_____c_out),
    .saida_desloca(celula_operacoes_32_saida_desloca),
    .transporte_saida_____B_OUT(celula_operacoes_32_transporte_saida_____b_out),
    .\Saída_operador (\celula_operacoes_32_saída_operador ),
    .C_in___compara(celula_operacoes_31_c_out___compara),
    .C_out___compara(celula_operacoes_32_c_out___compara));
  xnor xnor_1 (xnor_1_out, A[31], B[31]);
  xor xor_1 (xor_1_out, B[31], saida[31]);
  and and_1 (and_1_out, xnor_1_out, xor_1_out);
  or or_1 (overflow, celula_operacoes_17_saida_desloca, celula_operacoes_17_transporte_saida_____b_out, celula_operacoes_17_transporte_saida_____c_out, and_1_out);
  comparador comparador_1 (.in_1(A), .in_2(B), .out_3(sao_iguais));

  // Notes on the sheet:
  //   overflow comp 2
  //   underflow [-]
  //   overflow [+] 
  //   overflow [+] comp 2 
  //   overflow desloca
  //   ULA
  //   Sistemas Digitais
  //   TADS 2014.1
  //   0 = and
  //   1 = or
  //   2 = xor
  //   3 = nand
  //   4 = somar
  //   5 = soma comp_2
  //   6 = subtrair
  //   7 = xnor
  //   8 = desloca
  //   9 = compara A < B
  //   Aluno: Renato F. Soares
endmodule

module comparador_novo (
  input  B,
  input  A,
  input  C_in,
  output C_out,
  output A___B
);

  wire and_1_out, not_1_out, xnor_1_out;

  not not_1 (not_1_out, A);
  xnor xnor_1 (xnor_1_out, A, B);
  and and_1 (and_1_out, not_1_out, B);
  and and_2 (C_out, C_in, xnor_1_out);
  and and_3 (A___B, C_in, and_1_out);

  // Notes on the sheet:
  //   CELULA COMPARADOR A<B
endmodule

module registrador (
  input  Dt31,
  input  Dt30,
  input  Dt29,
  input  Dt28,
  input  Dt27,
  input  Dt26,
  input  Dt25,
  input  Dt24,
  input  Dt23,
  input  Dt22,
  input  Dt21,
  input  Dt20,
  input  Dt19,
  input  Dt18,
  input  Dt17,
  input  Dt16,
  input  Dt15,
  input  Dt14,
  input  Dt13,
  input  Dt12,
  input  Dt11,
  input  Dt10,
  input  Dt09,
  input  Dt08,
  input  Dt07,
  input  Dt06,
  input  Dt05,
  input  Dt04,
  input  Dt03,
  input  Dt02,
  input  Dt01,
  input  Dt00,
  input  clear,
  input  write,
  output S31,
  output S30,
  output S29,
  output S28,
  output S27,
  output S26,
  output S25,
  output S24,
  output S23,
  output S22,
  output S21,
  output S20,
  output S19,
  output S18,
  output S17,
  output S16,
  output S15,
  output S14,
  output S13,
  output S12,
  output S11,
  output S10,
  output S09,
  output S08,
  output S07,
  output S06,
  output S05,
  output S04,
  output S03,
  output S02,
  output S01,
  output S00
);

  D_Flip_Flop d_ff_1 (.clk(write), .D(Dt31), .Q(S31), .reset(clear));  // open: Qn, preset, en
  D_Flip_Flop d_ff_2 (.clk(write), .D(Dt30), .Q(S30), .reset(clear));  // open: Qn, preset, en
  D_Flip_Flop d_ff_3 (.clk(write), .D(Dt29), .Q(S29), .reset(clear));  // open: Qn, preset, en
  D_Flip_Flop d_ff_4 (.clk(write), .D(Dt28), .Q(S28), .reset(clear));  // open: Qn, preset, en
  D_Flip_Flop d_ff_5 (.clk(write), .D(Dt27), .Q(S27), .reset(clear));  // open: Qn, preset, en
  D_Flip_Flop d_ff_6 (.clk(write), .D(Dt26), .Q(S26), .reset(clear));  // open: Qn, preset, en
  D_Flip_Flop d_ff_7 (.clk(write), .D(Dt25), .Q(S25), .reset(clear));  // open: Qn, preset, en
  D_Flip_Flop d_ff_8 (.clk(write), .D(Dt24), .Q(S24), .reset(clear));  // open: Qn, preset, en
  D_Flip_Flop d_ff_9 (.clk(write), .D(Dt23), .Q(S23), .reset(clear));  // open: Qn, preset, en
  D_Flip_Flop d_ff_10 (.clk(write), .D(Dt22), .Q(S22), .reset(clear));  // open: Qn, preset, en
  D_Flip_Flop d_ff_11 (.clk(write), .D(Dt21), .Q(S21), .reset(clear));  // open: Qn, preset, en
  D_Flip_Flop d_ff_12 (.clk(write), .D(Dt20), .Q(S20), .reset(clear));  // open: Qn, preset, en
  D_Flip_Flop d_ff_13 (.clk(write), .D(Dt19), .Q(S19), .reset(clear));  // open: Qn, preset, en
  D_Flip_Flop d_ff_14 (.clk(write), .D(Dt18), .Q(S18), .reset(clear));  // open: Qn, preset, en
  D_Flip_Flop d_ff_15 (.clk(write), .D(Dt17), .Q(S17), .reset(clear));  // open: Qn, preset, en
  D_Flip_Flop d_ff_16 (.clk(write), .D(Dt16), .Q(S16), .reset(clear));  // open: Qn, preset, en
  D_Flip_Flop d_ff_17 (.clk(write), .D(Dt15), .Q(S15), .reset(clear));  // open: Qn, preset, en
  D_Flip_Flop d_ff_18 (.clk(write), .D(Dt14), .Q(S14), .reset(clear));  // open: Qn, preset, en
  D_Flip_Flop d_ff_19 (.clk(write), .D(Dt13), .Q(S13), .reset(clear));  // open: Qn, preset, en
  D_Flip_Flop d_ff_20 (.clk(write), .D(Dt12), .Q(S12), .reset(clear));  // open: Qn, preset, en
  D_Flip_Flop d_ff_21 (.clk(write), .D(Dt11), .Q(S11), .reset(clear));  // open: Qn, preset, en
  D_Flip_Flop d_ff_22 (.clk(write), .D(Dt10), .Q(S10), .reset(clear));  // open: Qn, preset, en
  D_Flip_Flop d_ff_23 (.clk(write), .D(Dt09), .Q(S09), .reset(clear));  // open: Qn, preset, en
  D_Flip_Flop d_ff_24 (.clk(write), .D(Dt08), .Q(S08), .reset(clear));  // open: Qn, preset, en
  D_Flip_Flop d_ff_25 (.clk(write), .D(Dt07), .Q(S07), .reset(clear));  // open: Qn, preset, en
  D_Flip_Flop d_ff_26 (.clk(write), .D(Dt06), .Q(S06), .reset(clear));  // open: Qn, preset, en
  D_Flip_Flop d_ff_27 (.clk(write), .D(Dt05), .Q(S05), .reset(clear));  // open: Qn, preset, en
  D_Flip_Flop d_ff_28 (.clk(write), .D(Dt04), .Q(S04), .reset(clear));  // open: Qn, preset, en
  D_Flip_Flop d_ff_29 (.clk(write), .D(Dt03), .Q(S03), .reset(clear));  // open: Qn, preset, en
  D_Flip_Flop d_ff_30 (.clk(write), .D(Dt02), .Q(S02), .reset(clear));  // open: Qn, preset, en
  D_Flip_Flop d_ff_31 (.clk(write), .D(Dt01), .Q(S01), .reset(clear));  // open: Qn, preset, en
  D_Flip_Flop d_ff_32 (.clk(write), .D(Dt00), .Q(S00), .reset(clear));  // open: Qn, preset, en
endmodule
module banco_registrador (
  input  clear,
  input  [31:0] DATA_IN,
  input  [4:0] registrador_A,
  input  write,
  input  [4:0] \endereço_write ,
  input  [4:0] registrador_B,
  output [31:0] DATAreg_A,
  output [31:0] DATAreg_B
);

  wire demultiplexer_1_out0, demultiplexer_1_out1, demultiplexer_1_out2, demultiplexer_1_out3,
       demultiplexer_1_out4, demultiplexer_1_out5, demultiplexer_1_out6, demultiplexer_1_out7,
       demultiplexer_1_out8, demultiplexer_1_out9, demultiplexer_1_out10, demultiplexer_1_out11,
       demultiplexer_1_out12, demultiplexer_1_out13, demultiplexer_1_out14, demultiplexer_1_out15,
       demultiplexer_1_out16, demultiplexer_1_out17, demultiplexer_1_out18, demultiplexer_1_out19,
       demultiplexer_1_out20, demultiplexer_1_out21, demultiplexer_1_out22, demultiplexer_1_out23,
       demultiplexer_1_out24, demultiplexer_1_out25, demultiplexer_1_out26, demultiplexer_1_out27,
       demultiplexer_1_out28, demultiplexer_1_out29, demultiplexer_1_out30, demultiplexer_1_out31;
  wire [31:0] _00000_s00, _00001_s00, _00010_s00, _00011_s00, _00100_s00, _00101_s00, registrador_1_s00,
       registrador_2_s00, registrador_3_s00, registrador_4_s00, registrador_5_s00, registrador_6_s00,
       registrador_7_s00, registrador_8_s00, registrador_9_s00, registrador_10_s00, registrador_11_s00,
       registrador_12_s00, registrador_13_s00, registrador_14_s00, registrador_15_s00, registrador_16_s00,
       registrador_17_s00, registrador_18_s00, registrador_19_s00, registrador_20_s00, registrador_21_s00,
       registrador_22_s00, registrador_23_s00, registrador_24_s00, registrador_25_s00, registrador_26_s00;

  Demultiplexer #(.select(5), .enable("false")) demultiplexer_1 (
    .out0(demultiplexer_1_out0), .out1(demultiplexer_1_out1), .out2(demultiplexer_1_out2),
    .out3(demultiplexer_1_out3), .out4(demultiplexer_1_out4), .out5(demultiplexer_1_out5),
    .out6(demultiplexer_1_out6), .out7(demultiplexer_1_out7), .out8(demultiplexer_1_out8),
    .out9(demultiplexer_1_out9), .out10(demultiplexer_1_out10), .out11(demultiplexer_1_out11),
    .out12(demultiplexer_1_out12), .out13(demultiplexer_1_out13), .out14(demultiplexer_1_out14),
    .out15(demultiplexer_1_out15), .out16(demultiplexer_1_out16), .out17(demultiplexer_1_out17),
    .out18(demultiplexer_1_out18), .out19(demultiplexer_1_out19), .out20(demultiplexer_1_out20),
    .out21(demultiplexer_1_out21), .out22(demultiplexer_1_out22), .out23(demultiplexer_1_out23),
    .out24(demultiplexer_1_out24), .out25(demultiplexer_1_out25), .out26(demultiplexer_1_out26),
    .out27(demultiplexer_1_out27), .out28(demultiplexer_1_out28), .out29(demultiplexer_1_out29),
    .out30(demultiplexer_1_out30), .out31(demultiplexer_1_out31), .in(write), .sel(\endereço_write ));
  registrador _00000 (
    .write(demultiplexer_1_out0), .clear(clear), .Dt31(DATA_IN[31]), .Dt30(DATA_IN[30]), .Dt29(DATA_IN[29]),
    .Dt28(DATA_IN[28]), .Dt27(DATA_IN[27]), .Dt26(DATA_IN[26]), .Dt25(DATA_IN[25]), .Dt24(DATA_IN[24]),
    .Dt23(DATA_IN[23]), .Dt22(DATA_IN[22]), .Dt21(DATA_IN[21]), .Dt20(DATA_IN[20]), .Dt19(DATA_IN[19]),
    .Dt18(DATA_IN[18]), .Dt17(DATA_IN[17]), .Dt16(DATA_IN[16]), .Dt15(DATA_IN[15]), .Dt14(DATA_IN[14]),
    .Dt13(DATA_IN[13]), .Dt12(DATA_IN[12]), .Dt11(DATA_IN[11]), .Dt10(DATA_IN[10]), .Dt09(DATA_IN[9]),
    .Dt08(DATA_IN[8]), .Dt07(DATA_IN[7]), .Dt06(DATA_IN[6]), .Dt05(DATA_IN[5]), .Dt04(DATA_IN[4]),
    .Dt03(DATA_IN[3]), .Dt02(DATA_IN[2]), .Dt01(DATA_IN[1]), .Dt00(DATA_IN[0]), .S31(_00000_s00[31]),
    .S30(_00000_s00[30]), .S29(_00000_s00[29]), .S28(_00000_s00[28]), .S27(_00000_s00[27]),
    .S26(_00000_s00[26]), .S25(_00000_s00[25]), .S24(_00000_s00[24]), .S23(_00000_s00[23]),
    .S22(_00000_s00[22]), .S21(_00000_s00[21]), .S20(_00000_s00[20]), .S19(_00000_s00[19]),
    .S18(_00000_s00[18]), .S17(_00000_s00[17]), .S16(_00000_s00[16]), .S15(_00000_s00[15]),
    .S14(_00000_s00[14]), .S13(_00000_s00[13]), .S12(_00000_s00[12]), .S11(_00000_s00[11]),
    .S10(_00000_s00[10]), .S09(_00000_s00[9]), .S08(_00000_s00[8]), .S07(_00000_s00[7]), .S06(_00000_s00[6]),
    .S05(_00000_s00[5]), .S04(_00000_s00[4]), .S03(_00000_s00[3]), .S02(_00000_s00[2]), .S01(_00000_s00[1]),
    .S00(_00000_s00[0]));
  registrador _00001 (
    .write(demultiplexer_1_out1), .clear(clear), .Dt31(DATA_IN[31]), .Dt30(DATA_IN[30]), .Dt29(DATA_IN[29]),
    .Dt28(DATA_IN[28]), .Dt27(DATA_IN[27]), .Dt26(DATA_IN[26]), .Dt25(DATA_IN[25]), .Dt24(DATA_IN[24]),
    .Dt23(DATA_IN[23]), .Dt22(DATA_IN[22]), .Dt21(DATA_IN[21]), .Dt20(DATA_IN[20]), .Dt19(DATA_IN[19]),
    .Dt18(DATA_IN[18]), .Dt17(DATA_IN[17]), .Dt16(DATA_IN[16]), .Dt15(DATA_IN[15]), .Dt14(DATA_IN[14]),
    .Dt13(DATA_IN[13]), .Dt12(DATA_IN[12]), .Dt11(DATA_IN[11]), .Dt10(DATA_IN[10]), .Dt09(DATA_IN[9]),
    .Dt08(DATA_IN[8]), .Dt07(DATA_IN[7]), .Dt06(DATA_IN[6]), .Dt05(DATA_IN[5]), .Dt04(DATA_IN[4]),
    .Dt03(DATA_IN[3]), .Dt02(DATA_IN[2]), .Dt01(DATA_IN[1]), .Dt00(DATA_IN[0]), .S31(_00001_s00[31]),
    .S30(_00001_s00[30]), .S29(_00001_s00[29]), .S28(_00001_s00[28]), .S27(_00001_s00[27]),
    .S26(_00001_s00[26]), .S25(_00001_s00[25]), .S24(_00001_s00[24]), .S23(_00001_s00[23]),
    .S22(_00001_s00[22]), .S21(_00001_s00[21]), .S20(_00001_s00[20]), .S19(_00001_s00[19]),
    .S18(_00001_s00[18]), .S17(_00001_s00[17]), .S16(_00001_s00[16]), .S15(_00001_s00[15]),
    .S14(_00001_s00[14]), .S13(_00001_s00[13]), .S12(_00001_s00[12]), .S11(_00001_s00[11]),
    .S10(_00001_s00[10]), .S09(_00001_s00[9]), .S08(_00001_s00[8]), .S07(_00001_s00[7]), .S06(_00001_s00[6]),
    .S05(_00001_s00[5]), .S04(_00001_s00[4]), .S03(_00001_s00[3]), .S02(_00001_s00[2]), .S01(_00001_s00[1]),
    .S00(_00001_s00[0]));
  registrador _00010 (
    .write(demultiplexer_1_out2), .clear(clear), .Dt31(DATA_IN[31]), .Dt30(DATA_IN[30]), .Dt29(DATA_IN[29]),
    .Dt28(DATA_IN[28]), .Dt27(DATA_IN[27]), .Dt26(DATA_IN[26]), .Dt25(DATA_IN[25]), .Dt24(DATA_IN[24]),
    .Dt23(DATA_IN[23]), .Dt22(DATA_IN[22]), .Dt21(DATA_IN[21]), .Dt20(DATA_IN[20]), .Dt19(DATA_IN[19]),
    .Dt18(DATA_IN[18]), .Dt17(DATA_IN[17]), .Dt16(DATA_IN[16]), .Dt15(DATA_IN[15]), .Dt14(DATA_IN[14]),
    .Dt13(DATA_IN[13]), .Dt12(DATA_IN[12]), .Dt11(DATA_IN[11]), .Dt10(DATA_IN[10]), .Dt09(DATA_IN[9]),
    .Dt08(DATA_IN[8]), .Dt07(DATA_IN[7]), .Dt06(DATA_IN[6]), .Dt05(DATA_IN[5]), .Dt04(DATA_IN[4]),
    .Dt03(DATA_IN[3]), .Dt02(DATA_IN[2]), .Dt01(DATA_IN[1]), .Dt00(DATA_IN[0]), .S31(_00010_s00[31]),
    .S30(_00010_s00[30]), .S29(_00010_s00[29]), .S28(_00010_s00[28]), .S27(_00010_s00[27]),
    .S26(_00010_s00[26]), .S25(_00010_s00[25]), .S24(_00010_s00[24]), .S23(_00010_s00[23]),
    .S22(_00010_s00[22]), .S21(_00010_s00[21]), .S20(_00010_s00[20]), .S19(_00010_s00[19]),
    .S18(_00010_s00[18]), .S17(_00010_s00[17]), .S16(_00010_s00[16]), .S15(_00010_s00[15]),
    .S14(_00010_s00[14]), .S13(_00010_s00[13]), .S12(_00010_s00[12]), .S11(_00010_s00[11]),
    .S10(_00010_s00[10]), .S09(_00010_s00[9]), .S08(_00010_s00[8]), .S07(_00010_s00[7]), .S06(_00010_s00[6]),
    .S05(_00010_s00[5]), .S04(_00010_s00[4]), .S03(_00010_s00[3]), .S02(_00010_s00[2]), .S01(_00010_s00[1]),
    .S00(_00010_s00[0]));
  registrador _00011 (
    .write(demultiplexer_1_out3), .clear(clear), .Dt31(DATA_IN[31]), .Dt30(DATA_IN[30]), .Dt29(DATA_IN[29]),
    .Dt28(DATA_IN[28]), .Dt27(DATA_IN[27]), .Dt26(DATA_IN[26]), .Dt25(DATA_IN[25]), .Dt24(DATA_IN[24]),
    .Dt23(DATA_IN[23]), .Dt22(DATA_IN[22]), .Dt21(DATA_IN[21]), .Dt20(DATA_IN[20]), .Dt19(DATA_IN[19]),
    .Dt18(DATA_IN[18]), .Dt17(DATA_IN[17]), .Dt16(DATA_IN[16]), .Dt15(DATA_IN[15]), .Dt14(DATA_IN[14]),
    .Dt13(DATA_IN[13]), .Dt12(DATA_IN[12]), .Dt11(DATA_IN[11]), .Dt10(DATA_IN[10]), .Dt09(DATA_IN[9]),
    .Dt08(DATA_IN[8]), .Dt07(DATA_IN[7]), .Dt06(DATA_IN[6]), .Dt05(DATA_IN[5]), .Dt04(DATA_IN[4]),
    .Dt03(DATA_IN[3]), .Dt02(DATA_IN[2]), .Dt01(DATA_IN[1]), .Dt00(DATA_IN[0]), .S31(_00011_s00[31]),
    .S30(_00011_s00[30]), .S29(_00011_s00[29]), .S28(_00011_s00[28]), .S27(_00011_s00[27]),
    .S26(_00011_s00[26]), .S25(_00011_s00[25]), .S24(_00011_s00[24]), .S23(_00011_s00[23]),
    .S22(_00011_s00[22]), .S21(_00011_s00[21]), .S20(_00011_s00[20]), .S19(_00011_s00[19]),
    .S18(_00011_s00[18]), .S17(_00011_s00[17]), .S16(_00011_s00[16]), .S15(_00011_s00[15]),
    .S14(_00011_s00[14]), .S13(_00011_s00[13]), .S12(_00011_s00[12]), .S11(_00011_s00[11]),
    .S10(_00011_s00[10]), .S09(_00011_s00[9]), .S08(_00011_s00[8]), .S07(_00011_s00[7]), .S06(_00011_s00[6]),
    .S05(_00011_s00[5]), .S04(_00011_s00[4]), .S03(_00011_s00[3]), .S02(_00011_s00[2]), .S01(_00011_s00[1]),
    .S00(_00011_s00[0]));
  registrador _00100 (
    .write(demultiplexer_1_out4), .clear(clear), .Dt31(DATA_IN[31]), .Dt30(DATA_IN[30]), .Dt29(DATA_IN[29]),
    .Dt28(DATA_IN[28]), .Dt27(DATA_IN[27]), .Dt26(DATA_IN[26]), .Dt25(DATA_IN[25]), .Dt24(DATA_IN[24]),
    .Dt23(DATA_IN[23]), .Dt22(DATA_IN[22]), .Dt21(DATA_IN[21]), .Dt20(DATA_IN[20]), .Dt19(DATA_IN[19]),
    .Dt18(DATA_IN[18]), .Dt17(DATA_IN[17]), .Dt16(DATA_IN[16]), .Dt15(DATA_IN[15]), .Dt14(DATA_IN[14]),
    .Dt13(DATA_IN[13]), .Dt12(DATA_IN[12]), .Dt11(DATA_IN[11]), .Dt10(DATA_IN[10]), .Dt09(DATA_IN[9]),
    .Dt08(DATA_IN[8]), .Dt07(DATA_IN[7]), .Dt06(DATA_IN[6]), .Dt05(DATA_IN[5]), .Dt04(DATA_IN[4]),
    .Dt03(DATA_IN[3]), .Dt02(DATA_IN[2]), .Dt01(DATA_IN[1]), .Dt00(DATA_IN[0]), .S31(_00100_s00[31]),
    .S30(_00100_s00[30]), .S29(_00100_s00[29]), .S28(_00100_s00[28]), .S27(_00100_s00[27]),
    .S26(_00100_s00[26]), .S25(_00100_s00[25]), .S24(_00100_s00[24]), .S23(_00100_s00[23]),
    .S22(_00100_s00[22]), .S21(_00100_s00[21]), .S20(_00100_s00[20]), .S19(_00100_s00[19]),
    .S18(_00100_s00[18]), .S17(_00100_s00[17]), .S16(_00100_s00[16]), .S15(_00100_s00[15]),
    .S14(_00100_s00[14]), .S13(_00100_s00[13]), .S12(_00100_s00[12]), .S11(_00100_s00[11]),
    .S10(_00100_s00[10]), .S09(_00100_s00[9]), .S08(_00100_s00[8]), .S07(_00100_s00[7]), .S06(_00100_s00[6]),
    .S05(_00100_s00[5]), .S04(_00100_s00[4]), .S03(_00100_s00[3]), .S02(_00100_s00[2]), .S01(_00100_s00[1]),
    .S00(_00100_s00[0]));
  registrador _00101 (
    .write(demultiplexer_1_out5), .clear(clear), .Dt31(DATA_IN[31]), .Dt30(DATA_IN[30]), .Dt29(DATA_IN[29]),
    .Dt28(DATA_IN[28]), .Dt27(DATA_IN[27]), .Dt26(DATA_IN[26]), .Dt25(DATA_IN[25]), .Dt24(DATA_IN[24]),
    .Dt23(DATA_IN[23]), .Dt22(DATA_IN[22]), .Dt21(DATA_IN[21]), .Dt20(DATA_IN[20]), .Dt19(DATA_IN[19]),
    .Dt18(DATA_IN[18]), .Dt17(DATA_IN[17]), .Dt16(DATA_IN[16]), .Dt15(DATA_IN[15]), .Dt14(DATA_IN[14]),
    .Dt13(DATA_IN[13]), .Dt12(DATA_IN[12]), .Dt11(DATA_IN[11]), .Dt10(DATA_IN[10]), .Dt09(DATA_IN[9]),
    .Dt08(DATA_IN[8]), .Dt07(DATA_IN[7]), .Dt06(DATA_IN[6]), .Dt05(DATA_IN[5]), .Dt04(DATA_IN[4]),
    .Dt03(DATA_IN[3]), .Dt02(DATA_IN[2]), .Dt01(DATA_IN[1]), .Dt00(DATA_IN[0]), .S31(_00101_s00[31]),
    .S30(_00101_s00[30]), .S29(_00101_s00[29]), .S28(_00101_s00[28]), .S27(_00101_s00[27]),
    .S26(_00101_s00[26]), .S25(_00101_s00[25]), .S24(_00101_s00[24]), .S23(_00101_s00[23]),
    .S22(_00101_s00[22]), .S21(_00101_s00[21]), .S20(_00101_s00[20]), .S19(_00101_s00[19]),
    .S18(_00101_s00[18]), .S17(_00101_s00[17]), .S16(_00101_s00[16]), .S15(_00101_s00[15]),
    .S14(_00101_s00[14]), .S13(_00101_s00[13]), .S12(_00101_s00[12]), .S11(_00101_s00[11]),
    .S10(_00101_s00[10]), .S09(_00101_s00[9]), .S08(_00101_s00[8]), .S07(_00101_s00[7]), .S06(_00101_s00[6]),
    .S05(_00101_s00[5]), .S04(_00101_s00[4]), .S03(_00101_s00[3]), .S02(_00101_s00[2]), .S01(_00101_s00[1]),
    .S00(_00101_s00[0]));
  registrador registrador_1 (
    .write(demultiplexer_1_out6), .clear(clear), .Dt31(DATA_IN[31]), .Dt30(DATA_IN[30]), .Dt29(DATA_IN[29]),
    .Dt28(DATA_IN[28]), .Dt27(DATA_IN[27]), .Dt26(DATA_IN[26]), .Dt25(DATA_IN[25]), .Dt24(DATA_IN[24]),
    .Dt23(DATA_IN[23]), .Dt22(DATA_IN[22]), .Dt21(DATA_IN[21]), .Dt20(DATA_IN[20]), .Dt19(DATA_IN[19]),
    .Dt18(DATA_IN[18]), .Dt17(DATA_IN[17]), .Dt16(DATA_IN[16]), .Dt15(DATA_IN[15]), .Dt14(DATA_IN[14]),
    .Dt13(DATA_IN[13]), .Dt12(DATA_IN[12]), .Dt11(DATA_IN[11]), .Dt10(DATA_IN[10]), .Dt09(DATA_IN[9]),
    .Dt08(DATA_IN[8]), .Dt07(DATA_IN[7]), .Dt06(DATA_IN[6]), .Dt05(DATA_IN[5]), .Dt04(DATA_IN[4]),
    .Dt03(DATA_IN[3]), .Dt02(DATA_IN[2]), .Dt01(DATA_IN[1]), .Dt00(DATA_IN[0]), .S31(registrador_1_s00[31]),
    .S30(registrador_1_s00[30]), .S29(registrador_1_s00[29]), .S28(registrador_1_s00[28]),
    .S27(registrador_1_s00[27]), .S26(registrador_1_s00[26]), .S25(registrador_1_s00[25]),
    .S24(registrador_1_s00[24]), .S23(registrador_1_s00[23]), .S22(registrador_1_s00[22]),
    .S21(registrador_1_s00[21]), .S20(registrador_1_s00[20]), .S19(registrador_1_s00[19]),
    .S18(registrador_1_s00[18]), .S17(registrador_1_s00[17]), .S16(registrador_1_s00[16]),
    .S15(registrador_1_s00[15]), .S14(registrador_1_s00[14]), .S13(registrador_1_s00[13]),
    .S12(registrador_1_s00[12]), .S11(registrador_1_s00[11]), .S10(registrador_1_s00[10]),
    .S09(registrador_1_s00[9]), .S08(registrador_1_s00[8]), .S07(registrador_1_s00[7]),
    .S06(registrador_1_s00[6]), .S05(registrador_1_s00[5]), .S04(registrador_1_s00[4]),
    .S03(registrador_1_s00[3]), .S02(registrador_1_s00[2]), .S01(registrador_1_s00[1]),
    .S00(registrador_1_s00[0]));
  registrador registrador_2 (
    .write(demultiplexer_1_out7), .clear(clear), .Dt31(DATA_IN[31]), .Dt30(DATA_IN[30]), .Dt29(DATA_IN[29]),
    .Dt28(DATA_IN[28]), .Dt27(DATA_IN[27]), .Dt26(DATA_IN[26]), .Dt25(DATA_IN[25]), .Dt24(DATA_IN[24]),
    .Dt23(DATA_IN[23]), .Dt22(DATA_IN[22]), .Dt21(DATA_IN[21]), .Dt20(DATA_IN[20]), .Dt19(DATA_IN[19]),
    .Dt18(DATA_IN[18]), .Dt17(DATA_IN[17]), .Dt16(DATA_IN[16]), .Dt15(DATA_IN[15]), .Dt14(DATA_IN[14]),
    .Dt13(DATA_IN[13]), .Dt12(DATA_IN[12]), .Dt11(DATA_IN[11]), .Dt10(DATA_IN[10]), .Dt09(DATA_IN[9]),
    .Dt08(DATA_IN[8]), .Dt07(DATA_IN[7]), .Dt06(DATA_IN[6]), .Dt05(DATA_IN[5]), .Dt04(DATA_IN[4]),
    .Dt03(DATA_IN[3]), .Dt02(DATA_IN[2]), .Dt01(DATA_IN[1]), .Dt00(DATA_IN[0]), .S31(registrador_2_s00[31]),
    .S30(registrador_2_s00[30]), .S29(registrador_2_s00[29]), .S28(registrador_2_s00[28]),
    .S27(registrador_2_s00[27]), .S26(registrador_2_s00[26]), .S25(registrador_2_s00[25]),
    .S24(registrador_2_s00[24]), .S23(registrador_2_s00[23]), .S22(registrador_2_s00[22]),
    .S21(registrador_2_s00[21]), .S20(registrador_2_s00[20]), .S19(registrador_2_s00[19]),
    .S18(registrador_2_s00[18]), .S17(registrador_2_s00[17]), .S16(registrador_2_s00[16]),
    .S15(registrador_2_s00[15]), .S14(registrador_2_s00[14]), .S13(registrador_2_s00[13]),
    .S12(registrador_2_s00[12]), .S11(registrador_2_s00[11]), .S10(registrador_2_s00[10]),
    .S09(registrador_2_s00[9]), .S08(registrador_2_s00[8]), .S07(registrador_2_s00[7]),
    .S06(registrador_2_s00[6]), .S05(registrador_2_s00[5]), .S04(registrador_2_s00[4]),
    .S03(registrador_2_s00[3]), .S02(registrador_2_s00[2]), .S01(registrador_2_s00[1]),
    .S00(registrador_2_s00[0]));
  registrador registrador_3 (
    .write(demultiplexer_1_out8), .clear(clear), .Dt31(DATA_IN[31]), .Dt30(DATA_IN[30]), .Dt29(DATA_IN[29]),
    .Dt28(DATA_IN[28]), .Dt27(DATA_IN[27]), .Dt26(DATA_IN[26]), .Dt25(DATA_IN[25]), .Dt24(DATA_IN[24]),
    .Dt23(DATA_IN[23]), .Dt22(DATA_IN[22]), .Dt21(DATA_IN[21]), .Dt20(DATA_IN[20]), .Dt19(DATA_IN[19]),
    .Dt18(DATA_IN[18]), .Dt17(DATA_IN[17]), .Dt16(DATA_IN[16]), .Dt15(DATA_IN[15]), .Dt14(DATA_IN[14]),
    .Dt13(DATA_IN[13]), .Dt12(DATA_IN[12]), .Dt11(DATA_IN[11]), .Dt10(DATA_IN[10]), .Dt09(DATA_IN[9]),
    .Dt08(DATA_IN[8]), .Dt07(DATA_IN[7]), .Dt06(DATA_IN[6]), .Dt05(DATA_IN[5]), .Dt04(DATA_IN[4]),
    .Dt03(DATA_IN[3]), .Dt02(DATA_IN[2]), .Dt01(DATA_IN[1]), .Dt00(DATA_IN[0]), .S31(registrador_3_s00[31]),
    .S30(registrador_3_s00[30]), .S29(registrador_3_s00[29]), .S28(registrador_3_s00[28]),
    .S27(registrador_3_s00[27]), .S26(registrador_3_s00[26]), .S25(registrador_3_s00[25]),
    .S24(registrador_3_s00[24]), .S23(registrador_3_s00[23]), .S22(registrador_3_s00[22]),
    .S21(registrador_3_s00[21]), .S20(registrador_3_s00[20]), .S19(registrador_3_s00[19]),
    .S18(registrador_3_s00[18]), .S17(registrador_3_s00[17]), .S16(registrador_3_s00[16]),
    .S15(registrador_3_s00[15]), .S14(registrador_3_s00[14]), .S13(registrador_3_s00[13]),
    .S12(registrador_3_s00[12]), .S11(registrador_3_s00[11]), .S10(registrador_3_s00[10]),
    .S09(registrador_3_s00[9]), .S08(registrador_3_s00[8]), .S07(registrador_3_s00[7]),
    .S06(registrador_3_s00[6]), .S05(registrador_3_s00[5]), .S04(registrador_3_s00[4]),
    .S03(registrador_3_s00[3]), .S02(registrador_3_s00[2]), .S01(registrador_3_s00[1]),
    .S00(registrador_3_s00[0]));
  registrador registrador_4 (
    .write(demultiplexer_1_out9), .clear(clear), .Dt31(DATA_IN[31]), .Dt30(DATA_IN[30]), .Dt29(DATA_IN[29]),
    .Dt28(DATA_IN[28]), .Dt27(DATA_IN[27]), .Dt26(DATA_IN[26]), .Dt25(DATA_IN[25]), .Dt24(DATA_IN[24]),
    .Dt23(DATA_IN[23]), .Dt22(DATA_IN[22]), .Dt21(DATA_IN[21]), .Dt20(DATA_IN[20]), .Dt19(DATA_IN[19]),
    .Dt18(DATA_IN[18]), .Dt17(DATA_IN[17]), .Dt16(DATA_IN[16]), .Dt15(DATA_IN[15]), .Dt14(DATA_IN[14]),
    .Dt13(DATA_IN[13]), .Dt12(DATA_IN[12]), .Dt11(DATA_IN[11]), .Dt10(DATA_IN[10]), .Dt09(DATA_IN[9]),
    .Dt08(DATA_IN[8]), .Dt07(DATA_IN[7]), .Dt06(DATA_IN[6]), .Dt05(DATA_IN[5]), .Dt04(DATA_IN[4]),
    .Dt03(DATA_IN[3]), .Dt02(DATA_IN[2]), .Dt01(DATA_IN[1]), .Dt00(DATA_IN[0]), .S31(registrador_4_s00[31]),
    .S30(registrador_4_s00[30]), .S29(registrador_4_s00[29]), .S28(registrador_4_s00[28]),
    .S27(registrador_4_s00[27]), .S26(registrador_4_s00[26]), .S25(registrador_4_s00[25]),
    .S24(registrador_4_s00[24]), .S23(registrador_4_s00[23]), .S22(registrador_4_s00[22]),
    .S21(registrador_4_s00[21]), .S20(registrador_4_s00[20]), .S19(registrador_4_s00[19]),
    .S18(registrador_4_s00[18]), .S17(registrador_4_s00[17]), .S16(registrador_4_s00[16]),
    .S15(registrador_4_s00[15]), .S14(registrador_4_s00[14]), .S13(registrador_4_s00[13]),
    .S12(registrador_4_s00[12]), .S11(registrador_4_s00[11]), .S10(registrador_4_s00[10]),
    .S09(registrador_4_s00[9]), .S08(registrador_4_s00[8]), .S07(registrador_4_s00[7]),
    .S06(registrador_4_s00[6]), .S05(registrador_4_s00[5]), .S04(registrador_4_s00[4]),
    .S03(registrador_4_s00[3]), .S02(registrador_4_s00[2]), .S01(registrador_4_s00[1]),
    .S00(registrador_4_s00[0]));
  registrador registrador_5 (
    .write(demultiplexer_1_out10), .clear(clear), .Dt31(DATA_IN[31]), .Dt30(DATA_IN[30]), .Dt29(DATA_IN[29]),
    .Dt28(DATA_IN[28]), .Dt27(DATA_IN[27]), .Dt26(DATA_IN[26]), .Dt25(DATA_IN[25]), .Dt24(DATA_IN[24]),
    .Dt23(DATA_IN[23]), .Dt22(DATA_IN[22]), .Dt21(DATA_IN[21]), .Dt20(DATA_IN[20]), .Dt19(DATA_IN[19]),
    .Dt18(DATA_IN[18]), .Dt17(DATA_IN[17]), .Dt16(DATA_IN[16]), .Dt15(DATA_IN[15]), .Dt14(DATA_IN[14]),
    .Dt13(DATA_IN[13]), .Dt12(DATA_IN[12]), .Dt11(DATA_IN[11]), .Dt10(DATA_IN[10]), .Dt09(DATA_IN[9]),
    .Dt08(DATA_IN[8]), .Dt07(DATA_IN[7]), .Dt06(DATA_IN[6]), .Dt05(DATA_IN[5]), .Dt04(DATA_IN[4]),
    .Dt03(DATA_IN[3]), .Dt02(DATA_IN[2]), .Dt01(DATA_IN[1]), .Dt00(DATA_IN[0]), .S31(registrador_5_s00[31]),
    .S30(registrador_5_s00[30]), .S29(registrador_5_s00[29]), .S28(registrador_5_s00[28]),
    .S27(registrador_5_s00[27]), .S26(registrador_5_s00[26]), .S25(registrador_5_s00[25]),
    .S24(registrador_5_s00[24]), .S23(registrador_5_s00[23]), .S22(registrador_5_s00[22]),
    .S21(registrador_5_s00[21]), .S20(registrador_5_s00[20]), .S19(registrador_5_s00[19]),
    .S18(registrador_5_s00[18]), .S17(registrador_5_s00[17]), .S16(registrador_5_s00[16]),
    .S15(registrador_5_s00[15]), .S14(registrador_5_s00[14]), .S13(registrador_5_s00[13]),
    .S12(registrador_5_s00[12]), .S11(registrador_5_s00[11]), .S10(registrador_5_s00[10]),
    .S09(registrador_5_s00[9]), .S08(registrador_5_s00[8]), .S07(registrador_5_s00[7]),
    .S06(registrador_5_s00[6]), .S05(registrador_5_s00[5]), .S04(registrador_5_s00[4]),
    .S03(registrador_5_s00[3]), .S02(registrador_5_s00[2]), .S01(registrador_5_s00[1]),
    .S00(registrador_5_s00[0]));
  registrador registrador_6 (
    .write(demultiplexer_1_out11), .clear(clear), .Dt31(DATA_IN[31]), .Dt30(DATA_IN[30]), .Dt29(DATA_IN[29]),
    .Dt28(DATA_IN[28]), .Dt27(DATA_IN[27]), .Dt26(DATA_IN[26]), .Dt25(DATA_IN[25]), .Dt24(DATA_IN[24]),
    .Dt23(DATA_IN[23]), .Dt22(DATA_IN[22]), .Dt21(DATA_IN[21]), .Dt20(DATA_IN[20]), .Dt19(DATA_IN[19]),
    .Dt18(DATA_IN[18]), .Dt17(DATA_IN[17]), .Dt16(DATA_IN[16]), .Dt15(DATA_IN[15]), .Dt14(DATA_IN[14]),
    .Dt13(DATA_IN[13]), .Dt12(DATA_IN[12]), .Dt11(DATA_IN[11]), .Dt10(DATA_IN[10]), .Dt09(DATA_IN[9]),
    .Dt08(DATA_IN[8]), .Dt07(DATA_IN[7]), .Dt06(DATA_IN[6]), .Dt05(DATA_IN[5]), .Dt04(DATA_IN[4]),
    .Dt03(DATA_IN[3]), .Dt02(DATA_IN[2]), .Dt01(DATA_IN[1]), .Dt00(DATA_IN[0]), .S31(registrador_6_s00[31]),
    .S30(registrador_6_s00[30]), .S29(registrador_6_s00[29]), .S28(registrador_6_s00[28]),
    .S27(registrador_6_s00[27]), .S26(registrador_6_s00[26]), .S25(registrador_6_s00[25]),
    .S24(registrador_6_s00[24]), .S23(registrador_6_s00[23]), .S22(registrador_6_s00[22]),
    .S21(registrador_6_s00[21]), .S20(registrador_6_s00[20]), .S19(registrador_6_s00[19]),
    .S18(registrador_6_s00[18]), .S17(registrador_6_s00[17]), .S16(registrador_6_s00[16]),
    .S15(registrador_6_s00[15]), .S14(registrador_6_s00[14]), .S13(registrador_6_s00[13]),
    .S12(registrador_6_s00[12]), .S11(registrador_6_s00[11]), .S10(registrador_6_s00[10]),
    .S09(registrador_6_s00[9]), .S08(registrador_6_s00[8]), .S07(registrador_6_s00[7]),
    .S06(registrador_6_s00[6]), .S05(registrador_6_s00[5]), .S04(registrador_6_s00[4]),
    .S03(registrador_6_s00[3]), .S02(registrador_6_s00[2]), .S01(registrador_6_s00[1]),
    .S00(registrador_6_s00[0]));
  registrador registrador_7 (
    .write(demultiplexer_1_out12), .clear(clear), .Dt31(DATA_IN[31]), .Dt30(DATA_IN[30]), .Dt29(DATA_IN[29]),
    .Dt28(DATA_IN[28]), .Dt27(DATA_IN[27]), .Dt26(DATA_IN[26]), .Dt25(DATA_IN[25]), .Dt24(DATA_IN[24]),
    .Dt23(DATA_IN[23]), .Dt22(DATA_IN[22]), .Dt21(DATA_IN[21]), .Dt20(DATA_IN[20]), .Dt19(DATA_IN[19]),
    .Dt18(DATA_IN[18]), .Dt17(DATA_IN[17]), .Dt16(DATA_IN[16]), .Dt15(DATA_IN[15]), .Dt14(DATA_IN[14]),
    .Dt13(DATA_IN[13]), .Dt12(DATA_IN[12]), .Dt11(DATA_IN[11]), .Dt10(DATA_IN[10]), .Dt09(DATA_IN[9]),
    .Dt08(DATA_IN[8]), .Dt07(DATA_IN[7]), .Dt06(DATA_IN[6]), .Dt05(DATA_IN[5]), .Dt04(DATA_IN[4]),
    .Dt03(DATA_IN[3]), .Dt02(DATA_IN[2]), .Dt01(DATA_IN[1]), .Dt00(DATA_IN[0]), .S31(registrador_7_s00[31]),
    .S30(registrador_7_s00[30]), .S29(registrador_7_s00[29]), .S28(registrador_7_s00[28]),
    .S27(registrador_7_s00[27]), .S26(registrador_7_s00[26]), .S25(registrador_7_s00[25]),
    .S24(registrador_7_s00[24]), .S23(registrador_7_s00[23]), .S22(registrador_7_s00[22]),
    .S21(registrador_7_s00[21]), .S20(registrador_7_s00[20]), .S19(registrador_7_s00[19]),
    .S18(registrador_7_s00[18]), .S17(registrador_7_s00[17]), .S16(registrador_7_s00[16]),
    .S15(registrador_7_s00[15]), .S14(registrador_7_s00[14]), .S13(registrador_7_s00[13]),
    .S12(registrador_7_s00[12]), .S11(registrador_7_s00[11]), .S10(registrador_7_s00[10]),
    .S09(registrador_7_s00[9]), .S08(registrador_7_s00[8]), .S07(registrador_7_s00[7]),
    .S06(registrador_7_s00[6]), .S05(registrador_7_s00[5]), .S04(registrador_7_s00[4]),
    .S03(registrador_7_s00[3]), .S02(registrador_7_s00[2]), .S01(registrador_7_s00[1]),
    .S00(registrador_7_s00[0]));
  registrador registrador_8 (
    .write(demultiplexer_1_out13), .clear(clear), .Dt31(DATA_IN[31]), .Dt30(DATA_IN[30]), .Dt29(DATA_IN[29]),
    .Dt28(DATA_IN[28]), .Dt27(DATA_IN[27]), .Dt26(DATA_IN[26]), .Dt25(DATA_IN[25]), .Dt24(DATA_IN[24]),
    .Dt23(DATA_IN[23]), .Dt22(DATA_IN[22]), .Dt21(DATA_IN[21]), .Dt20(DATA_IN[20]), .Dt19(DATA_IN[19]),
    .Dt18(DATA_IN[18]), .Dt17(DATA_IN[17]), .Dt16(DATA_IN[16]), .Dt15(DATA_IN[15]), .Dt14(DATA_IN[14]),
    .Dt13(DATA_IN[13]), .Dt12(DATA_IN[12]), .Dt11(DATA_IN[11]), .Dt10(DATA_IN[10]), .Dt09(DATA_IN[9]),
    .Dt08(DATA_IN[8]), .Dt07(DATA_IN[7]), .Dt06(DATA_IN[6]), .Dt05(DATA_IN[5]), .Dt04(DATA_IN[4]),
    .Dt03(DATA_IN[3]), .Dt02(DATA_IN[2]), .Dt01(DATA_IN[1]), .Dt00(DATA_IN[0]), .S31(registrador_8_s00[31]),
    .S30(registrador_8_s00[30]), .S29(registrador_8_s00[29]), .S28(registrador_8_s00[28]),
    .S27(registrador_8_s00[27]), .S26(registrador_8_s00[26]), .S25(registrador_8_s00[25]),
    .S24(registrador_8_s00[24]), .S23(registrador_8_s00[23]), .S22(registrador_8_s00[22]),
    .S21(registrador_8_s00[21]), .S20(registrador_8_s00[20]), .S19(registrador_8_s00[19]),
    .S18(registrador_8_s00[18]), .S17(registrador_8_s00[17]), .S16(registrador_8_s00[16]),
    .S15(registrador_8_s00[15]), .S14(registrador_8_s00[14]), .S13(registrador_8_s00[13]),
    .S12(registrador_8_s00[12]), .S11(registrador_8_s00[11]), .S10(registrador_8_s00[10]),
    .S09(registrador_8_s00[9]), .S08(registrador_8_s00[8]), .S07(registrador_8_s00[7]),
    .S06(registrador_8_s00[6]), .S05(registrador_8_s00[5]), .S04(registrador_8_s00[4]),
    .S03(registrador_8_s00[3]), .S02(registrador_8_s00[2]), .S01(registrador_8_s00[1]),
    .S00(registrador_8_s00[0]));
  registrador registrador_9 (
    .write(demultiplexer_1_out14), .clear(clear), .Dt31(DATA_IN[31]), .Dt30(DATA_IN[30]), .Dt29(DATA_IN[29]),
    .Dt28(DATA_IN[28]), .Dt27(DATA_IN[27]), .Dt26(DATA_IN[26]), .Dt25(DATA_IN[25]), .Dt24(DATA_IN[24]),
    .Dt23(DATA_IN[23]), .Dt22(DATA_IN[22]), .Dt21(DATA_IN[21]), .Dt20(DATA_IN[20]), .Dt19(DATA_IN[19]),
    .Dt18(DATA_IN[18]), .Dt17(DATA_IN[17]), .Dt16(DATA_IN[16]), .Dt15(DATA_IN[15]), .Dt14(DATA_IN[14]),
    .Dt13(DATA_IN[13]), .Dt12(DATA_IN[12]), .Dt11(DATA_IN[11]), .Dt10(DATA_IN[10]), .Dt09(DATA_IN[9]),
    .Dt08(DATA_IN[8]), .Dt07(DATA_IN[7]), .Dt06(DATA_IN[6]), .Dt05(DATA_IN[5]), .Dt04(DATA_IN[4]),
    .Dt03(DATA_IN[3]), .Dt02(DATA_IN[2]), .Dt01(DATA_IN[1]), .Dt00(DATA_IN[0]), .S31(registrador_9_s00[31]),
    .S30(registrador_9_s00[30]), .S29(registrador_9_s00[29]), .S28(registrador_9_s00[28]),
    .S27(registrador_9_s00[27]), .S26(registrador_9_s00[26]), .S25(registrador_9_s00[25]),
    .S24(registrador_9_s00[24]), .S23(registrador_9_s00[23]), .S22(registrador_9_s00[22]),
    .S21(registrador_9_s00[21]), .S20(registrador_9_s00[20]), .S19(registrador_9_s00[19]),
    .S18(registrador_9_s00[18]), .S17(registrador_9_s00[17]), .S16(registrador_9_s00[16]),
    .S15(registrador_9_s00[15]), .S14(registrador_9_s00[14]), .S13(registrador_9_s00[13]),
    .S12(registrador_9_s00[12]), .S11(registrador_9_s00[11]), .S10(registrador_9_s00[10]),
    .S09(registrador_9_s00[9]), .S08(registrador_9_s00[8]), .S07(registrador_9_s00[7]),
    .S06(registrador_9_s00[6]), .S05(registrador_9_s00[5]), .S04(registrador_9_s00[4]),
    .S03(registrador_9_s00[3]), .S02(registrador_9_s00[2]), .S01(registrador_9_s00[1]),
    .S00(registrador_9_s00[0]));
  registrador registrador_10 (
    .write(demultiplexer_1_out15), .clear(clear), .Dt31(DATA_IN[31]), .Dt30(DATA_IN[30]), .Dt29(DATA_IN[29]),
    .Dt28(DATA_IN[28]), .Dt27(DATA_IN[27]), .Dt26(DATA_IN[26]), .Dt25(DATA_IN[25]), .Dt24(DATA_IN[24]),
    .Dt23(DATA_IN[23]), .Dt22(DATA_IN[22]), .Dt21(DATA_IN[21]), .Dt20(DATA_IN[20]), .Dt19(DATA_IN[19]),
    .Dt18(DATA_IN[18]), .Dt17(DATA_IN[17]), .Dt16(DATA_IN[16]), .Dt15(DATA_IN[15]), .Dt14(DATA_IN[14]),
    .Dt13(DATA_IN[13]), .Dt12(DATA_IN[12]), .Dt11(DATA_IN[11]), .Dt10(DATA_IN[10]), .Dt09(DATA_IN[9]),
    .Dt08(DATA_IN[8]), .Dt07(DATA_IN[7]), .Dt06(DATA_IN[6]), .Dt05(DATA_IN[5]), .Dt04(DATA_IN[4]),
    .Dt03(DATA_IN[3]), .Dt02(DATA_IN[2]), .Dt01(DATA_IN[1]), .Dt00(DATA_IN[0]), .S31(registrador_10_s00[31]),
    .S30(registrador_10_s00[30]), .S29(registrador_10_s00[29]), .S28(registrador_10_s00[28]),
    .S27(registrador_10_s00[27]), .S26(registrador_10_s00[26]), .S25(registrador_10_s00[25]),
    .S24(registrador_10_s00[24]), .S23(registrador_10_s00[23]), .S22(registrador_10_s00[22]),
    .S21(registrador_10_s00[21]), .S20(registrador_10_s00[20]), .S19(registrador_10_s00[19]),
    .S18(registrador_10_s00[18]), .S17(registrador_10_s00[17]), .S16(registrador_10_s00[16]),
    .S15(registrador_10_s00[15]), .S14(registrador_10_s00[14]), .S13(registrador_10_s00[13]),
    .S12(registrador_10_s00[12]), .S11(registrador_10_s00[11]), .S10(registrador_10_s00[10]),
    .S09(registrador_10_s00[9]), .S08(registrador_10_s00[8]), .S07(registrador_10_s00[7]),
    .S06(registrador_10_s00[6]), .S05(registrador_10_s00[5]), .S04(registrador_10_s00[4]),
    .S03(registrador_10_s00[3]), .S02(registrador_10_s00[2]), .S01(registrador_10_s00[1]),
    .S00(registrador_10_s00[0]));
  registrador registrador_11 (
    .write(demultiplexer_1_out16), .clear(clear), .Dt31(DATA_IN[31]), .Dt30(DATA_IN[30]), .Dt29(DATA_IN[29]),
    .Dt28(DATA_IN[28]), .Dt27(DATA_IN[27]), .Dt26(DATA_IN[26]), .Dt25(DATA_IN[25]), .Dt24(DATA_IN[24]),
    .Dt23(DATA_IN[23]), .Dt22(DATA_IN[22]), .Dt21(DATA_IN[21]), .Dt20(DATA_IN[20]), .Dt19(DATA_IN[19]),
    .Dt18(DATA_IN[18]), .Dt17(DATA_IN[17]), .Dt16(DATA_IN[16]), .Dt15(DATA_IN[15]), .Dt14(DATA_IN[14]),
    .Dt13(DATA_IN[13]), .Dt12(DATA_IN[12]), .Dt11(DATA_IN[11]), .Dt10(DATA_IN[10]), .Dt09(DATA_IN[9]),
    .Dt08(DATA_IN[8]), .Dt07(DATA_IN[7]), .Dt06(DATA_IN[6]), .Dt05(DATA_IN[5]), .Dt04(DATA_IN[4]),
    .Dt03(DATA_IN[3]), .Dt02(DATA_IN[2]), .Dt01(DATA_IN[1]), .Dt00(DATA_IN[0]), .S31(registrador_11_s00[31]),
    .S30(registrador_11_s00[30]), .S29(registrador_11_s00[29]), .S28(registrador_11_s00[28]),
    .S27(registrador_11_s00[27]), .S26(registrador_11_s00[26]), .S25(registrador_11_s00[25]),
    .S24(registrador_11_s00[24]), .S23(registrador_11_s00[23]), .S22(registrador_11_s00[22]),
    .S21(registrador_11_s00[21]), .S20(registrador_11_s00[20]), .S19(registrador_11_s00[19]),
    .S18(registrador_11_s00[18]), .S17(registrador_11_s00[17]), .S16(registrador_11_s00[16]),
    .S15(registrador_11_s00[15]), .S14(registrador_11_s00[14]), .S13(registrador_11_s00[13]),
    .S12(registrador_11_s00[12]), .S11(registrador_11_s00[11]), .S10(registrador_11_s00[10]),
    .S09(registrador_11_s00[9]), .S08(registrador_11_s00[8]), .S07(registrador_11_s00[7]),
    .S06(registrador_11_s00[6]), .S05(registrador_11_s00[5]), .S04(registrador_11_s00[4]),
    .S03(registrador_11_s00[3]), .S02(registrador_11_s00[2]), .S01(registrador_11_s00[1]),
    .S00(registrador_11_s00[0]));
  registrador registrador_12 (
    .write(demultiplexer_1_out17), .clear(clear), .Dt31(DATA_IN[31]), .Dt30(DATA_IN[30]), .Dt29(DATA_IN[29]),
    .Dt28(DATA_IN[28]), .Dt27(DATA_IN[27]), .Dt26(DATA_IN[26]), .Dt25(DATA_IN[25]), .Dt24(DATA_IN[24]),
    .Dt23(DATA_IN[23]), .Dt22(DATA_IN[22]), .Dt21(DATA_IN[21]), .Dt20(DATA_IN[20]), .Dt19(DATA_IN[19]),
    .Dt18(DATA_IN[18]), .Dt17(DATA_IN[17]), .Dt16(DATA_IN[16]), .Dt15(DATA_IN[15]), .Dt14(DATA_IN[14]),
    .Dt13(DATA_IN[13]), .Dt12(DATA_IN[12]), .Dt11(DATA_IN[11]), .Dt10(DATA_IN[10]), .Dt09(DATA_IN[9]),
    .Dt08(DATA_IN[8]), .Dt07(DATA_IN[7]), .Dt06(DATA_IN[6]), .Dt05(DATA_IN[5]), .Dt04(DATA_IN[4]),
    .Dt03(DATA_IN[3]), .Dt02(DATA_IN[2]), .Dt01(DATA_IN[1]), .Dt00(DATA_IN[0]), .S31(registrador_12_s00[31]),
    .S30(registrador_12_s00[30]), .S29(registrador_12_s00[29]), .S28(registrador_12_s00[28]),
    .S27(registrador_12_s00[27]), .S26(registrador_12_s00[26]), .S25(registrador_12_s00[25]),
    .S24(registrador_12_s00[24]), .S23(registrador_12_s00[23]), .S22(registrador_12_s00[22]),
    .S21(registrador_12_s00[21]), .S20(registrador_12_s00[20]), .S19(registrador_12_s00[19]),
    .S18(registrador_12_s00[18]), .S17(registrador_12_s00[17]), .S16(registrador_12_s00[16]),
    .S15(registrador_12_s00[15]), .S14(registrador_12_s00[14]), .S13(registrador_12_s00[13]),
    .S12(registrador_12_s00[12]), .S11(registrador_12_s00[11]), .S10(registrador_12_s00[10]),
    .S09(registrador_12_s00[9]), .S08(registrador_12_s00[8]), .S07(registrador_12_s00[7]),
    .S06(registrador_12_s00[6]), .S05(registrador_12_s00[5]), .S04(registrador_12_s00[4]),
    .S03(registrador_12_s00[3]), .S02(registrador_12_s00[2]), .S01(registrador_12_s00[1]),
    .S00(registrador_12_s00[0]));
  registrador registrador_13 (
    .write(demultiplexer_1_out18), .clear(clear), .Dt31(DATA_IN[31]), .Dt30(DATA_IN[30]), .Dt29(DATA_IN[29]),
    .Dt28(DATA_IN[28]), .Dt27(DATA_IN[27]), .Dt26(DATA_IN[26]), .Dt25(DATA_IN[25]), .Dt24(DATA_IN[24]),
    .Dt23(DATA_IN[23]), .Dt22(DATA_IN[22]), .Dt21(DATA_IN[21]), .Dt20(DATA_IN[20]), .Dt19(DATA_IN[19]),
    .Dt18(DATA_IN[18]), .Dt17(DATA_IN[17]), .Dt16(DATA_IN[16]), .Dt15(DATA_IN[15]), .Dt14(DATA_IN[14]),
    .Dt13(DATA_IN[13]), .Dt12(DATA_IN[12]), .Dt11(DATA_IN[11]), .Dt10(DATA_IN[10]), .Dt09(DATA_IN[9]),
    .Dt08(DATA_IN[8]), .Dt07(DATA_IN[7]), .Dt06(DATA_IN[6]), .Dt05(DATA_IN[5]), .Dt04(DATA_IN[4]),
    .Dt03(DATA_IN[3]), .Dt02(DATA_IN[2]), .Dt01(DATA_IN[1]), .Dt00(DATA_IN[0]), .S31(registrador_13_s00[31]),
    .S30(registrador_13_s00[30]), .S29(registrador_13_s00[29]), .S28(registrador_13_s00[28]),
    .S27(registrador_13_s00[27]), .S26(registrador_13_s00[26]), .S25(registrador_13_s00[25]),
    .S24(registrador_13_s00[24]), .S23(registrador_13_s00[23]), .S22(registrador_13_s00[22]),
    .S21(registrador_13_s00[21]), .S20(registrador_13_s00[20]), .S19(registrador_13_s00[19]),
    .S18(registrador_13_s00[18]), .S17(registrador_13_s00[17]), .S16(registrador_13_s00[16]),
    .S15(registrador_13_s00[15]), .S14(registrador_13_s00[14]), .S13(registrador_13_s00[13]),
    .S12(registrador_13_s00[12]), .S11(registrador_13_s00[11]), .S10(registrador_13_s00[10]),
    .S09(registrador_13_s00[9]), .S08(registrador_13_s00[8]), .S07(registrador_13_s00[7]),
    .S06(registrador_13_s00[6]), .S05(registrador_13_s00[5]), .S04(registrador_13_s00[4]),
    .S03(registrador_13_s00[3]), .S02(registrador_13_s00[2]), .S01(registrador_13_s00[1]),
    .S00(registrador_13_s00[0]));
  registrador registrador_14 (
    .write(demultiplexer_1_out19), .clear(clear), .Dt31(DATA_IN[31]), .Dt30(DATA_IN[30]), .Dt29(DATA_IN[29]),
    .Dt28(DATA_IN[28]), .Dt27(DATA_IN[27]), .Dt26(DATA_IN[26]), .Dt25(DATA_IN[25]), .Dt24(DATA_IN[24]),
    .Dt23(DATA_IN[23]), .Dt22(DATA_IN[22]), .Dt21(DATA_IN[21]), .Dt20(DATA_IN[20]), .Dt19(DATA_IN[19]),
    .Dt18(DATA_IN[18]), .Dt17(DATA_IN[17]), .Dt16(DATA_IN[16]), .Dt15(DATA_IN[15]), .Dt14(DATA_IN[14]),
    .Dt13(DATA_IN[13]), .Dt12(DATA_IN[12]), .Dt11(DATA_IN[11]), .Dt10(DATA_IN[10]), .Dt09(DATA_IN[9]),
    .Dt08(DATA_IN[8]), .Dt07(DATA_IN[7]), .Dt06(DATA_IN[6]), .Dt05(DATA_IN[5]), .Dt04(DATA_IN[4]),
    .Dt03(DATA_IN[3]), .Dt02(DATA_IN[2]), .Dt01(DATA_IN[1]), .Dt00(DATA_IN[0]), .S31(registrador_14_s00[31]),
    .S30(registrador_14_s00[30]), .S29(registrador_14_s00[29]), .S28(registrador_14_s00[28]),
    .S27(registrador_14_s00[27]), .S26(registrador_14_s00[26]), .S25(registrador_14_s00[25]),
    .S24(registrador_14_s00[24]), .S23(registrador_14_s00[23]), .S22(registrador_14_s00[22]),
    .S21(registrador_14_s00[21]), .S20(registrador_14_s00[20]), .S19(registrador_14_s00[19]),
    .S18(registrador_14_s00[18]), .S17(registrador_14_s00[17]), .S16(registrador_14_s00[16]),
    .S15(registrador_14_s00[15]), .S14(registrador_14_s00[14]), .S13(registrador_14_s00[13]),
    .S12(registrador_14_s00[12]), .S11(registrador_14_s00[11]), .S10(registrador_14_s00[10]),
    .S09(registrador_14_s00[9]), .S08(registrador_14_s00[8]), .S07(registrador_14_s00[7]),
    .S06(registrador_14_s00[6]), .S05(registrador_14_s00[5]), .S04(registrador_14_s00[4]),
    .S03(registrador_14_s00[3]), .S02(registrador_14_s00[2]), .S01(registrador_14_s00[1]),
    .S00(registrador_14_s00[0]));
  registrador registrador_15 (
    .write(demultiplexer_1_out20), .clear(clear), .Dt31(DATA_IN[31]), .Dt30(DATA_IN[30]), .Dt29(DATA_IN[29]),
    .Dt28(DATA_IN[28]), .Dt27(DATA_IN[27]), .Dt26(DATA_IN[26]), .Dt25(DATA_IN[25]), .Dt24(DATA_IN[24]),
    .Dt23(DATA_IN[23]), .Dt22(DATA_IN[22]), .Dt21(DATA_IN[21]), .Dt20(DATA_IN[20]), .Dt19(DATA_IN[19]),
    .Dt18(DATA_IN[18]), .Dt17(DATA_IN[17]), .Dt16(DATA_IN[16]), .Dt15(DATA_IN[15]), .Dt14(DATA_IN[14]),
    .Dt13(DATA_IN[13]), .Dt12(DATA_IN[12]), .Dt11(DATA_IN[11]), .Dt10(DATA_IN[10]), .Dt09(DATA_IN[9]),
    .Dt08(DATA_IN[8]), .Dt07(DATA_IN[7]), .Dt06(DATA_IN[6]), .Dt05(DATA_IN[5]), .Dt04(DATA_IN[4]),
    .Dt03(DATA_IN[3]), .Dt02(DATA_IN[2]), .Dt01(DATA_IN[1]), .Dt00(DATA_IN[0]), .S31(registrador_15_s00[31]),
    .S30(registrador_15_s00[30]), .S29(registrador_15_s00[29]), .S28(registrador_15_s00[28]),
    .S27(registrador_15_s00[27]), .S26(registrador_15_s00[26]), .S25(registrador_15_s00[25]),
    .S24(registrador_15_s00[24]), .S23(registrador_15_s00[23]), .S22(registrador_15_s00[22]),
    .S21(registrador_15_s00[21]), .S20(registrador_15_s00[20]), .S19(registrador_15_s00[19]),
    .S18(registrador_15_s00[18]), .S17(registrador_15_s00[17]), .S16(registrador_15_s00[16]),
    .S15(registrador_15_s00[15]), .S14(registrador_15_s00[14]), .S13(registrador_15_s00[13]),
    .S12(registrador_15_s00[12]), .S11(registrador_15_s00[11]), .S10(registrador_15_s00[10]),
    .S09(registrador_15_s00[9]), .S08(registrador_15_s00[8]), .S07(registrador_15_s00[7]),
    .S06(registrador_15_s00[6]), .S05(registrador_15_s00[5]), .S04(registrador_15_s00[4]),
    .S03(registrador_15_s00[3]), .S02(registrador_15_s00[2]), .S01(registrador_15_s00[1]),
    .S00(registrador_15_s00[0]));
  registrador registrador_16 (
    .write(demultiplexer_1_out21), .clear(clear), .Dt31(DATA_IN[31]), .Dt30(DATA_IN[30]), .Dt29(DATA_IN[29]),
    .Dt28(DATA_IN[28]), .Dt27(DATA_IN[27]), .Dt26(DATA_IN[26]), .Dt25(DATA_IN[25]), .Dt24(DATA_IN[24]),
    .Dt23(DATA_IN[23]), .Dt22(DATA_IN[22]), .Dt21(DATA_IN[21]), .Dt20(DATA_IN[20]), .Dt19(DATA_IN[19]),
    .Dt18(DATA_IN[18]), .Dt17(DATA_IN[17]), .Dt16(DATA_IN[16]), .Dt15(DATA_IN[15]), .Dt14(DATA_IN[14]),
    .Dt13(DATA_IN[13]), .Dt12(DATA_IN[12]), .Dt11(DATA_IN[11]), .Dt10(DATA_IN[10]), .Dt09(DATA_IN[9]),
    .Dt08(DATA_IN[8]), .Dt07(DATA_IN[7]), .Dt06(DATA_IN[6]), .Dt05(DATA_IN[5]), .Dt04(DATA_IN[4]),
    .Dt03(DATA_IN[3]), .Dt02(DATA_IN[2]), .Dt01(DATA_IN[1]), .Dt00(DATA_IN[0]), .S31(registrador_16_s00[31]),
    .S30(registrador_16_s00[30]), .S29(registrador_16_s00[29]), .S28(registrador_16_s00[28]),
    .S27(registrador_16_s00[27]), .S26(registrador_16_s00[26]), .S25(registrador_16_s00[25]),
    .S24(registrador_16_s00[24]), .S23(registrador_16_s00[23]), .S22(registrador_16_s00[22]),
    .S21(registrador_16_s00[21]), .S20(registrador_16_s00[20]), .S19(registrador_16_s00[19]),
    .S18(registrador_16_s00[18]), .S17(registrador_16_s00[17]), .S16(registrador_16_s00[16]),
    .S15(registrador_16_s00[15]), .S14(registrador_16_s00[14]), .S13(registrador_16_s00[13]),
    .S12(registrador_16_s00[12]), .S11(registrador_16_s00[11]), .S10(registrador_16_s00[10]),
    .S09(registrador_16_s00[9]), .S08(registrador_16_s00[8]), .S07(registrador_16_s00[7]),
    .S06(registrador_16_s00[6]), .S05(registrador_16_s00[5]), .S04(registrador_16_s00[4]),
    .S03(registrador_16_s00[3]), .S02(registrador_16_s00[2]), .S01(registrador_16_s00[1]),
    .S00(registrador_16_s00[0]));
  registrador registrador_17 (
    .write(demultiplexer_1_out22), .clear(clear), .Dt31(DATA_IN[31]), .Dt30(DATA_IN[30]), .Dt29(DATA_IN[29]),
    .Dt28(DATA_IN[28]), .Dt27(DATA_IN[27]), .Dt26(DATA_IN[26]), .Dt25(DATA_IN[25]), .Dt24(DATA_IN[24]),
    .Dt23(DATA_IN[23]), .Dt22(DATA_IN[22]), .Dt21(DATA_IN[21]), .Dt20(DATA_IN[20]), .Dt19(DATA_IN[19]),
    .Dt18(DATA_IN[18]), .Dt17(DATA_IN[17]), .Dt16(DATA_IN[16]), .Dt15(DATA_IN[15]), .Dt14(DATA_IN[14]),
    .Dt13(DATA_IN[13]), .Dt12(DATA_IN[12]), .Dt11(DATA_IN[11]), .Dt10(DATA_IN[10]), .Dt09(DATA_IN[9]),
    .Dt08(DATA_IN[8]), .Dt07(DATA_IN[7]), .Dt06(DATA_IN[6]), .Dt05(DATA_IN[5]), .Dt04(DATA_IN[4]),
    .Dt03(DATA_IN[3]), .Dt02(DATA_IN[2]), .Dt01(DATA_IN[1]), .Dt00(DATA_IN[0]), .S31(registrador_17_s00[31]),
    .S30(registrador_17_s00[30]), .S29(registrador_17_s00[29]), .S28(registrador_17_s00[28]),
    .S27(registrador_17_s00[27]), .S26(registrador_17_s00[26]), .S25(registrador_17_s00[25]),
    .S24(registrador_17_s00[24]), .S23(registrador_17_s00[23]), .S22(registrador_17_s00[22]),
    .S21(registrador_17_s00[21]), .S20(registrador_17_s00[20]), .S19(registrador_17_s00[19]),
    .S18(registrador_17_s00[18]), .S17(registrador_17_s00[17]), .S16(registrador_17_s00[16]),
    .S15(registrador_17_s00[15]), .S14(registrador_17_s00[14]), .S13(registrador_17_s00[13]),
    .S12(registrador_17_s00[12]), .S11(registrador_17_s00[11]), .S10(registrador_17_s00[10]),
    .S09(registrador_17_s00[9]), .S08(registrador_17_s00[8]), .S07(registrador_17_s00[7]),
    .S06(registrador_17_s00[6]), .S05(registrador_17_s00[5]), .S04(registrador_17_s00[4]),
    .S03(registrador_17_s00[3]), .S02(registrador_17_s00[2]), .S01(registrador_17_s00[1]),
    .S00(registrador_17_s00[0]));
  registrador registrador_18 (
    .write(demultiplexer_1_out23), .clear(clear), .Dt31(DATA_IN[31]), .Dt30(DATA_IN[30]), .Dt29(DATA_IN[29]),
    .Dt28(DATA_IN[28]), .Dt27(DATA_IN[27]), .Dt26(DATA_IN[26]), .Dt25(DATA_IN[25]), .Dt24(DATA_IN[24]),
    .Dt23(DATA_IN[23]), .Dt22(DATA_IN[22]), .Dt21(DATA_IN[21]), .Dt20(DATA_IN[20]), .Dt19(DATA_IN[19]),
    .Dt18(DATA_IN[18]), .Dt17(DATA_IN[17]), .Dt16(DATA_IN[16]), .Dt15(DATA_IN[15]), .Dt14(DATA_IN[14]),
    .Dt13(DATA_IN[13]), .Dt12(DATA_IN[12]), .Dt11(DATA_IN[11]), .Dt10(DATA_IN[10]), .Dt09(DATA_IN[9]),
    .Dt08(DATA_IN[8]), .Dt07(DATA_IN[7]), .Dt06(DATA_IN[6]), .Dt05(DATA_IN[5]), .Dt04(DATA_IN[4]),
    .Dt03(DATA_IN[3]), .Dt02(DATA_IN[2]), .Dt01(DATA_IN[1]), .Dt00(DATA_IN[0]), .S31(registrador_18_s00[31]),
    .S30(registrador_18_s00[30]), .S29(registrador_18_s00[29]), .S28(registrador_18_s00[28]),
    .S27(registrador_18_s00[27]), .S26(registrador_18_s00[26]), .S25(registrador_18_s00[25]),
    .S24(registrador_18_s00[24]), .S23(registrador_18_s00[23]), .S22(registrador_18_s00[22]),
    .S21(registrador_18_s00[21]), .S20(registrador_18_s00[20]), .S19(registrador_18_s00[19]),
    .S18(registrador_18_s00[18]), .S17(registrador_18_s00[17]), .S16(registrador_18_s00[16]),
    .S15(registrador_18_s00[15]), .S14(registrador_18_s00[14]), .S13(registrador_18_s00[13]),
    .S12(registrador_18_s00[12]), .S11(registrador_18_s00[11]), .S10(registrador_18_s00[10]),
    .S09(registrador_18_s00[9]), .S08(registrador_18_s00[8]), .S07(registrador_18_s00[7]),
    .S06(registrador_18_s00[6]), .S05(registrador_18_s00[5]), .S04(registrador_18_s00[4]),
    .S03(registrador_18_s00[3]), .S02(registrador_18_s00[2]), .S01(registrador_18_s00[1]),
    .S00(registrador_18_s00[0]));
  registrador registrador_19 (
    .write(demultiplexer_1_out24), .clear(clear), .Dt31(DATA_IN[31]), .Dt30(DATA_IN[30]), .Dt29(DATA_IN[29]),
    .Dt28(DATA_IN[28]), .Dt27(DATA_IN[27]), .Dt26(DATA_IN[26]), .Dt25(DATA_IN[25]), .Dt24(DATA_IN[24]),
    .Dt23(DATA_IN[23]), .Dt22(DATA_IN[22]), .Dt21(DATA_IN[21]), .Dt20(DATA_IN[20]), .Dt19(DATA_IN[19]),
    .Dt18(DATA_IN[18]), .Dt17(DATA_IN[17]), .Dt16(DATA_IN[16]), .Dt15(DATA_IN[15]), .Dt14(DATA_IN[14]),
    .Dt13(DATA_IN[13]), .Dt12(DATA_IN[12]), .Dt11(DATA_IN[11]), .Dt10(DATA_IN[10]), .Dt09(DATA_IN[9]),
    .Dt08(DATA_IN[8]), .Dt07(DATA_IN[7]), .Dt06(DATA_IN[6]), .Dt05(DATA_IN[5]), .Dt04(DATA_IN[4]),
    .Dt03(DATA_IN[3]), .Dt02(DATA_IN[2]), .Dt01(DATA_IN[1]), .Dt00(DATA_IN[0]), .S31(registrador_19_s00[31]),
    .S30(registrador_19_s00[30]), .S29(registrador_19_s00[29]), .S28(registrador_19_s00[28]),
    .S27(registrador_19_s00[27]), .S26(registrador_19_s00[26]), .S25(registrador_19_s00[25]),
    .S24(registrador_19_s00[24]), .S23(registrador_19_s00[23]), .S22(registrador_19_s00[22]),
    .S21(registrador_19_s00[21]), .S20(registrador_19_s00[20]), .S19(registrador_19_s00[19]),
    .S18(registrador_19_s00[18]), .S17(registrador_19_s00[17]), .S16(registrador_19_s00[16]),
    .S15(registrador_19_s00[15]), .S14(registrador_19_s00[14]), .S13(registrador_19_s00[13]),
    .S12(registrador_19_s00[12]), .S11(registrador_19_s00[11]), .S10(registrador_19_s00[10]),
    .S09(registrador_19_s00[9]), .S08(registrador_19_s00[8]), .S07(registrador_19_s00[7]),
    .S06(registrador_19_s00[6]), .S05(registrador_19_s00[5]), .S04(registrador_19_s00[4]),
    .S03(registrador_19_s00[3]), .S02(registrador_19_s00[2]), .S01(registrador_19_s00[1]),
    .S00(registrador_19_s00[0]));
  registrador registrador_20 (
    .write(demultiplexer_1_out25), .clear(clear), .Dt31(DATA_IN[31]), .Dt30(DATA_IN[30]), .Dt29(DATA_IN[29]),
    .Dt28(DATA_IN[28]), .Dt27(DATA_IN[27]), .Dt26(DATA_IN[26]), .Dt25(DATA_IN[25]), .Dt24(DATA_IN[24]),
    .Dt23(DATA_IN[23]), .Dt22(DATA_IN[22]), .Dt21(DATA_IN[21]), .Dt20(DATA_IN[20]), .Dt19(DATA_IN[19]),
    .Dt18(DATA_IN[18]), .Dt17(DATA_IN[17]), .Dt16(DATA_IN[16]), .Dt15(DATA_IN[15]), .Dt14(DATA_IN[14]),
    .Dt13(DATA_IN[13]), .Dt12(DATA_IN[12]), .Dt11(DATA_IN[11]), .Dt10(DATA_IN[10]), .Dt09(DATA_IN[9]),
    .Dt08(DATA_IN[8]), .Dt07(DATA_IN[7]), .Dt06(DATA_IN[6]), .Dt05(DATA_IN[5]), .Dt04(DATA_IN[4]),
    .Dt03(DATA_IN[3]), .Dt02(DATA_IN[2]), .Dt01(DATA_IN[1]), .Dt00(DATA_IN[0]), .S31(registrador_20_s00[31]),
    .S30(registrador_20_s00[30]), .S29(registrador_20_s00[29]), .S28(registrador_20_s00[28]),
    .S27(registrador_20_s00[27]), .S26(registrador_20_s00[26]), .S25(registrador_20_s00[25]),
    .S24(registrador_20_s00[24]), .S23(registrador_20_s00[23]), .S22(registrador_20_s00[22]),
    .S21(registrador_20_s00[21]), .S20(registrador_20_s00[20]), .S19(registrador_20_s00[19]),
    .S18(registrador_20_s00[18]), .S17(registrador_20_s00[17]), .S16(registrador_20_s00[16]),
    .S15(registrador_20_s00[15]), .S14(registrador_20_s00[14]), .S13(registrador_20_s00[13]),
    .S12(registrador_20_s00[12]), .S11(registrador_20_s00[11]), .S10(registrador_20_s00[10]),
    .S09(registrador_20_s00[9]), .S08(registrador_20_s00[8]), .S07(registrador_20_s00[7]),
    .S06(registrador_20_s00[6]), .S05(registrador_20_s00[5]), .S04(registrador_20_s00[4]),
    .S03(registrador_20_s00[3]), .S02(registrador_20_s00[2]), .S01(registrador_20_s00[1]),
    .S00(registrador_20_s00[0]));
  registrador registrador_21 (
    .write(demultiplexer_1_out26), .clear(clear), .Dt31(DATA_IN[31]), .Dt30(DATA_IN[30]), .Dt29(DATA_IN[29]),
    .Dt28(DATA_IN[28]), .Dt27(DATA_IN[27]), .Dt26(DATA_IN[26]), .Dt25(DATA_IN[25]), .Dt24(DATA_IN[24]),
    .Dt23(DATA_IN[23]), .Dt22(DATA_IN[22]), .Dt21(DATA_IN[21]), .Dt20(DATA_IN[20]), .Dt19(DATA_IN[19]),
    .Dt18(DATA_IN[18]), .Dt17(DATA_IN[17]), .Dt16(DATA_IN[16]), .Dt15(DATA_IN[15]), .Dt14(DATA_IN[14]),
    .Dt13(DATA_IN[13]), .Dt12(DATA_IN[12]), .Dt11(DATA_IN[11]), .Dt10(DATA_IN[10]), .Dt09(DATA_IN[9]),
    .Dt08(DATA_IN[8]), .Dt07(DATA_IN[7]), .Dt06(DATA_IN[6]), .Dt05(DATA_IN[5]), .Dt04(DATA_IN[4]),
    .Dt03(DATA_IN[3]), .Dt02(DATA_IN[2]), .Dt01(DATA_IN[1]), .Dt00(DATA_IN[0]), .S31(registrador_21_s00[31]),
    .S30(registrador_21_s00[30]), .S29(registrador_21_s00[29]), .S28(registrador_21_s00[28]),
    .S27(registrador_21_s00[27]), .S26(registrador_21_s00[26]), .S25(registrador_21_s00[25]),
    .S24(registrador_21_s00[24]), .S23(registrador_21_s00[23]), .S22(registrador_21_s00[22]),
    .S21(registrador_21_s00[21]), .S20(registrador_21_s00[20]), .S19(registrador_21_s00[19]),
    .S18(registrador_21_s00[18]), .S17(registrador_21_s00[17]), .S16(registrador_21_s00[16]),
    .S15(registrador_21_s00[15]), .S14(registrador_21_s00[14]), .S13(registrador_21_s00[13]),
    .S12(registrador_21_s00[12]), .S11(registrador_21_s00[11]), .S10(registrador_21_s00[10]),
    .S09(registrador_21_s00[9]), .S08(registrador_21_s00[8]), .S07(registrador_21_s00[7]),
    .S06(registrador_21_s00[6]), .S05(registrador_21_s00[5]), .S04(registrador_21_s00[4]),
    .S03(registrador_21_s00[3]), .S02(registrador_21_s00[2]), .S01(registrador_21_s00[1]),
    .S00(registrador_21_s00[0]));
  registrador registrador_22 (
    .write(demultiplexer_1_out27), .clear(clear), .Dt31(DATA_IN[31]), .Dt30(DATA_IN[30]), .Dt29(DATA_IN[29]),
    .Dt28(DATA_IN[28]), .Dt27(DATA_IN[27]), .Dt26(DATA_IN[26]), .Dt25(DATA_IN[25]), .Dt24(DATA_IN[24]),
    .Dt23(DATA_IN[23]), .Dt22(DATA_IN[22]), .Dt21(DATA_IN[21]), .Dt20(DATA_IN[20]), .Dt19(DATA_IN[19]),
    .Dt18(DATA_IN[18]), .Dt17(DATA_IN[17]), .Dt16(DATA_IN[16]), .Dt15(DATA_IN[15]), .Dt14(DATA_IN[14]),
    .Dt13(DATA_IN[13]), .Dt12(DATA_IN[12]), .Dt11(DATA_IN[11]), .Dt10(DATA_IN[10]), .Dt09(DATA_IN[9]),
    .Dt08(DATA_IN[8]), .Dt07(DATA_IN[7]), .Dt06(DATA_IN[6]), .Dt05(DATA_IN[5]), .Dt04(DATA_IN[4]),
    .Dt03(DATA_IN[3]), .Dt02(DATA_IN[2]), .Dt01(DATA_IN[1]), .Dt00(DATA_IN[0]), .S31(registrador_22_s00[31]),
    .S30(registrador_22_s00[30]), .S29(registrador_22_s00[29]), .S28(registrador_22_s00[28]),
    .S27(registrador_22_s00[27]), .S26(registrador_22_s00[26]), .S25(registrador_22_s00[25]),
    .S24(registrador_22_s00[24]), .S23(registrador_22_s00[23]), .S22(registrador_22_s00[22]),
    .S21(registrador_22_s00[21]), .S20(registrador_22_s00[20]), .S19(registrador_22_s00[19]),
    .S18(registrador_22_s00[18]), .S17(registrador_22_s00[17]), .S16(registrador_22_s00[16]),
    .S15(registrador_22_s00[15]), .S14(registrador_22_s00[14]), .S13(registrador_22_s00[13]),
    .S12(registrador_22_s00[12]), .S11(registrador_22_s00[11]), .S10(registrador_22_s00[10]),
    .S09(registrador_22_s00[9]), .S08(registrador_22_s00[8]), .S07(registrador_22_s00[7]),
    .S06(registrador_22_s00[6]), .S05(registrador_22_s00[5]), .S04(registrador_22_s00[4]),
    .S03(registrador_22_s00[3]), .S02(registrador_22_s00[2]), .S01(registrador_22_s00[1]),
    .S00(registrador_22_s00[0]));
  registrador registrador_23 (
    .write(demultiplexer_1_out28), .clear(clear), .Dt31(DATA_IN[31]), .Dt30(DATA_IN[30]), .Dt29(DATA_IN[29]),
    .Dt28(DATA_IN[28]), .Dt27(DATA_IN[27]), .Dt26(DATA_IN[26]), .Dt25(DATA_IN[25]), .Dt24(DATA_IN[24]),
    .Dt23(DATA_IN[23]), .Dt22(DATA_IN[22]), .Dt21(DATA_IN[21]), .Dt20(DATA_IN[20]), .Dt19(DATA_IN[19]),
    .Dt18(DATA_IN[18]), .Dt17(DATA_IN[17]), .Dt16(DATA_IN[16]), .Dt15(DATA_IN[15]), .Dt14(DATA_IN[14]),
    .Dt13(DATA_IN[13]), .Dt12(DATA_IN[12]), .Dt11(DATA_IN[11]), .Dt10(DATA_IN[10]), .Dt09(DATA_IN[9]),
    .Dt08(DATA_IN[8]), .Dt07(DATA_IN[7]), .Dt06(DATA_IN[6]), .Dt05(DATA_IN[5]), .Dt04(DATA_IN[4]),
    .Dt03(DATA_IN[3]), .Dt02(DATA_IN[2]), .Dt01(DATA_IN[1]), .Dt00(DATA_IN[0]), .S31(registrador_23_s00[31]),
    .S30(registrador_23_s00[30]), .S29(registrador_23_s00[29]), .S28(registrador_23_s00[28]),
    .S27(registrador_23_s00[27]), .S26(registrador_23_s00[26]), .S25(registrador_23_s00[25]),
    .S24(registrador_23_s00[24]), .S23(registrador_23_s00[23]), .S22(registrador_23_s00[22]),
    .S21(registrador_23_s00[21]), .S20(registrador_23_s00[20]), .S19(registrador_23_s00[19]),
    .S18(registrador_23_s00[18]), .S17(registrador_23_s00[17]), .S16(registrador_23_s00[16]),
    .S15(registrador_23_s00[15]), .S14(registrador_23_s00[14]), .S13(registrador_23_s00[13]),
    .S12(registrador_23_s00[12]), .S11(registrador_23_s00[11]), .S10(registrador_23_s00[10]),
    .S09(registrador_23_s00[9]), .S08(registrador_23_s00[8]), .S07(registrador_23_s00[7]),
    .S06(registrador_23_s00[6]), .S05(registrador_23_s00[5]), .S04(registrador_23_s00[4]),
    .S03(registrador_23_s00[3]), .S02(registrador_23_s00[2]), .S01(registrador_23_s00[1]),
    .S00(registrador_23_s00[0]));
  registrador registrador_24 (
    .write(demultiplexer_1_out29), .clear(clear), .Dt31(DATA_IN[31]), .Dt30(DATA_IN[30]), .Dt29(DATA_IN[29]),
    .Dt28(DATA_IN[28]), .Dt27(DATA_IN[27]), .Dt26(DATA_IN[26]), .Dt25(DATA_IN[25]), .Dt24(DATA_IN[24]),
    .Dt23(DATA_IN[23]), .Dt22(DATA_IN[22]), .Dt21(DATA_IN[21]), .Dt20(DATA_IN[20]), .Dt19(DATA_IN[19]),
    .Dt18(DATA_IN[18]), .Dt17(DATA_IN[17]), .Dt16(DATA_IN[16]), .Dt15(DATA_IN[15]), .Dt14(DATA_IN[14]),
    .Dt13(DATA_IN[13]), .Dt12(DATA_IN[12]), .Dt11(DATA_IN[11]), .Dt10(DATA_IN[10]), .Dt09(DATA_IN[9]),
    .Dt08(DATA_IN[8]), .Dt07(DATA_IN[7]), .Dt06(DATA_IN[6]), .Dt05(DATA_IN[5]), .Dt04(DATA_IN[4]),
    .Dt03(DATA_IN[3]), .Dt02(DATA_IN[2]), .Dt01(DATA_IN[1]), .Dt00(DATA_IN[0]), .S31(registrador_24_s00[31]),
    .S30(registrador_24_s00[30]), .S29(registrador_24_s00[29]), .S28(registrador_24_s00[28]),
    .S27(registrador_24_s00[27]), .S26(registrador_24_s00[26]), .S25(registrador_24_s00[25]),
    .S24(registrador_24_s00[24]), .S23(registrador_24_s00[23]), .S22(registrador_24_s00[22]),
    .S21(registrador_24_s00[21]), .S20(registrador_24_s00[20]), .S19(registrador_24_s00[19]),
    .S18(registrador_24_s00[18]), .S17(registrador_24_s00[17]), .S16(registrador_24_s00[16]),
    .S15(registrador_24_s00[15]), .S14(registrador_24_s00[14]), .S13(registrador_24_s00[13]),
    .S12(registrador_24_s00[12]), .S11(registrador_24_s00[11]), .S10(registrador_24_s00[10]),
    .S09(registrador_24_s00[9]), .S08(registrador_24_s00[8]), .S07(registrador_24_s00[7]),
    .S06(registrador_24_s00[6]), .S05(registrador_24_s00[5]), .S04(registrador_24_s00[4]),
    .S03(registrador_24_s00[3]), .S02(registrador_24_s00[2]), .S01(registrador_24_s00[1]),
    .S00(registrador_24_s00[0]));
  registrador registrador_25 (
    .write(demultiplexer_1_out30), .clear(clear), .Dt31(DATA_IN[31]), .Dt30(DATA_IN[30]), .Dt29(DATA_IN[29]),
    .Dt28(DATA_IN[28]), .Dt27(DATA_IN[27]), .Dt26(DATA_IN[26]), .Dt25(DATA_IN[25]), .Dt24(DATA_IN[24]),
    .Dt23(DATA_IN[23]), .Dt22(DATA_IN[22]), .Dt21(DATA_IN[21]), .Dt20(DATA_IN[20]), .Dt19(DATA_IN[19]),
    .Dt18(DATA_IN[18]), .Dt17(DATA_IN[17]), .Dt16(DATA_IN[16]), .Dt15(DATA_IN[15]), .Dt14(DATA_IN[14]),
    .Dt13(DATA_IN[13]), .Dt12(DATA_IN[12]), .Dt11(DATA_IN[11]), .Dt10(DATA_IN[10]), .Dt09(DATA_IN[9]),
    .Dt08(DATA_IN[8]), .Dt07(DATA_IN[7]), .Dt06(DATA_IN[6]), .Dt05(DATA_IN[5]), .Dt04(DATA_IN[4]),
    .Dt03(DATA_IN[3]), .Dt02(DATA_IN[2]), .Dt01(DATA_IN[1]), .Dt00(DATA_IN[0]), .S31(registrador_25_s00[31]),
    .S30(registrador_25_s00[30]), .S29(registrador_25_s00[29]), .S28(registrador_25_s00[28]),
    .S27(registrador_25_s00[27]), .S26(registrador_25_s00[26]), .S25(registrador_25_s00[25]),
    .S24(registrador_25_s00[24]), .S23(registrador_25_s00[23]), .S22(registrador_25_s00[22]),
    .S21(registrador_25_s00[21]), .S20(registrador_25_s00[20]), .S19(registrador_25_s00[19]),
    .S18(registrador_25_s00[18]), .S17(registrador_25_s00[17]), .S16(registrador_25_s00[16]),
    .S15(registrador_25_s00[15]), .S14(registrador_25_s00[14]), .S13(registrador_25_s00[13]),
    .S12(registrador_25_s00[12]), .S11(registrador_25_s00[11]), .S10(registrador_25_s00[10]),
    .S09(registrador_25_s00[9]), .S08(registrador_25_s00[8]), .S07(registrador_25_s00[7]),
    .S06(registrador_25_s00[6]), .S05(registrador_25_s00[5]), .S04(registrador_25_s00[4]),
    .S03(registrador_25_s00[3]), .S02(registrador_25_s00[2]), .S01(registrador_25_s00[1]),
    .S00(registrador_25_s00[0]));
  registrador registrador_26 (
    .write(demultiplexer_1_out31), .clear(clear), .Dt31(DATA_IN[31]), .Dt30(DATA_IN[30]), .Dt29(DATA_IN[29]),
    .Dt28(DATA_IN[28]), .Dt27(DATA_IN[27]), .Dt26(DATA_IN[26]), .Dt25(DATA_IN[25]), .Dt24(DATA_IN[24]),
    .Dt23(DATA_IN[23]), .Dt22(DATA_IN[22]), .Dt21(DATA_IN[21]), .Dt20(DATA_IN[20]), .Dt19(DATA_IN[19]),
    .Dt18(DATA_IN[18]), .Dt17(DATA_IN[17]), .Dt16(DATA_IN[16]), .Dt15(DATA_IN[15]), .Dt14(DATA_IN[14]),
    .Dt13(DATA_IN[13]), .Dt12(DATA_IN[12]), .Dt11(DATA_IN[11]), .Dt10(DATA_IN[10]), .Dt09(DATA_IN[9]),
    .Dt08(DATA_IN[8]), .Dt07(DATA_IN[7]), .Dt06(DATA_IN[6]), .Dt05(DATA_IN[5]), .Dt04(DATA_IN[4]),
    .Dt03(DATA_IN[3]), .Dt02(DATA_IN[2]), .Dt01(DATA_IN[1]), .Dt00(DATA_IN[0]), .S31(registrador_26_s00[31]),
    .S30(registrador_26_s00[30]), .S29(registrador_26_s00[29]), .S28(registrador_26_s00[28]),
    .S27(registrador_26_s00[27]), .S26(registrador_26_s00[26]), .S25(registrador_26_s00[25]),
    .S24(registrador_26_s00[24]), .S23(registrador_26_s00[23]), .S22(registrador_26_s00[22]),
    .S21(registrador_26_s00[21]), .S20(registrador_26_s00[20]), .S19(registrador_26_s00[19]),
    .S18(registrador_26_s00[18]), .S17(registrador_26_s00[17]), .S16(registrador_26_s00[16]),
    .S15(registrador_26_s00[15]), .S14(registrador_26_s00[14]), .S13(registrador_26_s00[13]),
    .S12(registrador_26_s00[12]), .S11(registrador_26_s00[11]), .S10(registrador_26_s00[10]),
    .S09(registrador_26_s00[9]), .S08(registrador_26_s00[8]), .S07(registrador_26_s00[7]),
    .S06(registrador_26_s00[6]), .S05(registrador_26_s00[5]), .S04(registrador_26_s00[4]),
    .S03(registrador_26_s00[3]), .S02(registrador_26_s00[2]), .S01(registrador_26_s00[1]),
    .S00(registrador_26_s00[0]));
  Multiplexer #(.select(5), .width(32), .enable("false")) multiplexer_1 (
    .in0(_00000_s00), .in1(_00001_s00), .in2(_00010_s00), .in3(_00011_s00), .in4(_00100_s00),
    .in5(_00101_s00), .in6(registrador_1_s00), .in7(registrador_2_s00), .in8(registrador_3_s00),
    .in9(registrador_4_s00), .in10(registrador_5_s00), .in11(registrador_6_s00), .in12(registrador_7_s00),
    .in13(registrador_8_s00), .in14(registrador_9_s00), .in15(registrador_10_s00), .in16(registrador_11_s00),
    .in17(registrador_12_s00), .in18(registrador_13_s00), .in19(registrador_14_s00),
    .in20(registrador_15_s00), .in21(registrador_16_s00), .in22(registrador_17_s00),
    .in23(registrador_18_s00), .in24(registrador_19_s00), .in25(registrador_20_s00),
    .in26(registrador_21_s00), .in27(registrador_22_s00), .in28(registrador_23_s00),
    .in29(registrador_24_s00), .in30(registrador_25_s00), .in31(registrador_26_s00), .out(DATAreg_A),
    .sel(registrador_A));
  Multiplexer #(.select(5), .width(32), .enable("false")) multiplexer_2 (
    .in0(_00000_s00), .in1(_00001_s00), .in2(_00010_s00), .in3(_00011_s00), .in4(_00100_s00),
    .in5(_00101_s00), .in6(registrador_1_s00), .in7(registrador_2_s00), .in8(registrador_3_s00),
    .in9(registrador_4_s00), .in10(registrador_5_s00), .in11(registrador_6_s00), .in12(registrador_7_s00),
    .in13(registrador_8_s00), .in14(registrador_9_s00), .in15(registrador_10_s00), .in16(registrador_11_s00),
    .in17(registrador_12_s00), .in18(registrador_13_s00), .in19(registrador_14_s00),
    .in20(registrador_15_s00), .in21(registrador_16_s00), .in22(registrador_17_s00),
    .in23(registrador_18_s00), .in24(registrador_19_s00), .in25(registrador_20_s00),
    .in26(registrador_21_s00), .in27(registrador_22_s00), .in28(registrador_23_s00),
    .in29(registrador_24_s00), .in30(registrador_25_s00), .in31(registrador_26_s00), .out(DATAreg_B),
    .sel(registrador_B));
endmodule

module PC_MEM (
  input  [9:0] estado_do_salto,
  input  saltar,
  input  RESET,
  input  PC_CLK,
  output [31:0] MEMout
);

  wire [9:0] adder_1_out, multiplexer_1_out, register_1_q;

  Multiplexer #(.width(10), .enable("false")) multiplexer_1 (
    .in0(10'h1), .in1(estado_do_salto), .out(multiplexer_1_out), .sel(saltar));
  Adder #(.width(10)) adder_1 (.a(multiplexer_1_out), .b(register_1_q), .out(adder_1_out));  // open: cin, cout
  Register #(.width(10)) register_1 (.D(adder_1_out), .Q(register_1_q), .clk(PC_CLK), .clr(RESET));  // open: en
  RAM #(.addrWidth(10), .dataWidth(32)) ram_1 (.addr(register_1_q), .data(MEMout));  // open: sel, clk, ld, clr
endmodule

module comparador (
  input  [31:0] in_1,
  input  [31:0] in_2,
  output out_3
);

  wire xnor_1_out, xnor_2_out, xnor_3_out, xnor_4_out, xnor_5_out, xnor_6_out, xnor_7_out, xnor_8_out,
       xnor_9_out, xnor_10_out, xnor_11_out, xnor_12_out, xnor_13_out, xnor_14_out, xnor_15_out, xnor_16_out,
       xnor_17_out, xnor_18_out, xnor_19_out, xnor_20_out, xnor_21_out, xnor_22_out, xnor_23_out,
       xnor_24_out, xnor_25_out, xnor_26_out, xnor_27_out, xnor_28_out, xnor_29_out, xnor_30_out,
       xnor_31_out, xnor_32_out;

  xnor xnor_1 (xnor_1_out, in_1[0], in_2[0]);
  xnor xnor_2 (xnor_2_out, in_1[1], in_2[1]);
  xnor xnor_3 (xnor_3_out, in_1[2], in_2[2]);
  xnor xnor_4 (xnor_4_out, in_1[3], in_2[3]);
  xnor xnor_5 (xnor_5_out, in_1[4], in_2[4]);
  xnor xnor_6 (xnor_6_out, in_1[5], in_2[5]);
  xnor xnor_7 (xnor_7_out, in_1[6], in_2[6]);
  xnor xnor_8 (xnor_8_out, in_1[7], in_2[7]);
  xnor xnor_9 (xnor_9_out, in_1[8], in_2[8]);
  xnor xnor_10 (xnor_10_out, in_1[9], in_2[9]);
  xnor xnor_11 (xnor_11_out, in_1[10], in_2[10]);
  xnor xnor_12 (xnor_12_out, in_1[11], in_2[11]);
  xnor xnor_13 (xnor_13_out, in_1[12], in_2[12]);
  xnor xnor_14 (xnor_14_out, in_1[13], in_2[13]);
  xnor xnor_15 (xnor_15_out, in_1[14], in_2[14]);
  xnor xnor_16 (xnor_16_out, in_1[15], in_2[15]);
  xnor xnor_17 (xnor_17_out, in_1[16], in_2[16]);
  xnor xnor_18 (xnor_18_out, in_1[17], in_2[17]);
  xnor xnor_19 (xnor_19_out, in_1[18], in_2[18]);
  xnor xnor_20 (xnor_20_out, in_1[19], in_2[19]);
  xnor xnor_21 (xnor_21_out, in_1[20], in_2[20]);
  xnor xnor_22 (xnor_22_out, in_1[21], in_2[21]);
  xnor xnor_23 (xnor_23_out, in_1[22], in_2[22]);
  xnor xnor_24 (xnor_24_out, in_1[23], in_2[23]);
  xnor xnor_25 (xnor_25_out, in_1[24], in_2[24]);
  xnor xnor_26 (xnor_26_out, in_1[25], in_2[25]);
  xnor xnor_27 (xnor_27_out, in_1[26], in_2[26]);
  xnor xnor_28 (xnor_28_out, in_1[27], in_2[27]);
  xnor xnor_29 (xnor_29_out, in_1[28], in_2[28]);
  xnor xnor_30 (xnor_30_out, in_1[29], in_2[29]);
  xnor xnor_31 (xnor_31_out, in_1[30], in_2[30]);
  xnor xnor_32 (xnor_32_out, in_1[31], in_2[31]);
  and and_1 (out_3, xnor_1_out, xnor_2_out, xnor_3_out, xnor_4_out, xnor_5_out, xnor_6_out, xnor_7_out, xnor_8_out, xnor_9_out, xnor_10_out, xnor_11_out, xnor_12_out, xnor_13_out, xnor_14_out, xnor_15_out, xnor_16_out, xnor_17_out, xnor_18_out, xnor_19_out, xnor_20_out, xnor_21_out, xnor_22_out, xnor_23_out, xnor_24_out, xnor_25_out, xnor_26_out, xnor_27_out, xnor_28_out, xnor_29_out, xnor_30_out, xnor_31_out, xnor_32_out);
endmodule

module teste_memmoria (
  input  in_1,
  input  in_2,
  input  in_3,
  input  [7:0] in_4
);

  wire clock_1_out;
  wire [3:0] adder_1_out, multiplexer_1_out, multiplexer_1_out_2, register_1_q;

  _7_Segment_Display u_7_segment_display_1 (
    .g(multiplexer_1_out[3]), .f(multiplexer_1_out[2]), .a(multiplexer_1_out[1]), .b(multiplexer_1_out[0]),
    .e(multiplexer_1_out_2[3]), .d(multiplexer_1_out_2[2]), .c(multiplexer_1_out_2[1]),
    .dp(multiplexer_1_out_2[0]));
  Adder #(.width(4)) adder_1 (.a(4'b0001), .b(register_1_q), .out(adder_1_out));  // open: cin, cout
  Register #(.width(4)) register_1 (.D(adder_1_out), .Q(register_1_q), .clk(in_1), .clr(in_2));  // open: en
  Clock clock_1 (.out(clock_1_out));
  Multiplexer #(.width(8), .enable("false")) multiplexer_1 (
    .in0(in_4), .in1({multiplexer_1_out, multiplexer_1_out_2}),
    .out({multiplexer_1_out, multiplexer_1_out_2}), .sel(in_3));
  RAM #(.addrWidth(4)) ram_1 (
    .addr(register_1_q), .data({multiplexer_1_out, multiplexer_1_out_2}), .clk(clock_1_out), .ld(in_3));  // open: sel, clr
endmodule

module barrel_shift_right (
  input  [31:0] in_1,
  input  b2_desloca_16,
  input  b2_desloca_8,
  input  b2_desloca_4,
  input  b1_desloca_2,
  input  b0_desloca_1,
  output [31:0] out_7
);

  wire multiplexer_1_out, multiplexer_2_out, multiplexer_3_out, multiplexer_4_out, multiplexer_5_out,
       multiplexer_7_out, multiplexer_8_out, multiplexer_9_out, multiplexer_10_out, multiplexer_11_out,
       multiplexer_12_out, multiplexer_13_out, multiplexer_16_out, multiplexer_17_out, multiplexer_18_out,
       multiplexer_19_out, multiplexer_20_out, multiplexer_21_out, multiplexer_23_out, multiplexer_24_out,
       multiplexer_25_out, multiplexer_26_out, multiplexer_27_out, multiplexer_28_out, multiplexer_31_out,
       multiplexer_32_out, multiplexer_33_out, multiplexer_34_out, multiplexer_35_out, multiplexer_36_out,
       multiplexer_37_out, multiplexer_38_out, multiplexer_40_out, multiplexer_41_out, multiplexer_42_out,
       multiplexer_43_out, multiplexer_44_out, multiplexer_47_out, multiplexer_48_out, multiplexer_49_out,
       multiplexer_50_out, multiplexer_51_out, multiplexer_52_out, multiplexer_53_out, multiplexer_56_out,
       multiplexer_57_out, multiplexer_58_out, multiplexer_59_out, multiplexer_60_out, multiplexer_61_out,
       multiplexer_63_out, multiplexer_64_out, multiplexer_65_out, multiplexer_66_out, multiplexer_67_out,
       multiplexer_68_out, multiplexer_71_out, multiplexer_72_out, multiplexer_73_out, multiplexer_74_out,
       multiplexer_75_out, multiplexer_76_out, multiplexer_77_out, multiplexer_78_out, multiplexer_80_out,
       multiplexer_81_out, multiplexer_82_out, multiplexer_83_out, multiplexer_84_out, multiplexer_87_out,
       multiplexer_88_out, multiplexer_89_out, multiplexer_90_out, multiplexer_91_out, multiplexer_92_out,
       multiplexer_93_out, multiplexer_96_out, multiplexer_97_out, multiplexer_98_out, multiplexer_99_out,
       multiplexer_100_out, multiplexer_101_out, multiplexer_103_out, multiplexer_104_out,
       multiplexer_105_out, multiplexer_106_out, multiplexer_107_out, multiplexer_108_out,
       multiplexer_111_out, multiplexer_112_out, multiplexer_113_out, multiplexer_114_out,
       multiplexer_115_out, multiplexer_116_out, multiplexer_117_out, multiplexer_118_out,
       multiplexer_120_out, multiplexer_121_out, multiplexer_122_out, multiplexer_123_out,
       multiplexer_124_out, multiplexer_127_out, multiplexer_128_out, multiplexer_129_out,
       multiplexer_130_out, multiplexer_131_out, multiplexer_132_out, multiplexer_133_out,
       multiplexer_136_out, multiplexer_137_out, multiplexer_138_out, multiplexer_139_out,
       multiplexer_140_out, multiplexer_141_out, multiplexer_143_out, multiplexer_144_out,
       multiplexer_145_out, multiplexer_146_out, multiplexer_147_out, multiplexer_148_out,
       multiplexer_151_out, multiplexer_152_out, multiplexer_153_out, multiplexer_154_out,
       multiplexer_155_out, multiplexer_156_out, multiplexer_157_out, multiplexer_158_out;

  Multiplexer #(.enable("false")) multiplexer_1 (
    .in0(in_1[31]), .in1(1'b0), .out(multiplexer_1_out), .sel(b2_desloca_16));
  Multiplexer #(.enable("false")) multiplexer_2 (
    .in0(in_1[30]), .in1(1'b0), .out(multiplexer_2_out), .sel(b2_desloca_16));
  Multiplexer #(.enable("false")) multiplexer_3 (
    .in0(multiplexer_1_out), .in1(1'b0), .out(multiplexer_3_out), .sel(b2_desloca_8));
  Multiplexer #(.enable("false")) multiplexer_4 (
    .in0(multiplexer_3_out), .in1(1'b0), .out(multiplexer_4_out), .sel(b2_desloca_4));
  Multiplexer #(.enable("false")) multiplexer_5 (
    .in0(multiplexer_4_out), .in1(1'b0), .out(multiplexer_5_out), .sel(b1_desloca_2));
  Multiplexer #(.enable("false")) multiplexer_6 (
    .in0(multiplexer_5_out), .in1(1'b0), .out(out_7[31]), .sel(b0_desloca_1));
  Multiplexer #(.enable("false")) multiplexer_7 (
    .in0(in_1[29]), .in1(1'b0), .out(multiplexer_7_out), .sel(b2_desloca_16));
  Multiplexer #(.enable("false")) multiplexer_8 (
    .in0(multiplexer_7_out), .in1(1'b0), .out(multiplexer_8_out), .sel(b2_desloca_8));
  Multiplexer #(.enable("false")) multiplexer_9 (
    .in0(multiplexer_2_out), .in1(1'b0), .out(multiplexer_9_out), .sel(b2_desloca_8));
  Multiplexer #(.enable("false")) multiplexer_10 (
    .in0(multiplexer_9_out), .in1(1'b0), .out(multiplexer_10_out), .sel(b2_desloca_4));
  Multiplexer #(.enable("false")) multiplexer_11 (
    .in0(multiplexer_8_out), .in1(1'b0), .out(multiplexer_11_out), .sel(b2_desloca_4));
  Multiplexer #(.enable("false")) multiplexer_12 (
    .in0(multiplexer_11_out), .in1(multiplexer_4_out), .out(multiplexer_12_out), .sel(b1_desloca_2));
  Multiplexer #(.enable("false")) multiplexer_13 (
    .in0(multiplexer_10_out), .in1(1'b0), .out(multiplexer_13_out), .sel(b1_desloca_2));
  Multiplexer #(.enable("false")) multiplexer_14 (
    .in0(multiplexer_13_out), .in1(multiplexer_5_out), .out(out_7[30]), .sel(b0_desloca_1));
  Multiplexer #(.enable("false")) multiplexer_15 (
    .in0(multiplexer_12_out), .in1(multiplexer_13_out), .out(out_7[29]), .sel(b0_desloca_1));
  Multiplexer #(.enable("false")) multiplexer_16 (
    .in0(in_1[28]), .in1(1'b0), .out(multiplexer_16_out), .sel(b2_desloca_16));
  Multiplexer #(.enable("false")) multiplexer_17 (
    .in0(in_1[27]), .in1(1'b0), .out(multiplexer_17_out), .sel(b2_desloca_16));
  Multiplexer #(.enable("false")) multiplexer_18 (
    .in0(multiplexer_16_out), .in1(1'b0), .out(multiplexer_18_out), .sel(b2_desloca_8));
  Multiplexer #(.enable("false")) multiplexer_19 (
    .in0(multiplexer_17_out), .in1(1'b0), .out(multiplexer_19_out), .sel(b2_desloca_8));
  Multiplexer #(.enable("false")) multiplexer_20 (
    .in0(multiplexer_18_out), .in1(1'b0), .out(multiplexer_20_out), .sel(b2_desloca_4));
  Multiplexer #(.enable("false")) multiplexer_21 (
    .in0(multiplexer_20_out), .in1(multiplexer_10_out), .out(multiplexer_21_out), .sel(b1_desloca_2));
  Multiplexer #(.enable("false")) multiplexer_22 (
    .in0(multiplexer_21_out), .in1(multiplexer_12_out), .out(out_7[28]), .sel(b0_desloca_1));
  Multiplexer #(.enable("false")) multiplexer_23 (
    .in0(in_1[26]), .in1(1'b0), .out(multiplexer_23_out), .sel(b2_desloca_16));
  Multiplexer #(.enable("false")) multiplexer_24 (
    .in0(multiplexer_23_out), .in1(1'b0), .out(multiplexer_24_out), .sel(b2_desloca_8));
  Multiplexer #(.enable("false")) multiplexer_25 (
    .in0(multiplexer_24_out), .in1(multiplexer_9_out), .out(multiplexer_25_out), .sel(b2_desloca_4));
  Multiplexer #(.enable("false")) multiplexer_26 (
    .in0(multiplexer_19_out), .in1(multiplexer_3_out), .out(multiplexer_26_out), .sel(b2_desloca_4));
  Multiplexer #(.enable("false")) multiplexer_27 (
    .in0(multiplexer_26_out), .in1(multiplexer_11_out), .out(multiplexer_27_out), .sel(b1_desloca_2));
  Multiplexer #(.enable("false")) multiplexer_28 (
    .in0(multiplexer_25_out), .in1(multiplexer_20_out), .out(multiplexer_28_out), .sel(b1_desloca_2));
  Multiplexer #(.enable("false")) multiplexer_29 (
    .in0(multiplexer_28_out), .in1(multiplexer_27_out), .out(out_7[26]), .sel(b0_desloca_1));
  Multiplexer #(.enable("false")) multiplexer_30 (
    .in0(multiplexer_27_out), .in1(multiplexer_21_out), .out(out_7[27]), .sel(b0_desloca_1));
  Multiplexer #(.enable("false")) multiplexer_31 (
    .in0(in_1[25]), .in1(1'b0), .out(multiplexer_31_out), .sel(b2_desloca_16));
  Multiplexer #(.enable("false")) multiplexer_32 (
    .in0(in_1[24]), .in1(1'b0), .out(multiplexer_32_out), .sel(b2_desloca_16));
  Multiplexer #(.enable("false")) multiplexer_33 (
    .in0(multiplexer_31_out), .in1(1'b0), .out(multiplexer_33_out), .sel(b2_desloca_8));
  Multiplexer #(.enable("false")) multiplexer_34 (
    .in0(multiplexer_32_out), .in1(1'b0), .out(multiplexer_34_out), .sel(b2_desloca_8));
  Multiplexer #(.enable("false")) multiplexer_35 (
    .in0(multiplexer_34_out), .in1(multiplexer_18_out), .out(multiplexer_35_out), .sel(b2_desloca_4));
  Multiplexer #(.enable("false")) multiplexer_36 (
    .in0(multiplexer_33_out), .in1(multiplexer_8_out), .out(multiplexer_36_out), .sel(b2_desloca_4));
  Multiplexer #(.enable("false")) multiplexer_37 (
    .in0(multiplexer_35_out), .in1(multiplexer_25_out), .out(multiplexer_37_out), .sel(b1_desloca_2));
  Multiplexer #(.enable("false")) multiplexer_38 (
    .in0(multiplexer_36_out), .in1(multiplexer_26_out), .out(multiplexer_38_out), .sel(b1_desloca_2));
  Multiplexer #(.enable("false")) multiplexer_39 (
    .in0(multiplexer_38_out), .in1(multiplexer_28_out), .out(out_7[25]), .sel(b0_desloca_1));
  Multiplexer #(.enable("false")) multiplexer_40 (
    .in0(in_1[22]), .in1(1'b0), .out(multiplexer_40_out), .sel(b2_desloca_16));
  Multiplexer #(.enable("false")) multiplexer_41 (
    .in0(in_1[23]), .in1(1'b0), .out(multiplexer_41_out), .sel(b2_desloca_16));
  Multiplexer #(.enable("false")) multiplexer_42 (
    .in0(multiplexer_41_out), .in1(multiplexer_1_out), .out(multiplexer_42_out), .sel(b2_desloca_8));
  Multiplexer #(.enable("false")) multiplexer_43 (
    .in0(multiplexer_42_out), .in1(multiplexer_19_out), .out(multiplexer_43_out), .sel(b2_desloca_4));
  Multiplexer #(.enable("false")) multiplexer_44 (
    .in0(multiplexer_43_out), .in1(multiplexer_36_out), .out(multiplexer_44_out), .sel(b1_desloca_2));
  Multiplexer #(.enable("false")) multiplexer_45 (
    .in0(multiplexer_44_out), .in1(multiplexer_37_out), .out(out_7[23]), .sel(b0_desloca_1));
  Multiplexer #(.enable("false")) multiplexer_46 (
    .in0(multiplexer_37_out), .in1(multiplexer_38_out), .out(out_7[24]), .sel(b0_desloca_1));
  Multiplexer #(.enable("false")) multiplexer_47 (
    .in0(in_1[21]), .in1(1'b0), .out(multiplexer_47_out), .sel(b2_desloca_16));
  Multiplexer #(.enable("false")) multiplexer_48 (
    .in0(multiplexer_40_out), .in1(multiplexer_2_out), .out(multiplexer_48_out), .sel(b2_desloca_8));
  Multiplexer #(.enable("false")) multiplexer_49 (
    .in0(multiplexer_47_out), .in1(multiplexer_7_out), .out(multiplexer_49_out), .sel(b2_desloca_8));
  Multiplexer #(.enable("false")) multiplexer_50 (
    .in0(multiplexer_48_out), .in1(multiplexer_24_out), .out(multiplexer_50_out), .sel(b2_desloca_4));
  Multiplexer #(.enable("false")) multiplexer_51 (
    .in0(multiplexer_49_out), .in1(multiplexer_33_out), .out(multiplexer_51_out), .sel(b2_desloca_4));
  Multiplexer #(.enable("false")) multiplexer_52 (
    .in0(multiplexer_51_out), .in1(multiplexer_43_out), .out(multiplexer_52_out), .sel(b1_desloca_2));
  Multiplexer #(.enable("false")) multiplexer_53 (
    .in0(multiplexer_50_out), .in1(multiplexer_35_out), .out(multiplexer_53_out), .sel(b1_desloca_2));
  Multiplexer #(.enable("false")) multiplexer_54 (
    .in0(multiplexer_52_out), .in1(multiplexer_53_out), .out(out_7[21]), .sel(b0_desloca_1));
  Multiplexer #(.enable("false")) multiplexer_55 (
    .in0(multiplexer_53_out), .in1(multiplexer_44_out), .out(out_7[22]), .sel(b0_desloca_1));
  Multiplexer #(.enable("false")) multiplexer_56 (
    .in0(in_1[20]), .in1(1'b0), .out(multiplexer_56_out), .sel(b2_desloca_16));
  Multiplexer #(.enable("false")) multiplexer_57 (
    .in0(in_1[19]), .in1(1'b0), .out(multiplexer_57_out), .sel(b2_desloca_16));
  Multiplexer #(.enable("false")) multiplexer_58 (
    .in0(multiplexer_56_out), .in1(multiplexer_16_out), .out(multiplexer_58_out), .sel(b2_desloca_8));
  Multiplexer #(.enable("false")) multiplexer_59 (
    .in0(multiplexer_57_out), .in1(multiplexer_17_out), .out(multiplexer_59_out), .sel(b2_desloca_8));
  Multiplexer #(.enable("false")) multiplexer_60 (
    .in0(multiplexer_58_out), .in1(multiplexer_34_out), .out(multiplexer_60_out), .sel(b2_desloca_4));
  Multiplexer #(.enable("false")) multiplexer_61 (
    .in0(multiplexer_60_out), .in1(multiplexer_50_out), .out(multiplexer_61_out), .sel(b1_desloca_2));
  Multiplexer #(.enable("false")) multiplexer_62 (
    .in0(multiplexer_61_out), .in1(multiplexer_52_out), .out(out_7[20]), .sel(b0_desloca_1));
  Multiplexer #(.enable("false")) multiplexer_63 (
    .in0(in_1[18]), .in1(1'b0), .out(multiplexer_63_out), .sel(b2_desloca_16));
  Multiplexer #(.enable("false")) multiplexer_64 (
    .in0(multiplexer_63_out), .in1(multiplexer_23_out), .out(multiplexer_64_out), .sel(b2_desloca_8));
  Multiplexer #(.enable("false")) multiplexer_65 (
    .in0(multiplexer_59_out), .in1(multiplexer_42_out), .out(multiplexer_65_out), .sel(b2_desloca_4));
  Multiplexer #(.enable("false")) multiplexer_66 (
    .in0(multiplexer_64_out), .in1(multiplexer_48_out), .out(multiplexer_66_out), .sel(b2_desloca_4));
  Multiplexer #(.enable("false")) multiplexer_67 (
    .in0(multiplexer_66_out), .in1(multiplexer_60_out), .out(multiplexer_67_out), .sel(b1_desloca_2));
  Multiplexer #(.enable("false")) multiplexer_68 (
    .in0(multiplexer_65_out), .in1(multiplexer_51_out), .out(multiplexer_68_out), .sel(b1_desloca_2));
  Multiplexer #(.enable("false")) multiplexer_69 (
    .in0(multiplexer_68_out), .in1(multiplexer_61_out), .out(out_7[19]), .sel(b0_desloca_1));
  Multiplexer #(.enable("false")) multiplexer_70 (
    .in0(multiplexer_67_out), .in1(multiplexer_68_out), .out(out_7[18]), .sel(b0_desloca_1));
  Multiplexer #(.enable("false")) multiplexer_71 (
    .in0(in_1[16]), .in1(1'b0), .out(multiplexer_71_out), .sel(b2_desloca_16));
  Multiplexer #(.enable("false")) multiplexer_72 (
    .in0(in_1[17]), .in1(1'b0), .out(multiplexer_72_out), .sel(b2_desloca_16));
  Multiplexer #(.enable("false")) multiplexer_73 (
    .in0(multiplexer_71_out), .in1(multiplexer_32_out), .out(multiplexer_73_out), .sel(b2_desloca_8));
  Multiplexer #(.enable("false")) multiplexer_74 (
    .in0(multiplexer_72_out), .in1(multiplexer_31_out), .out(multiplexer_74_out), .sel(b2_desloca_8));
  Multiplexer #(.enable("false")) multiplexer_75 (
    .in0(multiplexer_73_out), .in1(multiplexer_58_out), .out(multiplexer_75_out), .sel(b2_desloca_4));
  Multiplexer #(.enable("false")) multiplexer_76 (
    .in0(multiplexer_74_out), .in1(multiplexer_49_out), .out(multiplexer_76_out), .sel(b2_desloca_4));
  Multiplexer #(.enable("false")) multiplexer_77 (
    .in0(multiplexer_75_out), .in1(multiplexer_66_out), .out(multiplexer_77_out), .sel(b1_desloca_2));
  Multiplexer #(.enable("false")) multiplexer_78 (
    .in0(multiplexer_76_out), .in1(multiplexer_65_out), .out(multiplexer_78_out), .sel(b1_desloca_2));
  Multiplexer #(.enable("false")) multiplexer_79 (
    .in0(multiplexer_78_out), .in1(multiplexer_67_out), .out(out_7[17]), .sel(b0_desloca_1));
  Multiplexer #(.enable("false")) multiplexer_80 (
    .in0(in_1[15]), .in1(in_1[31]), .out(multiplexer_80_out), .sel(b2_desloca_16));
  Multiplexer #(.enable("false")) multiplexer_81 (
    .in0(in_1[14]), .in1(in_1[30]), .out(multiplexer_81_out), .sel(b2_desloca_16));
  Multiplexer #(.enable("false")) multiplexer_82 (
    .in0(multiplexer_80_out), .in1(multiplexer_41_out), .out(multiplexer_82_out), .sel(b2_desloca_8));
  Multiplexer #(.enable("false")) multiplexer_83 (
    .in0(multiplexer_82_out), .in1(multiplexer_59_out), .out(multiplexer_83_out), .sel(b2_desloca_4));
  Multiplexer #(.enable("false")) multiplexer_84 (
    .in0(multiplexer_83_out), .in1(multiplexer_76_out), .out(multiplexer_84_out), .sel(b1_desloca_2));
  Multiplexer #(.enable("false")) multiplexer_85 (
    .in0(multiplexer_84_out), .in1(multiplexer_77_out), .out(out_7[15]), .sel(b0_desloca_1));
  Multiplexer #(.enable("false")) multiplexer_86 (
    .in0(multiplexer_77_out), .in1(multiplexer_78_out), .out(out_7[16]), .sel(b0_desloca_1));
  Multiplexer #(.enable("false")) multiplexer_87 (
    .in0(in_1[13]), .in1(in_1[29]), .out(multiplexer_87_out), .sel(b2_desloca_16));
  Multiplexer #(.enable("false")) multiplexer_88 (
    .in0(multiplexer_81_out), .in1(multiplexer_40_out), .out(multiplexer_88_out), .sel(b2_desloca_8));
  Multiplexer #(.enable("false")) multiplexer_89 (
    .in0(multiplexer_87_out), .in1(multiplexer_47_out), .out(multiplexer_89_out), .sel(b2_desloca_8));
  Multiplexer #(.enable("false")) multiplexer_90 (
    .in0(multiplexer_89_out), .in1(multiplexer_74_out), .out(multiplexer_90_out), .sel(b2_desloca_4));
  Multiplexer #(.enable("false")) multiplexer_91 (
    .in0(multiplexer_88_out), .in1(multiplexer_64_out), .out(multiplexer_91_out), .sel(b2_desloca_4));
  Multiplexer #(.enable("false")) multiplexer_92 (
    .in0(multiplexer_91_out), .in1(multiplexer_75_out), .out(multiplexer_92_out), .sel(b1_desloca_2));
  Multiplexer #(.enable("false")) multiplexer_93 (
    .in0(multiplexer_90_out), .in1(multiplexer_83_out), .out(multiplexer_93_out), .sel(b1_desloca_2));
  Multiplexer #(.enable("false")) multiplexer_94 (
    .in0(multiplexer_92_out), .in1(multiplexer_84_out), .out(out_7[14]), .sel(b0_desloca_1));
  Multiplexer #(.enable("false")) multiplexer_95 (
    .in0(multiplexer_93_out), .in1(multiplexer_92_out), .out(out_7[13]), .sel(b0_desloca_1));
  Multiplexer #(.enable("false")) multiplexer_96 (
    .in0(in_1[11]), .in1(in_1[27]), .out(multiplexer_96_out), .sel(b2_desloca_16));
  Multiplexer #(.enable("false")) multiplexer_97 (
    .in0(in_1[12]), .in1(in_1[28]), .out(multiplexer_97_out), .sel(b2_desloca_16));
  Multiplexer #(.enable("false")) multiplexer_98 (
    .in0(multiplexer_96_out), .in1(multiplexer_57_out), .out(multiplexer_98_out), .sel(b2_desloca_8));
  Multiplexer #(.enable("false")) multiplexer_99 (
    .in0(multiplexer_97_out), .in1(multiplexer_56_out), .out(multiplexer_99_out), .sel(b2_desloca_8));
  Multiplexer #(.enable("false")) multiplexer_100 (
    .in0(multiplexer_99_out), .in1(multiplexer_73_out), .out(multiplexer_100_out), .sel(b2_desloca_4));
  Multiplexer #(.enable("false")) multiplexer_101 (
    .in0(multiplexer_100_out), .in1(multiplexer_91_out), .out(multiplexer_101_out), .sel(b1_desloca_2));
  Multiplexer #(.enable("false")) multiplexer_102 (
    .in0(multiplexer_101_out), .in1(multiplexer_93_out), .out(out_7[12]), .sel(b0_desloca_1));
  Multiplexer #(.enable("false")) multiplexer_103 (
    .in0(in_1[10]), .in1(in_1[26]), .out(multiplexer_103_out), .sel(b2_desloca_16));
  Multiplexer #(.enable("false")) multiplexer_104 (
    .in0(multiplexer_103_out), .in1(multiplexer_63_out), .out(multiplexer_104_out), .sel(b2_desloca_8));
  Multiplexer #(.enable("false")) multiplexer_105 (
    .in0(multiplexer_104_out), .in1(multiplexer_88_out), .out(multiplexer_105_out), .sel(b2_desloca_4));
  Multiplexer #(.enable("false")) multiplexer_106 (
    .in0(multiplexer_98_out), .in1(multiplexer_82_out), .out(multiplexer_106_out), .sel(b2_desloca_4));
  Multiplexer #(.enable("false")) multiplexer_107 (
    .in0(multiplexer_105_out), .in1(multiplexer_100_out), .out(multiplexer_107_out), .sel(b1_desloca_2));
  Multiplexer #(.enable("false")) multiplexer_108 (
    .in0(multiplexer_106_out), .in1(multiplexer_90_out), .out(multiplexer_108_out), .sel(b1_desloca_2));
  Multiplexer #(.enable("false")) multiplexer_109 (
    .in0(multiplexer_107_out), .in1(multiplexer_108_out), .out(out_7[10]), .sel(b0_desloca_1));
  Multiplexer #(.enable("false")) multiplexer_110 (
    .in0(multiplexer_108_out), .in1(multiplexer_101_out), .out(out_7[11]), .sel(b0_desloca_1));
  Multiplexer #(.enable("false")) multiplexer_111 (
    .in0(in_1[9]), .in1(in_1[25]), .out(multiplexer_111_out), .sel(b2_desloca_16));
  Multiplexer #(.enable("false")) multiplexer_112 (
    .in0(in_1[8]), .in1(in_1[24]), .out(multiplexer_112_out), .sel(b2_desloca_16));
  Multiplexer #(.enable("false")) multiplexer_113 (
    .in0(multiplexer_112_out), .in1(multiplexer_71_out), .out(multiplexer_113_out), .sel(b2_desloca_8));
  Multiplexer #(.enable("false")) multiplexer_114 (
    .in0(multiplexer_111_out), .in1(multiplexer_72_out), .out(multiplexer_114_out), .sel(b2_desloca_8));
  Multiplexer #(.enable("false")) multiplexer_115 (
    .in0(multiplexer_113_out), .in1(multiplexer_99_out), .out(multiplexer_115_out), .sel(b2_desloca_4));
  Multiplexer #(.enable("false")) multiplexer_116 (
    .in0(multiplexer_114_out), .in1(multiplexer_89_out), .out(multiplexer_116_out), .sel(b2_desloca_4));
  Multiplexer #(.enable("false")) multiplexer_117 (
    .in0(multiplexer_115_out), .in1(multiplexer_105_out), .out(multiplexer_117_out), .sel(b1_desloca_2));
  Multiplexer #(.enable("false")) multiplexer_118 (
    .in0(multiplexer_116_out), .in1(multiplexer_106_out), .out(multiplexer_118_out), .sel(b1_desloca_2));
  Multiplexer #(.enable("false")) multiplexer_119 (
    .in0(multiplexer_118_out), .in1(multiplexer_107_out), .out(out_7[9]), .sel(b0_desloca_1));
  Multiplexer #(.enable("false")) multiplexer_120 (
    .in0(in_1[6]), .in1(in_1[22]), .out(multiplexer_120_out), .sel(b2_desloca_16));
  Multiplexer #(.enable("false")) multiplexer_121 (
    .in0(in_1[7]), .in1(in_1[23]), .out(multiplexer_121_out), .sel(b2_desloca_16));
  Multiplexer #(.enable("false")) multiplexer_122 (
    .in0(multiplexer_121_out), .in1(multiplexer_80_out), .out(multiplexer_122_out), .sel(b2_desloca_8));
  Multiplexer #(.enable("false")) multiplexer_123 (
    .in0(multiplexer_122_out), .in1(multiplexer_98_out), .out(multiplexer_123_out), .sel(b2_desloca_4));
  Multiplexer #(.enable("false")) multiplexer_124 (
    .in0(multiplexer_123_out), .in1(multiplexer_116_out), .out(multiplexer_124_out), .sel(b1_desloca_2));
  Multiplexer #(.enable("false")) multiplexer_125 (
    .in0(multiplexer_117_out), .in1(multiplexer_118_out), .out(out_7[8]), .sel(b0_desloca_1));
  Multiplexer #(.enable("false")) multiplexer_126 (
    .in0(multiplexer_124_out), .in1(multiplexer_117_out), .out(out_7[7]), .sel(b0_desloca_1));
  Multiplexer #(.enable("false")) multiplexer_127 (
    .in0(in_1[5]), .in1(in_1[21]), .out(multiplexer_127_out), .sel(b2_desloca_16));
  Multiplexer #(.enable("false")) multiplexer_128 (
    .in0(multiplexer_120_out), .in1(multiplexer_81_out), .out(multiplexer_128_out), .sel(b2_desloca_8));
  Multiplexer #(.enable("false")) multiplexer_129 (
    .in0(multiplexer_127_out), .in1(multiplexer_87_out), .out(multiplexer_129_out), .sel(b2_desloca_8));
  Multiplexer #(.enable("false")) multiplexer_130 (
    .in0(multiplexer_129_out), .in1(multiplexer_114_out), .out(multiplexer_130_out), .sel(b2_desloca_4));
  Multiplexer #(.enable("false")) multiplexer_131 (
    .in0(multiplexer_128_out), .in1(multiplexer_104_out), .out(multiplexer_131_out), .sel(b2_desloca_4));
  Multiplexer #(.enable("false")) multiplexer_132 (
    .in0(multiplexer_130_out), .in1(multiplexer_123_out), .out(multiplexer_132_out), .sel(b1_desloca_2));
  Multiplexer #(.enable("false")) multiplexer_133 (
    .in0(multiplexer_131_out), .in1(multiplexer_115_out), .out(multiplexer_133_out), .sel(b1_desloca_2));
  Multiplexer #(.enable("false")) multiplexer_134 (
    .in0(multiplexer_133_out), .in1(multiplexer_124_out), .out(out_7[6]), .sel(b0_desloca_1));
  Multiplexer #(.enable("false")) multiplexer_135 (
    .in0(multiplexer_132_out), .in1(multiplexer_133_out), .out(out_7[5]), .sel(b0_desloca_1));
  Multiplexer #(.enable("false")) multiplexer_136 (
    .in0(in_1[3]), .in1(in_1[19]), .out(multiplexer_136_out), .sel(b2_desloca_16));
  Multiplexer #(.enable("false")) multiplexer_137 (
    .in0(in_1[4]), .in1(in_1[20]), .out(multiplexer_137_out), .sel(b2_desloca_16));
  Multiplexer #(.enable("false")) multiplexer_138 (
    .in0(multiplexer_136_out), .in1(multiplexer_96_out), .out(multiplexer_138_out), .sel(b2_desloca_8));
  Multiplexer #(.enable("false")) multiplexer_139 (
    .in0(multiplexer_137_out), .in1(multiplexer_97_out), .out(multiplexer_139_out), .sel(b2_desloca_8));
  Multiplexer #(.enable("false")) multiplexer_140 (
    .in0(multiplexer_139_out), .in1(multiplexer_113_out), .out(multiplexer_140_out), .sel(b2_desloca_4));
  Multiplexer #(.enable("false")) multiplexer_141 (
    .in0(multiplexer_140_out), .in1(multiplexer_131_out), .out(multiplexer_141_out), .sel(b1_desloca_2));
  Multiplexer #(.enable("false")) multiplexer_142 (
    .in0(multiplexer_141_out), .in1(multiplexer_132_out), .out(out_7[4]), .sel(b0_desloca_1));
  Multiplexer #(.enable("false")) multiplexer_143 (
    .in0(in_1[2]), .in1(in_1[18]), .out(multiplexer_143_out), .sel(b2_desloca_16));
  Multiplexer #(.enable("false")) multiplexer_144 (
    .in0(multiplexer_143_out), .in1(multiplexer_103_out), .out(multiplexer_144_out), .sel(b2_desloca_8));
  Multiplexer #(.enable("false")) multiplexer_145 (
    .in0(multiplexer_144_out), .in1(multiplexer_128_out), .out(multiplexer_145_out), .sel(b2_desloca_4));
  Multiplexer #(.enable("false")) multiplexer_146 (
    .in0(multiplexer_138_out), .in1(multiplexer_122_out), .out(multiplexer_146_out), .sel(b2_desloca_4));
  Multiplexer #(.enable("false")) multiplexer_147 (
    .in0(multiplexer_145_out), .in1(multiplexer_140_out), .out(multiplexer_147_out), .sel(b1_desloca_2));
  Multiplexer #(.enable("false")) multiplexer_148 (
    .in0(multiplexer_146_out), .in1(multiplexer_130_out), .out(multiplexer_148_out), .sel(b1_desloca_2));
  Multiplexer #(.enable("false")) multiplexer_149 (
    .in0(multiplexer_147_out), .in1(multiplexer_148_out), .out(out_7[2]), .sel(b0_desloca_1));
  Multiplexer #(.enable("false")) multiplexer_150 (
    .in0(multiplexer_148_out), .in1(multiplexer_141_out), .out(out_7[3]), .sel(b0_desloca_1));
  Multiplexer #(.enable("false")) multiplexer_151 (
    .in0(in_1[0]), .in1(in_1[16]), .out(multiplexer_151_out), .sel(b2_desloca_16));
  Multiplexer #(.enable("false")) multiplexer_152 (
    .in0(in_1[1]), .in1(in_1[17]), .out(multiplexer_152_out), .sel(b2_desloca_16));
  Multiplexer #(.enable("false")) multiplexer_153 (
    .in0(multiplexer_152_out), .in1(multiplexer_111_out), .out(multiplexer_153_out), .sel(b2_desloca_8));
  Multiplexer #(.enable("false")) multiplexer_154 (
    .in0(multiplexer_151_out), .in1(multiplexer_112_out), .out(multiplexer_154_out), .sel(b2_desloca_8));
  Multiplexer #(.enable("false")) multiplexer_155 (
    .in0(multiplexer_154_out), .in1(multiplexer_139_out), .out(multiplexer_155_out), .sel(b2_desloca_4));
  Multiplexer #(.enable("false")) multiplexer_156 (
    .in0(multiplexer_153_out), .in1(multiplexer_129_out), .out(multiplexer_156_out), .sel(b2_desloca_4));
  Multiplexer #(.enable("false")) multiplexer_157 (
    .in0(multiplexer_155_out), .in1(multiplexer_145_out), .out(multiplexer_157_out), .sel(b1_desloca_2));
  Multiplexer #(.enable("false")) multiplexer_158 (
    .in0(multiplexer_156_out), .in1(multiplexer_146_out), .out(multiplexer_158_out), .sel(b1_desloca_2));
  Multiplexer #(.enable("false")) multiplexer_159 (
    .in0(multiplexer_158_out), .in1(multiplexer_147_out), .out(out_7[1]), .sel(b0_desloca_1));
  Multiplexer #(.enable("false")) multiplexer_160 (
    .in0(multiplexer_157_out), .in1(multiplexer_158_out), .out(out_7[0]), .sel(b0_desloca_1));
endmodule
// b-s-left
module barrel_shift_left (
  input  [31:0] in_1,
  input  b2_desloca_16,
  input  b2_desloca_8,
  input  b2_desloca_4,
  input  b1_desloca_2,
  input  b0_desloca_1,
  output [31:0] out_7
);

  wire multiplexer_1_out, multiplexer_2_out, multiplexer_3_out, multiplexer_4_out, multiplexer_5_out,
       multiplexer_6_out, multiplexer_8_out, multiplexer_9_out, multiplexer_10_out, multiplexer_11_out,
       multiplexer_12_out, multiplexer_13_out, multiplexer_16_out, multiplexer_17_out, multiplexer_18_out,
       multiplexer_19_out, multiplexer_20_out, multiplexer_21_out, multiplexer_22_out, multiplexer_24_out,
       multiplexer_25_out, multiplexer_26_out, multiplexer_27_out, multiplexer_28_out, multiplexer_29_out,
       multiplexer_32_out, multiplexer_33_out, multiplexer_34_out, multiplexer_35_out, multiplexer_36_out,
       multiplexer_37_out, multiplexer_38_out, multiplexer_40_out, multiplexer_41_out, multiplexer_42_out,
       multiplexer_43_out, multiplexer_44_out, multiplexer_45_out, multiplexer_48_out, multiplexer_49_out,
       multiplexer_50_out, multiplexer_51_out, multiplexer_52_out, multiplexer_53_out, multiplexer_56_out,
       multiplexer_57_out, multiplexer_58_out, multiplexer_59_out, multiplexer_60_out, multiplexer_61_out,
       multiplexer_62_out, multiplexer_64_out, multiplexer_65_out, multiplexer_66_out, multiplexer_67_out,
       multiplexer_68_out, multiplexer_69_out, multiplexer_72_out, multiplexer_73_out, multiplexer_74_out,
       multiplexer_75_out, multiplexer_76_out, multiplexer_77_out, multiplexer_78_out, multiplexer_80_out,
       multiplexer_81_out, multiplexer_82_out, multiplexer_83_out, multiplexer_84_out, multiplexer_85_out,
       multiplexer_88_out, multiplexer_89_out, multiplexer_90_out, multiplexer_91_out, multiplexer_92_out,
       multiplexer_93_out, multiplexer_96_out, multiplexer_97_out, multiplexer_98_out, multiplexer_99_out,
       multiplexer_100_out, multiplexer_101_out, multiplexer_102_out, multiplexer_104_out,
       multiplexer_105_out, multiplexer_106_out, multiplexer_107_out, multiplexer_108_out,
       multiplexer_109_out, multiplexer_112_out, multiplexer_113_out, multiplexer_114_out,
       multiplexer_115_out, multiplexer_116_out, multiplexer_117_out, multiplexer_118_out,
       multiplexer_120_out, multiplexer_121_out, multiplexer_122_out, multiplexer_123_out,
       multiplexer_124_out, multiplexer_125_out, multiplexer_128_out, multiplexer_129_out,
       multiplexer_130_out, multiplexer_131_out, multiplexer_132_out, multiplexer_133_out,
       multiplexer_136_out, multiplexer_137_out, multiplexer_138_out, multiplexer_139_out,
       multiplexer_140_out, multiplexer_141_out, multiplexer_142_out, multiplexer_144_out,
       multiplexer_145_out, multiplexer_146_out, multiplexer_147_out, multiplexer_148_out,
       multiplexer_149_out, multiplexer_152_out, multiplexer_153_out, multiplexer_154_out,
       multiplexer_155_out, multiplexer_156_out, multiplexer_157_out, multiplexer_158_out;

  Multiplexer #(.enable("false")) multiplexer_1 (
    .in0(in_1[31]), .in1(in_1[15]), .out(multiplexer_1_out), .sel(b2_desloca_16));
  Multiplexer #(.enable("false")) multiplexer_2 (
    .in0(in_1[30]), .in1(in_1[14]), .out(multiplexer_2_out), .sel(b2_desloca_16));
  Multiplexer #(.enable("false")) multiplexer_3 (
    .in0(multiplexer_1_out), .in1(multiplexer_40_out), .out(multiplexer_3_out), .sel(b2_desloca_8));
  Multiplexer #(.enable("false")) multiplexer_4 (
    .in0(multiplexer_2_out), .in1(multiplexer_41_out), .out(multiplexer_4_out), .sel(b2_desloca_8));
  Multiplexer #(.enable("false")) multiplexer_5 (
    .in0(multiplexer_3_out), .in1(multiplexer_18_out), .out(multiplexer_5_out), .sel(b2_desloca_4));
  Multiplexer #(.enable("false")) multiplexer_6 (
    .in0(multiplexer_5_out), .in1(multiplexer_10_out), .out(multiplexer_6_out), .sel(b1_desloca_2));
  Multiplexer #(.enable("false")) multiplexer_7 (
    .in0(multiplexer_6_out), .in1(multiplexer_13_out), .out(out_7[31]), .sel(b0_desloca_1));
  Multiplexer #(.enable("false")) multiplexer_8 (
    .in0(in_1[29]), .in1(in_1[13]), .out(multiplexer_8_out), .sel(b2_desloca_16));
  Multiplexer #(.enable("false")) multiplexer_9 (
    .in0(multiplexer_8_out), .in1(multiplexer_48_out), .out(multiplexer_9_out), .sel(b2_desloca_8));
  Multiplexer #(.enable("false")) multiplexer_10 (
    .in0(multiplexer_9_out), .in1(multiplexer_34_out), .out(multiplexer_10_out), .sel(b2_desloca_4));
  Multiplexer #(.enable("false")) multiplexer_11 (
    .in0(multiplexer_4_out), .in1(multiplexer_26_out), .out(multiplexer_11_out), .sel(b2_desloca_4));
  Multiplexer #(.enable("false")) multiplexer_12 (
    .in0(multiplexer_10_out), .in1(multiplexer_21_out), .out(multiplexer_12_out), .sel(b1_desloca_2));
  Multiplexer #(.enable("false")) multiplexer_13 (
    .in0(multiplexer_11_out), .in1(multiplexer_20_out), .out(multiplexer_13_out), .sel(b1_desloca_2));
  Multiplexer #(.enable("false")) multiplexer_14 (
    .in0(multiplexer_13_out), .in1(multiplexer_12_out), .out(out_7[30]), .sel(b0_desloca_1));
  Multiplexer #(.enable("false")) multiplexer_15 (
    .in0(multiplexer_12_out), .in1(multiplexer_22_out), .out(out_7[29]), .sel(b0_desloca_1));
  Multiplexer #(.enable("false")) multiplexer_16 (
    .in0(in_1[27]), .in1(in_1[11]), .out(multiplexer_16_out), .sel(b2_desloca_16));
  Multiplexer #(.enable("false")) multiplexer_17 (
    .in0(in_1[28]), .in1(in_1[12]), .out(multiplexer_17_out), .sel(b2_desloca_16));
  Multiplexer #(.enable("false")) multiplexer_18 (
    .in0(multiplexer_16_out), .in1(multiplexer_56_out), .out(multiplexer_18_out), .sel(b2_desloca_8));
  Multiplexer #(.enable("false")) multiplexer_19 (
    .in0(multiplexer_17_out), .in1(multiplexer_57_out), .out(multiplexer_19_out), .sel(b2_desloca_8));
  Multiplexer #(.enable("false")) multiplexer_20 (
    .in0(multiplexer_19_out), .in1(multiplexer_33_out), .out(multiplexer_20_out), .sel(b2_desloca_4));
  Multiplexer #(.enable("false")) multiplexer_21 (
    .in0(multiplexer_18_out), .in1(multiplexer_42_out), .out(multiplexer_21_out), .sel(b2_desloca_4));
  Multiplexer #(.enable("false")) multiplexer_22 (
    .in0(multiplexer_20_out), .in1(multiplexer_27_out), .out(multiplexer_22_out), .sel(b1_desloca_2));
  Multiplexer #(.enable("false")) multiplexer_23 (
    .in0(multiplexer_22_out), .in1(multiplexer_29_out), .out(out_7[28]), .sel(b0_desloca_1));
  Multiplexer #(.enable("false")) multiplexer_24 (
    .in0(in_1[25]), .in1(in_1[9]), .out(multiplexer_24_out), .sel(b2_desloca_16));
  Multiplexer #(.enable("false")) multiplexer_25 (
    .in0(in_1[26]), .in1(in_1[10]), .out(multiplexer_25_out), .sel(b2_desloca_16));
  Multiplexer #(.enable("false")) multiplexer_26 (
    .in0(multiplexer_25_out), .in1(multiplexer_65_out), .out(multiplexer_26_out), .sel(b2_desloca_8));
  Multiplexer #(.enable("false")) multiplexer_27 (
    .in0(multiplexer_26_out), .in1(multiplexer_43_out), .out(multiplexer_27_out), .sel(b2_desloca_4));
  Multiplexer #(.enable("false")) multiplexer_28 (
    .in0(multiplexer_27_out), .in1(multiplexer_35_out), .out(multiplexer_28_out), .sel(b1_desloca_2));
  Multiplexer #(.enable("false")) multiplexer_29 (
    .in0(multiplexer_21_out), .in1(multiplexer_36_out), .out(multiplexer_29_out), .sel(b1_desloca_2));
  Multiplexer #(.enable("false")) multiplexer_30 (
    .in0(multiplexer_29_out), .in1(multiplexer_28_out), .out(out_7[27]), .sel(b0_desloca_1));
  Multiplexer #(.enable("false")) multiplexer_31 (
    .in0(multiplexer_28_out), .in1(multiplexer_38_out), .out(out_7[26]), .sel(b0_desloca_1));
  Multiplexer #(.enable("false")) multiplexer_32 (
    .in0(in_1[24]), .in1(in_1[8]), .out(multiplexer_32_out), .sel(b2_desloca_16));
  Multiplexer #(.enable("false")) multiplexer_33 (
    .in0(multiplexer_32_out), .in1(multiplexer_72_out), .out(multiplexer_33_out), .sel(b2_desloca_8));
  Multiplexer #(.enable("false")) multiplexer_34 (
    .in0(multiplexer_24_out), .in1(multiplexer_64_out), .out(multiplexer_34_out), .sel(b2_desloca_8));
  Multiplexer #(.enable("false")) multiplexer_35 (
    .in0(multiplexer_33_out), .in1(multiplexer_58_out), .out(multiplexer_35_out), .sel(b2_desloca_4));
  Multiplexer #(.enable("false")) multiplexer_36 (
    .in0(multiplexer_34_out), .in1(multiplexer_49_out), .out(multiplexer_36_out), .sel(b2_desloca_4));
  Multiplexer #(.enable("false")) multiplexer_37 (
    .in0(multiplexer_35_out), .in1(multiplexer_50_out), .out(multiplexer_37_out), .sel(b1_desloca_2));
  Multiplexer #(.enable("false")) multiplexer_38 (
    .in0(multiplexer_36_out), .in1(multiplexer_44_out), .out(multiplexer_38_out), .sel(b1_desloca_2));
  Multiplexer #(.enable("false")) multiplexer_39 (
    .in0(multiplexer_38_out), .in1(multiplexer_37_out), .out(out_7[25]), .sel(b0_desloca_1));
  Multiplexer #(.enable("false")) multiplexer_40 (
    .in0(in_1[23]), .in1(in_1[7]), .out(multiplexer_40_out), .sel(b2_desloca_16));
  Multiplexer #(.enable("false")) multiplexer_41 (
    .in0(in_1[22]), .in1(in_1[6]), .out(multiplexer_41_out), .sel(b2_desloca_16));
  Multiplexer #(.enable("false")) multiplexer_42 (
    .in0(multiplexer_40_out), .in1(multiplexer_81_out), .out(multiplexer_42_out), .sel(b2_desloca_8));
  Multiplexer #(.enable("false")) multiplexer_43 (
    .in0(multiplexer_41_out), .in1(multiplexer_80_out), .out(multiplexer_43_out), .sel(b2_desloca_8));
  Multiplexer #(.enable("false")) multiplexer_44 (
    .in0(multiplexer_42_out), .in1(multiplexer_59_out), .out(multiplexer_44_out), .sel(b2_desloca_4));
  Multiplexer #(.enable("false")) multiplexer_45 (
    .in0(multiplexer_44_out), .in1(multiplexer_51_out), .out(multiplexer_45_out), .sel(b1_desloca_2));
  Multiplexer #(.enable("false")) multiplexer_46 (
    .in0(multiplexer_37_out), .in1(multiplexer_45_out), .out(out_7[24]), .sel(b0_desloca_1));
  Multiplexer #(.enable("false")) multiplexer_47 (
    .in0(multiplexer_45_out), .in1(multiplexer_53_out), .out(out_7[23]), .sel(b0_desloca_1));
  Multiplexer #(.enable("false")) multiplexer_48 (
    .in0(in_1[21]), .in1(in_1[5]), .out(multiplexer_48_out), .sel(b2_desloca_16));
  Multiplexer #(.enable("false")) multiplexer_49 (
    .in0(multiplexer_48_out), .in1(multiplexer_88_out), .out(multiplexer_49_out), .sel(b2_desloca_8));
  Multiplexer #(.enable("false")) multiplexer_50 (
    .in0(multiplexer_43_out), .in1(multiplexer_66_out), .out(multiplexer_50_out), .sel(b2_desloca_4));
  Multiplexer #(.enable("false")) multiplexer_51 (
    .in0(multiplexer_49_out), .in1(multiplexer_73_out), .out(multiplexer_51_out), .sel(b2_desloca_4));
  Multiplexer #(.enable("false")) multiplexer_52 (
    .in0(multiplexer_51_out), .in1(multiplexer_60_out), .out(multiplexer_52_out), .sel(b1_desloca_2));
  Multiplexer #(.enable("false")) multiplexer_53 (
    .in0(multiplexer_50_out), .in1(multiplexer_61_out), .out(multiplexer_53_out), .sel(b1_desloca_2));
  Multiplexer #(.enable("false")) multiplexer_54 (
    .in0(multiplexer_53_out), .in1(multiplexer_52_out), .out(out_7[22]), .sel(b0_desloca_1));
  Multiplexer #(.enable("false")) multiplexer_55 (
    .in0(multiplexer_52_out), .in1(multiplexer_62_out), .out(out_7[21]), .sel(b0_desloca_1));
  Multiplexer #(.enable("false")) multiplexer_56 (
    .in0(in_1[19]), .in1(in_1[3]), .out(multiplexer_56_out), .sel(b2_desloca_16));
  Multiplexer #(.enable("false")) multiplexer_57 (
    .in0(in_1[20]), .in1(in_1[4]), .out(multiplexer_57_out), .sel(b2_desloca_16));
  Multiplexer #(.enable("false")) multiplexer_58 (
    .in0(multiplexer_57_out), .in1(multiplexer_96_out), .out(multiplexer_58_out), .sel(b2_desloca_8));
  Multiplexer #(.enable("false")) multiplexer_59 (
    .in0(multiplexer_56_out), .in1(multiplexer_97_out), .out(multiplexer_59_out), .sel(b2_desloca_8));
  Multiplexer #(.enable("false")) multiplexer_60 (
    .in0(multiplexer_59_out), .in1(multiplexer_83_out), .out(multiplexer_60_out), .sel(b2_desloca_4));
  Multiplexer #(.enable("false")) multiplexer_61 (
    .in0(multiplexer_58_out), .in1(multiplexer_74_out), .out(multiplexer_61_out), .sel(b2_desloca_4));
  Multiplexer #(.enable("false")) multiplexer_62 (
    .in0(multiplexer_61_out), .in1(multiplexer_67_out), .out(multiplexer_62_out), .sel(b1_desloca_2));
  Multiplexer #(.enable("false")) multiplexer_63 (
    .in0(multiplexer_62_out), .in1(multiplexer_69_out), .out(out_7[20]), .sel(b0_desloca_1));
  Multiplexer #(.enable("false")) multiplexer_64 (
    .in0(in_1[17]), .in1(in_1[1]), .out(multiplexer_64_out), .sel(b2_desloca_16));
  Multiplexer #(.enable("false")) multiplexer_65 (
    .in0(in_1[18]), .in1(in_1[2]), .out(multiplexer_65_out), .sel(b2_desloca_16));
  Multiplexer #(.enable("false")) multiplexer_66 (
    .in0(multiplexer_65_out), .in1(multiplexer_105_out), .out(multiplexer_66_out), .sel(b2_desloca_8));
  Multiplexer #(.enable("false")) multiplexer_67 (
    .in0(multiplexer_66_out), .in1(multiplexer_82_out), .out(multiplexer_67_out), .sel(b2_desloca_4));
  Multiplexer #(.enable("false")) multiplexer_68 (
    .in0(multiplexer_67_out), .in1(multiplexer_76_out), .out(multiplexer_68_out), .sel(b1_desloca_2));
  Multiplexer #(.enable("false")) multiplexer_69 (
    .in0(multiplexer_60_out), .in1(multiplexer_75_out), .out(multiplexer_69_out), .sel(b1_desloca_2));
  Multiplexer #(.enable("false")) multiplexer_70 (
    .in0(multiplexer_68_out), .in1(multiplexer_77_out), .out(out_7[18]), .sel(b0_desloca_1));
  Multiplexer #(.enable("false")) multiplexer_71 (
    .in0(multiplexer_69_out), .in1(multiplexer_68_out), .out(out_7[19]), .sel(b0_desloca_1));
  Multiplexer #(.enable("false")) multiplexer_72 (
    .in0(in_1[16]), .in1(in_1[0]), .out(multiplexer_72_out), .sel(b2_desloca_16));
  Multiplexer #(.enable("false")) multiplexer_73 (
    .in0(multiplexer_64_out), .in1(multiplexer_104_out), .out(multiplexer_73_out), .sel(b2_desloca_8));
  Multiplexer #(.enable("false")) multiplexer_74 (
    .in0(multiplexer_72_out), .in1(multiplexer_112_out), .out(multiplexer_74_out), .sel(b2_desloca_8));
  Multiplexer #(.enable("false")) multiplexer_75 (
    .in0(multiplexer_73_out), .in1(multiplexer_89_out), .out(multiplexer_75_out), .sel(b2_desloca_4));
  Multiplexer #(.enable("false")) multiplexer_76 (
    .in0(multiplexer_74_out), .in1(multiplexer_98_out), .out(multiplexer_76_out), .sel(b2_desloca_4));
  Multiplexer #(.enable("false")) multiplexer_77 (
    .in0(multiplexer_75_out), .in1(multiplexer_84_out), .out(multiplexer_77_out), .sel(b1_desloca_2));
  Multiplexer #(.enable("false")) multiplexer_78 (
    .in0(multiplexer_76_out), .in1(multiplexer_90_out), .out(multiplexer_78_out), .sel(b1_desloca_2));
  Multiplexer #(.enable("false")) multiplexer_79 (
    .in0(multiplexer_77_out), .in1(multiplexer_78_out), .out(out_7[17]), .sel(b0_desloca_1));
  Multiplexer #(.enable("false")) multiplexer_80 (
    .in0(in_1[14]), .in1(1'b0), .out(multiplexer_80_out), .sel(b2_desloca_16));
  Multiplexer #(.enable("false")) multiplexer_81 (
    .in0(in_1[15]), .in1(1'b0), .out(multiplexer_81_out), .sel(b2_desloca_16));
  Multiplexer #(.enable("false")) multiplexer_82 (
    .in0(multiplexer_80_out), .in1(multiplexer_120_out), .out(multiplexer_82_out), .sel(b2_desloca_8));
  Multiplexer #(.enable("false")) multiplexer_83 (
    .in0(multiplexer_81_out), .in1(multiplexer_121_out), .out(multiplexer_83_out), .sel(b2_desloca_8));
  Multiplexer #(.enable("false")) multiplexer_84 (
    .in0(multiplexer_83_out), .in1(multiplexer_99_out), .out(multiplexer_84_out), .sel(b2_desloca_4));
  Multiplexer #(.enable("false")) multiplexer_85 (
    .in0(multiplexer_84_out), .in1(multiplexer_91_out), .out(multiplexer_85_out), .sel(b1_desloca_2));
  Multiplexer #(.enable("false")) multiplexer_86 (
    .in0(multiplexer_78_out), .in1(multiplexer_85_out), .out(out_7[16]), .sel(b0_desloca_1));
  Multiplexer #(.enable("false")) multiplexer_87 (
    .in0(multiplexer_85_out), .in1(multiplexer_92_out), .out(out_7[15]), .sel(b0_desloca_1));
  Multiplexer #(.enable("false")) multiplexer_88 (
    .in0(in_1[13]), .in1(1'b0), .out(multiplexer_88_out), .sel(b2_desloca_16));
  Multiplexer #(.enable("false")) multiplexer_89 (
    .in0(multiplexer_88_out), .in1(multiplexer_128_out), .out(multiplexer_89_out), .sel(b2_desloca_8));
  Multiplexer #(.enable("false")) multiplexer_90 (
    .in0(multiplexer_82_out), .in1(multiplexer_106_out), .out(multiplexer_90_out), .sel(b2_desloca_4));
  Multiplexer #(.enable("false")) multiplexer_91 (
    .in0(multiplexer_89_out), .in1(multiplexer_114_out), .out(multiplexer_91_out), .sel(b2_desloca_4));
  Multiplexer #(.enable("false")) multiplexer_92 (
    .in0(multiplexer_90_out), .in1(multiplexer_101_out), .out(multiplexer_92_out), .sel(b1_desloca_2));
  Multiplexer #(.enable("false")) multiplexer_93 (
    .in0(multiplexer_91_out), .in1(multiplexer_100_out), .out(multiplexer_93_out), .sel(b1_desloca_2));
  Multiplexer #(.enable("false")) multiplexer_94 (
    .in0(multiplexer_92_out), .in1(multiplexer_93_out), .out(out_7[14]), .sel(b0_desloca_1));
  Multiplexer #(.enable("false")) multiplexer_95 (
    .in0(multiplexer_93_out), .in1(multiplexer_102_out), .out(out_7[13]), .sel(b0_desloca_1));
  Multiplexer #(.enable("false")) multiplexer_96 (
    .in0(in_1[12]), .in1(1'b0), .out(multiplexer_96_out), .sel(b2_desloca_16));
  Multiplexer #(.enable("false")) multiplexer_97 (
    .in0(in_1[11]), .in1(1'b0), .out(multiplexer_97_out), .sel(b2_desloca_16));
  Multiplexer #(.enable("false")) multiplexer_98 (
    .in0(multiplexer_96_out), .in1(multiplexer_137_out), .out(multiplexer_98_out), .sel(b2_desloca_8));
  Multiplexer #(.enable("false")) multiplexer_99 (
    .in0(multiplexer_97_out), .in1(multiplexer_136_out), .out(multiplexer_99_out), .sel(b2_desloca_8));
  Multiplexer #(.enable("false")) multiplexer_100 (
    .in0(multiplexer_99_out), .in1(multiplexer_123_out), .out(multiplexer_100_out), .sel(b2_desloca_4));
  Multiplexer #(.enable("false")) multiplexer_101 (
    .in0(multiplexer_98_out), .in1(multiplexer_113_out), .out(multiplexer_101_out), .sel(b2_desloca_4));
  Multiplexer #(.enable("false")) multiplexer_102 (
    .in0(multiplexer_101_out), .in1(multiplexer_107_out), .out(multiplexer_102_out), .sel(b1_desloca_2));
  Multiplexer #(.enable("false")) multiplexer_103 (
    .in0(multiplexer_102_out), .in1(multiplexer_108_out), .out(out_7[12]), .sel(b0_desloca_1));
  Multiplexer #(.enable("false")) multiplexer_104 (
    .in0(in_1[9]), .in1(1'b0), .out(multiplexer_104_out), .sel(b2_desloca_16));
  Multiplexer #(.enable("false")) multiplexer_105 (
    .in0(in_1[10]), .in1(1'b0), .out(multiplexer_105_out), .sel(b2_desloca_16));
  Multiplexer #(.enable("false")) multiplexer_106 (
    .in0(multiplexer_105_out), .in1(multiplexer_144_out), .out(multiplexer_106_out), .sel(b2_desloca_8));
  Multiplexer #(.enable("false")) multiplexer_107 (
    .in0(multiplexer_106_out), .in1(multiplexer_122_out), .out(multiplexer_107_out), .sel(b2_desloca_4));
  Multiplexer #(.enable("false")) multiplexer_108 (
    .in0(multiplexer_100_out), .in1(multiplexer_115_out), .out(multiplexer_108_out), .sel(b1_desloca_2));
  Multiplexer #(.enable("false")) multiplexer_109 (
    .in0(multiplexer_107_out), .in1(multiplexer_116_out), .out(multiplexer_109_out), .sel(b1_desloca_2));
  Multiplexer #(.enable("false")) multiplexer_110 (
    .in0(multiplexer_108_out), .in1(multiplexer_109_out), .out(out_7[11]), .sel(b0_desloca_1));
  Multiplexer #(.enable("false")) multiplexer_111 (
    .in0(multiplexer_109_out), .in1(multiplexer_118_out), .out(out_7[10]), .sel(b0_desloca_1));
  Multiplexer #(.enable("false")) multiplexer_112 (
    .in0(in_1[8]), .in1(1'b0), .out(multiplexer_112_out), .sel(b2_desloca_16));
  Multiplexer #(.enable("false")) multiplexer_113 (
    .in0(multiplexer_112_out), .in1(multiplexer_152_out), .out(multiplexer_113_out), .sel(b2_desloca_8));
  Multiplexer #(.enable("false")) multiplexer_114 (
    .in0(multiplexer_104_out), .in1(multiplexer_145_out), .out(multiplexer_114_out), .sel(b2_desloca_8));
  Multiplexer #(.enable("false")) multiplexer_115 (
    .in0(multiplexer_114_out), .in1(multiplexer_129_out), .out(multiplexer_115_out), .sel(b2_desloca_4));
  Multiplexer #(.enable("false")) multiplexer_116 (
    .in0(multiplexer_113_out), .in1(multiplexer_138_out), .out(multiplexer_116_out), .sel(b2_desloca_4));
  Multiplexer #(.enable("false")) multiplexer_117 (
    .in0(multiplexer_116_out), .in1(multiplexer_130_out), .out(multiplexer_117_out), .sel(b1_desloca_2));
  Multiplexer #(.enable("false")) multiplexer_118 (
    .in0(multiplexer_115_out), .in1(multiplexer_124_out), .out(multiplexer_118_out), .sel(b1_desloca_2));
  Multiplexer #(.enable("false")) multiplexer_119 (
    .in0(multiplexer_118_out), .in1(multiplexer_117_out), .out(out_7[9]), .sel(b0_desloca_1));
  Multiplexer #(.enable("false")) multiplexer_120 (
    .in0(in_1[6]), .in1(1'b0), .out(multiplexer_120_out), .sel(b2_desloca_16));
  Multiplexer #(.enable("false")) multiplexer_121 (
    .in0(in_1[7]), .in1(1'b0), .out(multiplexer_121_out), .sel(b2_desloca_16));
  Multiplexer #(.enable("false")) multiplexer_122 (
    .in0(multiplexer_120_out), .in1(1'b0), .out(multiplexer_122_out), .sel(b2_desloca_8));
  Multiplexer #(.enable("false")) multiplexer_123 (
    .in0(multiplexer_121_out), .in1(1'b0), .out(multiplexer_123_out), .sel(b2_desloca_8));
  Multiplexer #(.enable("false")) multiplexer_124 (
    .in0(multiplexer_123_out), .in1(multiplexer_139_out), .out(multiplexer_124_out), .sel(b2_desloca_4));
  Multiplexer #(.enable("false")) multiplexer_125 (
    .in0(multiplexer_124_out), .in1(multiplexer_131_out), .out(multiplexer_125_out), .sel(b1_desloca_2));
  Multiplexer #(.enable("false")) multiplexer_126 (
    .in0(multiplexer_117_out), .in1(multiplexer_125_out), .out(out_7[8]), .sel(b0_desloca_1));
  Multiplexer #(.enable("false")) multiplexer_127 (
    .in0(multiplexer_125_out), .in1(multiplexer_132_out), .out(out_7[7]), .sel(b0_desloca_1));
  Multiplexer #(.enable("false")) multiplexer_128 (
    .in0(in_1[5]), .in1(1'b0), .out(multiplexer_128_out), .sel(b2_desloca_16));
  Multiplexer #(.enable("false")) multiplexer_129 (
    .in0(multiplexer_128_out), .in1(1'b0), .out(multiplexer_129_out), .sel(b2_desloca_8));
  Multiplexer #(.enable("false")) multiplexer_130 (
    .in0(multiplexer_122_out), .in1(multiplexer_146_out), .out(multiplexer_130_out), .sel(b2_desloca_4));
  Multiplexer #(.enable("false")) multiplexer_131 (
    .in0(multiplexer_129_out), .in1(multiplexer_153_out), .out(multiplexer_131_out), .sel(b2_desloca_4));
  Multiplexer #(.enable("false")) multiplexer_132 (
    .in0(multiplexer_130_out), .in1(multiplexer_141_out), .out(multiplexer_132_out), .sel(b1_desloca_2));
  Multiplexer #(.enable("false")) multiplexer_133 (
    .in0(multiplexer_131_out), .in1(multiplexer_140_out), .out(multiplexer_133_out), .sel(b1_desloca_2));
  Multiplexer #(.enable("false")) multiplexer_134 (
    .in0(multiplexer_132_out), .in1(multiplexer_133_out), .out(out_7[6]), .sel(b0_desloca_1));
  Multiplexer #(.enable("false")) multiplexer_135 (
    .in0(multiplexer_133_out), .in1(multiplexer_142_out), .out(out_7[5]), .sel(b0_desloca_1));
  Multiplexer #(.enable("false")) multiplexer_136 (
    .in0(in_1[3]), .in1(1'b0), .out(multiplexer_136_out), .sel(b2_desloca_16));
  Multiplexer #(.enable("false")) multiplexer_137 (
    .in0(in_1[4]), .in1(1'b0), .out(multiplexer_137_out), .sel(b2_desloca_16));
  Multiplexer #(.enable("false")) multiplexer_138 (
    .in0(multiplexer_137_out), .in1(1'b0), .out(multiplexer_138_out), .sel(b2_desloca_8));
  Multiplexer #(.enable("false")) multiplexer_139 (
    .in0(multiplexer_136_out), .in1(1'b0), .out(multiplexer_139_out), .sel(b2_desloca_8));
  Multiplexer #(.enable("false")) multiplexer_140 (
    .in0(multiplexer_139_out), .in1(1'b0), .out(multiplexer_140_out), .sel(b2_desloca_4));
  Multiplexer #(.enable("false")) multiplexer_141 (
    .in0(multiplexer_138_out), .in1(multiplexer_154_out), .out(multiplexer_141_out), .sel(b2_desloca_4));
  Multiplexer #(.enable("false")) multiplexer_142 (
    .in0(multiplexer_141_out), .in1(multiplexer_147_out), .out(multiplexer_142_out), .sel(b1_desloca_2));
  Multiplexer #(.enable("false")) multiplexer_143 (
    .in0(multiplexer_142_out), .in1(multiplexer_149_out), .out(out_7[4]), .sel(b0_desloca_1));
  Multiplexer #(.enable("false")) multiplexer_144 (
    .in0(in_1[2]), .in1(1'b0), .out(multiplexer_144_out), .sel(b2_desloca_16));
  Multiplexer #(.enable("false")) multiplexer_145 (
    .in0(in_1[1]), .in1(1'b0), .out(multiplexer_145_out), .sel(b2_desloca_16));
  Multiplexer #(.enable("false")) multiplexer_146 (
    .in0(multiplexer_144_out), .in1(1'b0), .out(multiplexer_146_out), .sel(b2_desloca_8));
  Multiplexer #(.enable("false")) multiplexer_147 (
    .in0(multiplexer_146_out), .in1(1'b0), .out(multiplexer_147_out), .sel(b2_desloca_4));
  Multiplexer #(.enable("false")) multiplexer_148 (
    .in0(multiplexer_147_out), .in1(multiplexer_156_out), .out(multiplexer_148_out), .sel(b1_desloca_2));
  Multiplexer #(.enable("false")) multiplexer_149 (
    .in0(multiplexer_140_out), .in1(multiplexer_155_out), .out(multiplexer_149_out), .sel(b1_desloca_2));
  Multiplexer #(.enable("false")) multiplexer_150 (
    .in0(multiplexer_149_out), .in1(multiplexer_148_out), .out(out_7[3]), .sel(b0_desloca_1));
  Multiplexer #(.enable("false")) multiplexer_151 (
    .in0(multiplexer_148_out), .in1(multiplexer_158_out), .out(out_7[2]), .sel(b0_desloca_1));
  Multiplexer #(.enable("false")) multiplexer_152 (
    .in0(in_1[0]), .in1(1'b0), .out(multiplexer_152_out), .sel(b2_desloca_16));
  Multiplexer #(.enable("false")) multiplexer_153 (
    .in0(multiplexer_145_out), .in1(1'b0), .out(multiplexer_153_out), .sel(b2_desloca_8));
  Multiplexer #(.enable("false")) multiplexer_154 (
    .in0(multiplexer_152_out), .in1(1'b0), .out(multiplexer_154_out), .sel(b2_desloca_8));
  Multiplexer #(.enable("false")) multiplexer_155 (
    .in0(multiplexer_153_out), .in1(1'b0), .out(multiplexer_155_out), .sel(b2_desloca_4));
  Multiplexer #(.enable("false")) multiplexer_156 (
    .in0(multiplexer_154_out), .in1(1'b0), .out(multiplexer_156_out), .sel(b2_desloca_4));
  Multiplexer #(.enable("false")) multiplexer_157 (
    .in0(multiplexer_156_out), .in1(1'b0), .out(multiplexer_157_out), .sel(b1_desloca_2));
  Multiplexer #(.enable("false")) multiplexer_158 (
    .in0(multiplexer_155_out), .in1(1'b0), .out(multiplexer_158_out), .sel(b1_desloca_2));
  Multiplexer #(.enable("false")) multiplexer_159 (
    .in0(multiplexer_158_out), .in1(multiplexer_157_out), .out(out_7[1]), .sel(b0_desloca_1));
  Multiplexer #(.enable("false")) multiplexer_160 (
    .in0(multiplexer_157_out), .in1(1'b0), .out(out_7[0]), .sel(b0_desloca_1));
endmodule

// C-shift_right
module Circular_shift_right (
  input  [31:0] in_1,
  input  b2_desloca_16,
  input  b2_desloca_8,
  input  b2_desloca_4,
  input  b1_desloca_2,
  input  b0_desloca_1,
  output [31:0] out_7
);

  wire multiplexer_1_out, multiplexer_2_out, multiplexer_3_out, multiplexer_4_out, multiplexer_5_out,
       multiplexer_6_out, multiplexer_7_out, multiplexer_8_out, multiplexer_10_out, multiplexer_11_out,
       multiplexer_12_out, multiplexer_13_out, multiplexer_14_out, multiplexer_17_out, multiplexer_18_out,
       multiplexer_19_out, multiplexer_20_out, multiplexer_21_out, multiplexer_22_out, multiplexer_23_out,
       multiplexer_26_out, multiplexer_27_out, multiplexer_28_out, multiplexer_29_out, multiplexer_30_out,
       multiplexer_31_out, multiplexer_33_out, multiplexer_34_out, multiplexer_35_out, multiplexer_36_out,
       multiplexer_37_out, multiplexer_38_out, multiplexer_41_out, multiplexer_42_out, multiplexer_43_out,
       multiplexer_44_out, multiplexer_45_out, multiplexer_46_out, multiplexer_47_out, multiplexer_48_out,
       multiplexer_50_out, multiplexer_51_out, multiplexer_52_out, multiplexer_53_out, multiplexer_54_out,
       multiplexer_57_out, multiplexer_58_out, multiplexer_59_out, multiplexer_60_out, multiplexer_61_out,
       multiplexer_62_out, multiplexer_63_out, multiplexer_66_out, multiplexer_67_out, multiplexer_68_out,
       multiplexer_69_out, multiplexer_70_out, multiplexer_71_out, multiplexer_73_out, multiplexer_74_out,
       multiplexer_75_out, multiplexer_76_out, multiplexer_77_out, multiplexer_78_out, multiplexer_81_out,
       multiplexer_82_out, multiplexer_83_out, multiplexer_84_out, multiplexer_85_out, multiplexer_86_out,
       multiplexer_87_out, multiplexer_88_out, multiplexer_90_out, multiplexer_91_out, multiplexer_92_out,
       multiplexer_93_out, multiplexer_94_out, multiplexer_97_out, multiplexer_98_out, multiplexer_99_out,
       multiplexer_100_out, multiplexer_101_out, multiplexer_102_out, multiplexer_103_out,
       multiplexer_106_out, multiplexer_107_out, multiplexer_108_out, multiplexer_109_out,
       multiplexer_110_out, multiplexer_111_out, multiplexer_113_out, multiplexer_114_out,
       multiplexer_115_out, multiplexer_116_out, multiplexer_117_out, multiplexer_118_out,
       multiplexer_121_out, multiplexer_122_out, multiplexer_123_out, multiplexer_124_out,
       multiplexer_125_out, multiplexer_126_out, multiplexer_127_out, multiplexer_128_out,
       multiplexer_130_out, multiplexer_131_out, multiplexer_132_out, multiplexer_133_out,
       multiplexer_134_out, multiplexer_137_out, multiplexer_138_out, multiplexer_139_out,
       multiplexer_140_out, multiplexer_141_out, multiplexer_142_out, multiplexer_143_out,
       multiplexer_146_out, multiplexer_147_out, multiplexer_148_out, multiplexer_149_out,
       multiplexer_150_out, multiplexer_151_out, multiplexer_153_out, multiplexer_154_out,
       multiplexer_155_out, multiplexer_156_out, multiplexer_157_out, multiplexer_158_out;

  Multiplexer #(.enable("false")) multiplexer_1 (
    .in0(in_1[30]), .in1(in_1[14]), .out(multiplexer_1_out), .sel(b2_desloca_16));
  Multiplexer #(.enable("false")) multiplexer_2 (
    .in0(in_1[31]), .in1(in_1[15]), .out(multiplexer_2_out), .sel(b2_desloca_16));
  Multiplexer #(.enable("false")) multiplexer_3 (
    .in0(multiplexer_1_out), .in1(multiplexer_122_out), .out(multiplexer_3_out), .sel(b2_desloca_8));
  Multiplexer #(.enable("false")) multiplexer_4 (
    .in0(multiplexer_2_out), .in1(multiplexer_121_out), .out(multiplexer_4_out), .sel(b2_desloca_8));
  Multiplexer #(.enable("false")) multiplexer_5 (
    .in0(multiplexer_4_out), .in1(multiplexer_139_out), .out(multiplexer_5_out), .sel(b2_desloca_4));
  Multiplexer #(.enable("false")) multiplexer_6 (
    .in0(multiplexer_3_out), .in1(multiplexer_148_out), .out(multiplexer_6_out), .sel(b2_desloca_4));
  Multiplexer #(.enable("false")) multiplexer_7 (
    .in0(multiplexer_6_out), .in1(multiplexer_155_out), .out(multiplexer_7_out), .sel(b1_desloca_2));
  Multiplexer #(.enable("false")) multiplexer_8 (
    .in0(multiplexer_5_out), .in1(multiplexer_156_out), .out(multiplexer_8_out), .sel(b1_desloca_2));
  Multiplexer #(.enable("false")) multiplexer_9 (
    .in0(multiplexer_8_out), .in1(multiplexer_157_out), .out(out_7[31]), .sel(b0_desloca_1));
  Multiplexer #(.enable("false")) multiplexer_10 (
    .in0(in_1[28]), .in1(in_1[12]), .out(multiplexer_10_out), .sel(b2_desloca_16));
  Multiplexer #(.enable("false")) multiplexer_11 (
    .in0(in_1[29]), .in1(in_1[13]), .out(multiplexer_11_out), .sel(b2_desloca_16));
  Multiplexer #(.enable("false")) multiplexer_12 (
    .in0(multiplexer_11_out), .in1(multiplexer_130_out), .out(multiplexer_12_out), .sel(b2_desloca_8));
  Multiplexer #(.enable("false")) multiplexer_13 (
    .in0(multiplexer_12_out), .in1(multiplexer_149_out), .out(multiplexer_13_out), .sel(b2_desloca_4));
  Multiplexer #(.enable("false")) multiplexer_14 (
    .in0(multiplexer_13_out), .in1(multiplexer_5_out), .out(multiplexer_14_out), .sel(b1_desloca_2));
  Multiplexer #(.enable("false")) multiplexer_15 (
    .in0(multiplexer_7_out), .in1(multiplexer_8_out), .out(out_7[30]), .sel(b0_desloca_1));
  Multiplexer #(.enable("false")) multiplexer_16 (
    .in0(multiplexer_14_out), .in1(multiplexer_7_out), .out(out_7[29]), .sel(b0_desloca_1));
  Multiplexer #(.enable("false")) multiplexer_17 (
    .in0(in_1[27]), .in1(in_1[11]), .out(multiplexer_17_out), .sel(b2_desloca_16));
  Multiplexer #(.enable("false")) multiplexer_18 (
    .in0(multiplexer_17_out), .in1(multiplexer_137_out), .out(multiplexer_18_out), .sel(b2_desloca_8));
  Multiplexer #(.enable("false")) multiplexer_19 (
    .in0(multiplexer_10_out), .in1(multiplexer_131_out), .out(multiplexer_19_out), .sel(b2_desloca_8));
  Multiplexer #(.enable("false")) multiplexer_20 (
    .in0(multiplexer_19_out), .in1(multiplexer_154_out), .out(multiplexer_20_out), .sel(b2_desloca_4));
  Multiplexer #(.enable("false")) multiplexer_21 (
    .in0(multiplexer_18_out), .in1(multiplexer_4_out), .out(multiplexer_21_out), .sel(b2_desloca_4));
  Multiplexer #(.enable("false")) multiplexer_22 (
    .in0(multiplexer_21_out), .in1(multiplexer_13_out), .out(multiplexer_22_out), .sel(b1_desloca_2));
  Multiplexer #(.enable("false")) multiplexer_23 (
    .in0(multiplexer_20_out), .in1(multiplexer_6_out), .out(multiplexer_23_out), .sel(b1_desloca_2));
  Multiplexer #(.enable("false")) multiplexer_24 (
    .in0(multiplexer_22_out), .in1(multiplexer_23_out), .out(out_7[27]), .sel(b0_desloca_1));
  Multiplexer #(.enable("false")) multiplexer_25 (
    .in0(multiplexer_23_out), .in1(multiplexer_14_out), .out(out_7[28]), .sel(b0_desloca_1));
  Multiplexer #(.enable("false")) multiplexer_26 (
    .in0(in_1[26]), .in1(in_1[10]), .out(multiplexer_26_out), .sel(b2_desloca_16));
  Multiplexer #(.enable("false")) multiplexer_27 (
    .in0(in_1[25]), .in1(in_1[9]), .out(multiplexer_27_out), .sel(b2_desloca_16));
  Multiplexer #(.enable("false")) multiplexer_28 (
    .in0(multiplexer_26_out), .in1(multiplexer_146_out), .out(multiplexer_28_out), .sel(b2_desloca_8));
  Multiplexer #(.enable("false")) multiplexer_29 (
    .in0(multiplexer_27_out), .in1(multiplexer_147_out), .out(multiplexer_29_out), .sel(b2_desloca_8));
  Multiplexer #(.enable("false")) multiplexer_30 (
    .in0(multiplexer_28_out), .in1(multiplexer_3_out), .out(multiplexer_30_out), .sel(b2_desloca_4));
  Multiplexer #(.enable("false")) multiplexer_31 (
    .in0(multiplexer_30_out), .in1(multiplexer_20_out), .out(multiplexer_31_out), .sel(b1_desloca_2));
  Multiplexer #(.enable("false")) multiplexer_32 (
    .in0(multiplexer_31_out), .in1(multiplexer_22_out), .out(out_7[26]), .sel(b0_desloca_1));
  Multiplexer #(.enable("false")) multiplexer_33 (
    .in0(in_1[24]), .in1(in_1[8]), .out(multiplexer_33_out), .sel(b2_desloca_16));
  Multiplexer #(.enable("false")) multiplexer_34 (
    .in0(multiplexer_33_out), .in1(multiplexer_153_out), .out(multiplexer_34_out), .sel(b2_desloca_8));
  Multiplexer #(.enable("false")) multiplexer_35 (
    .in0(multiplexer_29_out), .in1(multiplexer_12_out), .out(multiplexer_35_out), .sel(b2_desloca_4));
  Multiplexer #(.enable("false")) multiplexer_36 (
    .in0(multiplexer_34_out), .in1(multiplexer_19_out), .out(multiplexer_36_out), .sel(b2_desloca_4));
  Multiplexer #(.enable("false")) multiplexer_37 (
    .in0(multiplexer_35_out), .in1(multiplexer_21_out), .out(multiplexer_37_out), .sel(b1_desloca_2));
  Multiplexer #(.enable("false")) multiplexer_38 (
    .in0(multiplexer_36_out), .in1(multiplexer_30_out), .out(multiplexer_38_out), .sel(b1_desloca_2));
  Multiplexer #(.enable("false")) multiplexer_39 (
    .in0(multiplexer_38_out), .in1(multiplexer_37_out), .out(out_7[24]), .sel(b0_desloca_1));
  Multiplexer #(.enable("false")) multiplexer_40 (
    .in0(multiplexer_37_out), .in1(multiplexer_31_out), .out(out_7[25]), .sel(b0_desloca_1));
  Multiplexer #(.enable("false")) multiplexer_41 (
    .in0(in_1[23]), .in1(in_1[7]), .out(multiplexer_41_out), .sel(b2_desloca_16));
  Multiplexer #(.enable("false")) multiplexer_42 (
    .in0(in_1[22]), .in1(in_1[6]), .out(multiplexer_42_out), .sel(b2_desloca_16));
  Multiplexer #(.enable("false")) multiplexer_43 (
    .in0(multiplexer_42_out), .in1(multiplexer_1_out), .out(multiplexer_43_out), .sel(b2_desloca_8));
  Multiplexer #(.enable("false")) multiplexer_44 (
    .in0(multiplexer_41_out), .in1(multiplexer_2_out), .out(multiplexer_44_out), .sel(b2_desloca_8));
  Multiplexer #(.enable("false")) multiplexer_45 (
    .in0(multiplexer_44_out), .in1(multiplexer_18_out), .out(multiplexer_45_out), .sel(b2_desloca_4));
  Multiplexer #(.enable("false")) multiplexer_46 (
    .in0(multiplexer_43_out), .in1(multiplexer_28_out), .out(multiplexer_46_out), .sel(b2_desloca_4));
  Multiplexer #(.enable("false")) multiplexer_47 (
    .in0(multiplexer_46_out), .in1(multiplexer_36_out), .out(multiplexer_47_out), .sel(b1_desloca_2));
  Multiplexer #(.enable("false")) multiplexer_48 (
    .in0(multiplexer_45_out), .in1(multiplexer_35_out), .out(multiplexer_48_out), .sel(b1_desloca_2));
  Multiplexer #(.enable("false")) multiplexer_49 (
    .in0(multiplexer_48_out), .in1(multiplexer_38_out), .out(out_7[23]), .sel(b0_desloca_1));
  Multiplexer #(.enable("false")) multiplexer_50 (
    .in0(in_1[21]), .in1(in_1[5]), .out(multiplexer_50_out), .sel(b2_desloca_16));
  Multiplexer #(.enable("false")) multiplexer_51 (
    .in0(in_1[20]), .in1(in_1[4]), .out(multiplexer_51_out), .sel(b2_desloca_16));
  Multiplexer #(.enable("false")) multiplexer_52 (
    .in0(multiplexer_50_out), .in1(multiplexer_11_out), .out(multiplexer_52_out), .sel(b2_desloca_8));
  Multiplexer #(.enable("false")) multiplexer_53 (
    .in0(multiplexer_52_out), .in1(multiplexer_29_out), .out(multiplexer_53_out), .sel(b2_desloca_4));
  Multiplexer #(.enable("false")) multiplexer_54 (
    .in0(multiplexer_53_out), .in1(multiplexer_45_out), .out(multiplexer_54_out), .sel(b1_desloca_2));
  Multiplexer #(.enable("false")) multiplexer_55 (
    .in0(multiplexer_54_out), .in1(multiplexer_47_out), .out(out_7[21]), .sel(b0_desloca_1));
  Multiplexer #(.enable("false")) multiplexer_56 (
    .in0(multiplexer_47_out), .in1(multiplexer_48_out), .out(out_7[22]), .sel(b0_desloca_1));
  Multiplexer #(.enable("false")) multiplexer_57 (
    .in0(in_1[19]), .in1(in_1[3]), .out(multiplexer_57_out), .sel(b2_desloca_16));
  Multiplexer #(.enable("false")) multiplexer_58 (
    .in0(multiplexer_57_out), .in1(multiplexer_17_out), .out(multiplexer_58_out), .sel(b2_desloca_8));
  Multiplexer #(.enable("false")) multiplexer_59 (
    .in0(multiplexer_51_out), .in1(multiplexer_10_out), .out(multiplexer_59_out), .sel(b2_desloca_8));
  Multiplexer #(.enable("false")) multiplexer_60 (
    .in0(multiplexer_59_out), .in1(multiplexer_34_out), .out(multiplexer_60_out), .sel(b2_desloca_4));
  Multiplexer #(.enable("false")) multiplexer_61 (
    .in0(multiplexer_58_out), .in1(multiplexer_44_out), .out(multiplexer_61_out), .sel(b2_desloca_4));
  Multiplexer #(.enable("false")) multiplexer_62 (
    .in0(multiplexer_61_out), .in1(multiplexer_53_out), .out(multiplexer_62_out), .sel(b1_desloca_2));
  Multiplexer #(.enable("false")) multiplexer_63 (
    .in0(multiplexer_60_out), .in1(multiplexer_46_out), .out(multiplexer_63_out), .sel(b1_desloca_2));
  Multiplexer #(.enable("false")) multiplexer_64 (
    .in0(multiplexer_63_out), .in1(multiplexer_54_out), .out(out_7[20]), .sel(b0_desloca_1));
  Multiplexer #(.enable("false")) multiplexer_65 (
    .in0(multiplexer_62_out), .in1(multiplexer_63_out), .out(out_7[19]), .sel(b0_desloca_1));
  Multiplexer #(.enable("false")) multiplexer_66 (
    .in0(in_1[17]), .in1(in_1[1]), .out(multiplexer_66_out), .sel(b2_desloca_16));
  Multiplexer #(.enable("false")) multiplexer_67 (
    .in0(in_1[18]), .in1(in_1[2]), .out(multiplexer_67_out), .sel(b2_desloca_16));
  Multiplexer #(.enable("false")) multiplexer_68 (
    .in0(multiplexer_66_out), .in1(multiplexer_27_out), .out(multiplexer_68_out), .sel(b2_desloca_8));
  Multiplexer #(.enable("false")) multiplexer_69 (
    .in0(multiplexer_67_out), .in1(multiplexer_26_out), .out(multiplexer_69_out), .sel(b2_desloca_8));
  Multiplexer #(.enable("false")) multiplexer_70 (
    .in0(multiplexer_69_out), .in1(multiplexer_43_out), .out(multiplexer_70_out), .sel(b2_desloca_4));
  Multiplexer #(.enable("false")) multiplexer_71 (
    .in0(multiplexer_70_out), .in1(multiplexer_60_out), .out(multiplexer_71_out), .sel(b1_desloca_2));
  Multiplexer #(.enable("false")) multiplexer_72 (
    .in0(multiplexer_71_out), .in1(multiplexer_62_out), .out(out_7[18]), .sel(b0_desloca_1));
  Multiplexer #(.enable("false")) multiplexer_73 (
    .in0(in_1[16]), .in1(in_1[0]), .out(multiplexer_73_out), .sel(b2_desloca_16));
  Multiplexer #(.enable("false")) multiplexer_74 (
    .in0(multiplexer_73_out), .in1(multiplexer_33_out), .out(multiplexer_74_out), .sel(b2_desloca_8));
  Multiplexer #(.enable("false")) multiplexer_75 (
    .in0(multiplexer_68_out), .in1(multiplexer_52_out), .out(multiplexer_75_out), .sel(b2_desloca_4));
  Multiplexer #(.enable("false")) multiplexer_76 (
    .in0(multiplexer_74_out), .in1(multiplexer_59_out), .out(multiplexer_76_out), .sel(b2_desloca_4));
  Multiplexer #(.enable("false")) multiplexer_77 (
    .in0(multiplexer_75_out), .in1(multiplexer_61_out), .out(multiplexer_77_out), .sel(b1_desloca_2));
  Multiplexer #(.enable("false")) multiplexer_78 (
    .in0(multiplexer_76_out), .in1(multiplexer_70_out), .out(multiplexer_78_out), .sel(b1_desloca_2));
  Multiplexer #(.enable("false")) multiplexer_79 (
    .in0(multiplexer_77_out), .in1(multiplexer_71_out), .out(out_7[17]), .sel(b0_desloca_1));
  Multiplexer #(.enable("false")) multiplexer_80 (
    .in0(multiplexer_78_out), .in1(multiplexer_77_out), .out(out_7[16]), .sel(b0_desloca_1));
  Multiplexer #(.enable("false")) multiplexer_81 (
    .in0(in_1[15]), .in1(in_1[31]), .out(multiplexer_81_out), .sel(b2_desloca_16));
  Multiplexer #(.enable("false")) multiplexer_82 (
    .in0(in_1[14]), .in1(in_1[30]), .out(multiplexer_82_out), .sel(b2_desloca_16));
  Multiplexer #(.enable("false")) multiplexer_83 (
    .in0(multiplexer_82_out), .in1(multiplexer_42_out), .out(multiplexer_83_out), .sel(b2_desloca_8));
  Multiplexer #(.enable("false")) multiplexer_84 (
    .in0(multiplexer_81_out), .in1(multiplexer_41_out), .out(multiplexer_84_out), .sel(b2_desloca_8));
  Multiplexer #(.enable("false")) multiplexer_85 (
    .in0(multiplexer_83_out), .in1(multiplexer_69_out), .out(multiplexer_85_out), .sel(b2_desloca_4));
  Multiplexer #(.enable("false")) multiplexer_86 (
    .in0(multiplexer_84_out), .in1(multiplexer_58_out), .out(multiplexer_86_out), .sel(b2_desloca_4));
  Multiplexer #(.enable("false")) multiplexer_87 (
    .in0(multiplexer_86_out), .in1(multiplexer_75_out), .out(multiplexer_87_out), .sel(b1_desloca_2));
  Multiplexer #(.enable("false")) multiplexer_88 (
    .in0(multiplexer_85_out), .in1(multiplexer_76_out), .out(multiplexer_88_out), .sel(b1_desloca_2));
  Multiplexer #(.enable("false")) multiplexer_89 (
    .in0(multiplexer_87_out), .in1(multiplexer_78_out), .out(out_7[15]), .sel(b0_desloca_1));
  Multiplexer #(.enable("false")) multiplexer_90 (
    .in0(in_1[12]), .in1(in_1[28]), .out(multiplexer_90_out), .sel(b2_desloca_16));
  Multiplexer #(.enable("false")) multiplexer_91 (
    .in0(in_1[13]), .in1(in_1[29]), .out(multiplexer_91_out), .sel(b2_desloca_16));
  Multiplexer #(.enable("false")) multiplexer_92 (
    .in0(multiplexer_91_out), .in1(multiplexer_50_out), .out(multiplexer_92_out), .sel(b2_desloca_8));
  Multiplexer #(.enable("false")) multiplexer_93 (
    .in0(multiplexer_92_out), .in1(multiplexer_68_out), .out(multiplexer_93_out), .sel(b2_desloca_4));
  Multiplexer #(.enable("false")) multiplexer_94 (
    .in0(multiplexer_93_out), .in1(multiplexer_86_out), .out(multiplexer_94_out), .sel(b1_desloca_2));
  Multiplexer #(.enable("false")) multiplexer_95 (
    .in0(multiplexer_94_out), .in1(multiplexer_88_out), .out(out_7[13]), .sel(b0_desloca_1));
  Multiplexer #(.enable("false")) multiplexer_96 (
    .in0(multiplexer_88_out), .in1(multiplexer_87_out), .out(out_7[14]), .sel(b0_desloca_1));
  Multiplexer #(.enable("false")) multiplexer_97 (
    .in0(in_1[11]), .in1(in_1[27]), .out(multiplexer_97_out), .sel(b2_desloca_16));
  Multiplexer #(.enable("false")) multiplexer_98 (
    .in0(multiplexer_90_out), .in1(multiplexer_51_out), .out(multiplexer_98_out), .sel(b2_desloca_8));
  Multiplexer #(.enable("false")) multiplexer_99 (
    .in0(multiplexer_97_out), .in1(multiplexer_57_out), .out(multiplexer_99_out), .sel(b2_desloca_8));
  Multiplexer #(.enable("false")) multiplexer_100 (
    .in0(multiplexer_98_out), .in1(multiplexer_74_out), .out(multiplexer_100_out), .sel(b2_desloca_4));
  Multiplexer #(.enable("false")) multiplexer_101 (
    .in0(multiplexer_99_out), .in1(multiplexer_84_out), .out(multiplexer_101_out), .sel(b2_desloca_4));
  Multiplexer #(.enable("false")) multiplexer_102 (
    .in0(multiplexer_100_out), .in1(multiplexer_85_out), .out(multiplexer_102_out), .sel(b1_desloca_2));
  Multiplexer #(.enable("false")) multiplexer_103 (
    .in0(multiplexer_101_out), .in1(multiplexer_93_out), .out(multiplexer_103_out), .sel(b1_desloca_2));
  Multiplexer #(.enable("false")) multiplexer_104 (
    .in0(multiplexer_102_out), .in1(multiplexer_94_out), .out(out_7[12]), .sel(b0_desloca_1));
  Multiplexer #(.enable("false")) multiplexer_105 (
    .in0(multiplexer_103_out), .in1(multiplexer_102_out), .out(out_7[11]), .sel(b0_desloca_1));
  Multiplexer #(.enable("false")) multiplexer_106 (
    .in0(in_1[9]), .in1(in_1[25]), .out(multiplexer_106_out), .sel(b2_desloca_16));
  Multiplexer #(.enable("false")) multiplexer_107 (
    .in0(in_1[10]), .in1(in_1[26]), .out(multiplexer_107_out), .sel(b2_desloca_16));
  Multiplexer #(.enable("false")) multiplexer_108 (
    .in0(multiplexer_107_out), .in1(multiplexer_67_out), .out(multiplexer_108_out), .sel(b2_desloca_8));
  Multiplexer #(.enable("false")) multiplexer_109 (
    .in0(multiplexer_106_out), .in1(multiplexer_66_out), .out(multiplexer_109_out), .sel(b2_desloca_8));
  Multiplexer #(.enable("false")) multiplexer_110 (
    .in0(multiplexer_108_out), .in1(multiplexer_83_out), .out(multiplexer_110_out), .sel(b2_desloca_4));
  Multiplexer #(.enable("false")) multiplexer_111 (
    .in0(multiplexer_110_out), .in1(multiplexer_100_out), .out(multiplexer_111_out), .sel(b1_desloca_2));
  Multiplexer #(.enable("false")) multiplexer_112 (
    .in0(multiplexer_111_out), .in1(multiplexer_103_out), .out(out_7[10]), .sel(b0_desloca_1));
  Multiplexer #(.enable("false")) multiplexer_113 (
    .in0(in_1[8]), .in1(in_1[24]), .out(multiplexer_113_out), .sel(b2_desloca_16));
  Multiplexer #(.enable("false")) multiplexer_114 (
    .in0(multiplexer_113_out), .in1(multiplexer_73_out), .out(multiplexer_114_out), .sel(b2_desloca_8));
  Multiplexer #(.enable("false")) multiplexer_115 (
    .in0(multiplexer_114_out), .in1(multiplexer_98_out), .out(multiplexer_115_out), .sel(b2_desloca_4));
  Multiplexer #(.enable("false")) multiplexer_116 (
    .in0(multiplexer_109_out), .in1(multiplexer_92_out), .out(multiplexer_116_out), .sel(b2_desloca_4));
  Multiplexer #(.enable("false")) multiplexer_117 (
    .in0(multiplexer_115_out), .in1(multiplexer_110_out), .out(multiplexer_117_out), .sel(b1_desloca_2));
  Multiplexer #(.enable("false")) multiplexer_118 (
    .in0(multiplexer_116_out), .in1(multiplexer_101_out), .out(multiplexer_118_out), .sel(b1_desloca_2));
  Multiplexer #(.enable("false")) multiplexer_119 (
    .in0(multiplexer_118_out), .in1(multiplexer_111_out), .out(out_7[9]), .sel(b0_desloca_1));
  Multiplexer #(.enable("false")) multiplexer_120 (
    .in0(multiplexer_117_out), .in1(multiplexer_118_out), .out(out_7[8]), .sel(b0_desloca_1));
  Multiplexer #(.enable("false")) multiplexer_121 (
    .in0(in_1[7]), .in1(in_1[23]), .out(multiplexer_121_out), .sel(b2_desloca_16));
  Multiplexer #(.enable("false")) multiplexer_122 (
    .in0(in_1[6]), .in1(in_1[22]), .out(multiplexer_122_out), .sel(b2_desloca_16));
  Multiplexer #(.enable("false")) multiplexer_123 (
    .in0(multiplexer_121_out), .in1(multiplexer_81_out), .out(multiplexer_123_out), .sel(b2_desloca_8));
  Multiplexer #(.enable("false")) multiplexer_124 (
    .in0(multiplexer_122_out), .in1(multiplexer_82_out), .out(multiplexer_124_out), .sel(b2_desloca_8));
  Multiplexer #(.enable("false")) multiplexer_125 (
    .in0(multiplexer_124_out), .in1(multiplexer_108_out), .out(multiplexer_125_out), .sel(b2_desloca_4));
  Multiplexer #(.enable("false")) multiplexer_126 (
    .in0(multiplexer_123_out), .in1(multiplexer_99_out), .out(multiplexer_126_out), .sel(b2_desloca_4));
  Multiplexer #(.enable("false")) multiplexer_127 (
    .in0(multiplexer_126_out), .in1(multiplexer_116_out), .out(multiplexer_127_out), .sel(b1_desloca_2));
  Multiplexer #(.enable("false")) multiplexer_128 (
    .in0(multiplexer_125_out), .in1(multiplexer_115_out), .out(multiplexer_128_out), .sel(b1_desloca_2));
  Multiplexer #(.enable("false")) multiplexer_129 (
    .in0(multiplexer_127_out), .in1(multiplexer_117_out), .out(out_7[7]), .sel(b0_desloca_1));
  Multiplexer #(.enable("false")) multiplexer_130 (
    .in0(in_1[5]), .in1(in_1[21]), .out(multiplexer_130_out), .sel(b2_desloca_16));
  Multiplexer #(.enable("false")) multiplexer_131 (
    .in0(in_1[4]), .in1(in_1[20]), .out(multiplexer_131_out), .sel(b2_desloca_16));
  Multiplexer #(.enable("false")) multiplexer_132 (
    .in0(multiplexer_130_out), .in1(multiplexer_91_out), .out(multiplexer_132_out), .sel(b2_desloca_8));
  Multiplexer #(.enable("false")) multiplexer_133 (
    .in0(multiplexer_132_out), .in1(multiplexer_109_out), .out(multiplexer_133_out), .sel(b2_desloca_4));
  Multiplexer #(.enable("false")) multiplexer_134 (
    .in0(multiplexer_133_out), .in1(multiplexer_126_out), .out(multiplexer_134_out), .sel(b1_desloca_2));
  Multiplexer #(.enable("false")) multiplexer_135 (
    .in0(multiplexer_128_out), .in1(multiplexer_127_out), .out(out_7[6]), .sel(b0_desloca_1));
  Multiplexer #(.enable("false")) multiplexer_136 (
    .in0(multiplexer_134_out), .in1(multiplexer_128_out), .out(out_7[5]), .sel(b0_desloca_1));
  Multiplexer #(.enable("false")) multiplexer_137 (
    .in0(in_1[3]), .in1(in_1[19]), .out(multiplexer_137_out), .sel(b2_desloca_16));
  Multiplexer #(.enable("false")) multiplexer_138 (
    .in0(multiplexer_131_out), .in1(multiplexer_90_out), .out(multiplexer_138_out), .sel(b2_desloca_8));
  Multiplexer #(.enable("false")) multiplexer_139 (
    .in0(multiplexer_137_out), .in1(multiplexer_97_out), .out(multiplexer_139_out), .sel(b2_desloca_8));
  Multiplexer #(.enable("false")) multiplexer_140 (
    .in0(multiplexer_138_out), .in1(multiplexer_114_out), .out(multiplexer_140_out), .sel(b2_desloca_4));
  Multiplexer #(.enable("false")) multiplexer_141 (
    .in0(multiplexer_139_out), .in1(multiplexer_123_out), .out(multiplexer_141_out), .sel(b2_desloca_4));
  Multiplexer #(.enable("false")) multiplexer_142 (
    .in0(multiplexer_141_out), .in1(multiplexer_133_out), .out(multiplexer_142_out), .sel(b1_desloca_2));
  Multiplexer #(.enable("false")) multiplexer_143 (
    .in0(multiplexer_140_out), .in1(multiplexer_125_out), .out(multiplexer_143_out), .sel(b1_desloca_2));
  Multiplexer #(.enable("false")) multiplexer_144 (
    .in0(multiplexer_142_out), .in1(multiplexer_143_out), .out(out_7[3]), .sel(b0_desloca_1));
  Multiplexer #(.enable("false")) multiplexer_145 (
    .in0(multiplexer_143_out), .in1(multiplexer_134_out), .out(out_7[4]), .sel(b0_desloca_1));
  Multiplexer #(.enable("false")) multiplexer_146 (
    .in0(in_1[2]), .in1(in_1[18]), .out(multiplexer_146_out), .sel(b2_desloca_16));
  Multiplexer #(.enable("false")) multiplexer_147 (
    .in0(in_1[1]), .in1(in_1[17]), .out(multiplexer_147_out), .sel(b2_desloca_16));
  Multiplexer #(.enable("false")) multiplexer_148 (
    .in0(multiplexer_146_out), .in1(multiplexer_107_out), .out(multiplexer_148_out), .sel(b2_desloca_8));
  Multiplexer #(.enable("false")) multiplexer_149 (
    .in0(multiplexer_147_out), .in1(multiplexer_106_out), .out(multiplexer_149_out), .sel(b2_desloca_8));
  Multiplexer #(.enable("false")) multiplexer_150 (
    .in0(multiplexer_148_out), .in1(multiplexer_124_out), .out(multiplexer_150_out), .sel(b2_desloca_4));
  Multiplexer #(.enable("false")) multiplexer_151 (
    .in0(multiplexer_150_out), .in1(multiplexer_140_out), .out(multiplexer_151_out), .sel(b1_desloca_2));
  Multiplexer #(.enable("false")) multiplexer_152 (
    .in0(multiplexer_151_out), .in1(multiplexer_142_out), .out(out_7[2]), .sel(b0_desloca_1));
  Multiplexer #(.enable("false")) multiplexer_153 (
    .in0(in_1[0]), .in1(in_1[16]), .out(multiplexer_153_out), .sel(b2_desloca_16));
  Multiplexer #(.enable("false")) multiplexer_154 (
    .in0(multiplexer_153_out), .in1(multiplexer_113_out), .out(multiplexer_154_out), .sel(b2_desloca_8));
  Multiplexer #(.enable("false")) multiplexer_155 (
    .in0(multiplexer_154_out), .in1(multiplexer_138_out), .out(multiplexer_155_out), .sel(b2_desloca_4));
  Multiplexer #(.enable("false")) multiplexer_156 (
    .in0(multiplexer_149_out), .in1(multiplexer_132_out), .out(multiplexer_156_out), .sel(b2_desloca_4));
  Multiplexer #(.enable("false")) multiplexer_157 (
    .in0(multiplexer_155_out), .in1(multiplexer_150_out), .out(multiplexer_157_out), .sel(b1_desloca_2));
  Multiplexer #(.enable("false")) multiplexer_158 (
    .in0(multiplexer_156_out), .in1(multiplexer_141_out), .out(multiplexer_158_out), .sel(b1_desloca_2));
  Multiplexer #(.enable("false")) multiplexer_159 (
    .in0(multiplexer_157_out), .in1(multiplexer_158_out), .out(out_7[0]), .sel(b0_desloca_1));
  Multiplexer #(.enable("false")) multiplexer_160 (
    .in0(multiplexer_158_out), .in1(multiplexer_151_out), .out(out_7[1]), .sel(b0_desloca_1));
endmodule

// C_shift_sinal
module circular_shift_right__bit_sinal (
  input  [31:0] in_1,
  input  b2_desloca_16,
  input  b2_desloca_8,
  input  b2_desloca_4,
  input  b1_desloca_2,
  input  b0_desloca_1,
  output [31:0] out_7
);

  wire multiplexer_1_out, multiplexer_2_out, multiplexer_3_out, multiplexer_4_out, multiplexer_5_out,
       multiplexer_6_out, multiplexer_7_out, multiplexer_8_out, multiplexer_10_out, multiplexer_11_out,
       multiplexer_12_out, multiplexer_13_out, multiplexer_14_out, multiplexer_17_out, multiplexer_18_out,
       multiplexer_19_out, multiplexer_20_out, multiplexer_21_out, multiplexer_22_out, multiplexer_23_out,
       multiplexer_26_out, multiplexer_27_out, multiplexer_28_out, multiplexer_29_out, multiplexer_30_out,
       multiplexer_31_out, multiplexer_33_out, multiplexer_34_out, multiplexer_35_out, multiplexer_36_out,
       multiplexer_37_out, multiplexer_38_out, multiplexer_41_out, multiplexer_42_out, multiplexer_43_out,
       multiplexer_44_out, multiplexer_45_out, multiplexer_46_out, multiplexer_47_out, multiplexer_48_out,
       multiplexer_50_out, multiplexer_51_out, multiplexer_52_out, multiplexer_53_out, multiplexer_54_out,
       multiplexer_57_out, multiplexer_58_out, multiplexer_59_out, multiplexer_60_out, multiplexer_61_out,
       multiplexer_62_out, multiplexer_63_out, multiplexer_66_out, multiplexer_67_out, multiplexer_68_out,
       multiplexer_69_out, multiplexer_70_out, multiplexer_71_out, multiplexer_73_out, multiplexer_74_out,
       multiplexer_75_out, multiplexer_76_out, multiplexer_77_out, multiplexer_78_out, multiplexer_81_out,
       multiplexer_82_out, multiplexer_83_out, multiplexer_84_out, multiplexer_85_out, multiplexer_86_out,
       multiplexer_87_out, multiplexer_88_out, multiplexer_90_out, multiplexer_91_out, multiplexer_92_out,
       multiplexer_93_out, multiplexer_94_out, multiplexer_97_out, multiplexer_98_out, multiplexer_99_out,
       multiplexer_100_out, multiplexer_101_out, multiplexer_102_out, multiplexer_103_out,
       multiplexer_106_out, multiplexer_107_out, multiplexer_108_out, multiplexer_109_out,
       multiplexer_110_out, multiplexer_111_out, multiplexer_113_out, multiplexer_114_out,
       multiplexer_115_out, multiplexer_116_out, multiplexer_117_out, multiplexer_118_out,
       multiplexer_121_out, multiplexer_122_out, multiplexer_123_out, multiplexer_124_out,
       multiplexer_125_out, multiplexer_126_out, multiplexer_127_out, multiplexer_128_out,
       multiplexer_130_out, multiplexer_131_out, multiplexer_132_out, multiplexer_133_out,
       multiplexer_134_out, multiplexer_137_out, multiplexer_138_out, multiplexer_139_out,
       multiplexer_140_out, multiplexer_141_out, multiplexer_142_out, multiplexer_143_out,
       multiplexer_146_out, multiplexer_147_out, multiplexer_148_out, multiplexer_149_out,
       multiplexer_150_out, multiplexer_151_out, multiplexer_153_out, multiplexer_154_out,
       multiplexer_155_out, multiplexer_156_out, multiplexer_157_out, multiplexer_158_out;

  Multiplexer #(.enable("false")) multiplexer_1 (
    .in0(in_1[31]), .in1(in_1[31]), .out(multiplexer_1_out), .sel(b2_desloca_16));
  Multiplexer #(.enable("false")) multiplexer_2 (
    .in0(in_1[30]), .in1(in_1[15]), .out(multiplexer_2_out), .sel(b2_desloca_16));
  Multiplexer #(.enable("false")) multiplexer_3 (
    .in0(multiplexer_2_out), .in1(multiplexer_121_out), .out(multiplexer_3_out), .sel(b2_desloca_8));
  Multiplexer #(.enable("false")) multiplexer_4 (
    .in0(multiplexer_1_out), .in1(multiplexer_1_out), .out(multiplexer_4_out), .sel(b2_desloca_8));
  Multiplexer #(.enable("false")) multiplexer_5 (
    .in0(multiplexer_4_out), .in1(multiplexer_4_out), .out(multiplexer_5_out), .sel(b2_desloca_4));
  Multiplexer #(.enable("false")) multiplexer_6 (
    .in0(multiplexer_3_out), .in1(multiplexer_138_out), .out(multiplexer_6_out), .sel(b2_desloca_4));
  Multiplexer #(.enable("false")) multiplexer_7 (
    .in0(multiplexer_6_out), .in1(multiplexer_155_out), .out(multiplexer_7_out), .sel(b1_desloca_2));
  Multiplexer #(.enable("false")) multiplexer_8 (
    .in0(multiplexer_5_out), .in1(multiplexer_5_out), .out(multiplexer_8_out), .sel(b1_desloca_2));
  Multiplexer #(.enable("false")) multiplexer_9 (
    .in0(multiplexer_8_out), .in1(multiplexer_8_out), .out(out_7[31]), .sel(b0_desloca_1));
  Multiplexer #(.enable("false")) multiplexer_10 (
    .in0(in_1[28]), .in1(in_1[13]), .out(multiplexer_10_out), .sel(b2_desloca_16));
  Multiplexer #(.enable("false")) multiplexer_11 (
    .in0(in_1[29]), .in1(in_1[14]), .out(multiplexer_11_out), .sel(b2_desloca_16));
  Multiplexer #(.enable("false")) multiplexer_12 (
    .in0(multiplexer_11_out), .in1(multiplexer_122_out), .out(multiplexer_12_out), .sel(b2_desloca_8));
  Multiplexer #(.enable("false")) multiplexer_13 (
    .in0(multiplexer_12_out), .in1(multiplexer_149_out), .out(multiplexer_13_out), .sel(b2_desloca_4));
  Multiplexer #(.enable("false")) multiplexer_14 (
    .in0(multiplexer_13_out), .in1(multiplexer_156_out), .out(multiplexer_14_out), .sel(b1_desloca_2));
  Multiplexer #(.enable("false")) multiplexer_15 (
    .in0(multiplexer_7_out), .in1(multiplexer_157_out), .out(out_7[30]), .sel(b0_desloca_1));
  Multiplexer #(.enable("false")) multiplexer_16 (
    .in0(multiplexer_14_out), .in1(multiplexer_7_out), .out(out_7[29]), .sel(b0_desloca_1));
  Multiplexer #(.enable("false")) multiplexer_17 (
    .in0(in_1[27]), .in1(in_1[12]), .out(multiplexer_17_out), .sel(b2_desloca_16));
  Multiplexer #(.enable("false")) multiplexer_18 (
    .in0(multiplexer_10_out), .in1(multiplexer_130_out), .out(multiplexer_18_out), .sel(b2_desloca_8));
  Multiplexer #(.enable("false")) multiplexer_19 (
    .in0(multiplexer_17_out), .in1(multiplexer_131_out), .out(multiplexer_19_out), .sel(b2_desloca_8));
  Multiplexer #(.enable("false")) multiplexer_20 (
    .in0(multiplexer_19_out), .in1(multiplexer_154_out), .out(multiplexer_20_out), .sel(b2_desloca_4));
  Multiplexer #(.enable("false")) multiplexer_21 (
    .in0(multiplexer_18_out), .in1(multiplexer_148_out), .out(multiplexer_21_out), .sel(b2_desloca_4));
  Multiplexer #(.enable("false")) multiplexer_22 (
    .in0(multiplexer_20_out), .in1(multiplexer_13_out), .out(multiplexer_22_out), .sel(b1_desloca_2));
  Multiplexer #(.enable("false")) multiplexer_23 (
    .in0(multiplexer_21_out), .in1(multiplexer_6_out), .out(multiplexer_23_out), .sel(b1_desloca_2));
  Multiplexer #(.enable("false")) multiplexer_24 (
    .in0(multiplexer_23_out), .in1(multiplexer_14_out), .out(out_7[28]), .sel(b0_desloca_1));
  Multiplexer #(.enable("false")) multiplexer_25 (
    .in0(multiplexer_22_out), .in1(multiplexer_23_out), .out(out_7[27]), .sel(b0_desloca_1));
  Multiplexer #(.enable("false")) multiplexer_26 (
    .in0(in_1[25]), .in1(in_1[10]), .out(multiplexer_26_out), .sel(b2_desloca_16));
  Multiplexer #(.enable("false")) multiplexer_27 (
    .in0(in_1[26]), .in1(in_1[11]), .out(multiplexer_27_out), .sel(b2_desloca_16));
  Multiplexer #(.enable("false")) multiplexer_28 (
    .in0(multiplexer_26_out), .in1(multiplexer_146_out), .out(multiplexer_28_out), .sel(b2_desloca_8));
  Multiplexer #(.enable("false")) multiplexer_29 (
    .in0(multiplexer_27_out), .in1(multiplexer_137_out), .out(multiplexer_29_out), .sel(b2_desloca_8));
  Multiplexer #(.enable("false")) multiplexer_30 (
    .in0(multiplexer_29_out), .in1(multiplexer_3_out), .out(multiplexer_30_out), .sel(b2_desloca_4));
  Multiplexer #(.enable("false")) multiplexer_31 (
    .in0(multiplexer_30_out), .in1(multiplexer_21_out), .out(multiplexer_31_out), .sel(b1_desloca_2));
  Multiplexer #(.enable("false")) multiplexer_32 (
    .in0(multiplexer_31_out), .in1(multiplexer_22_out), .out(out_7[26]), .sel(b0_desloca_1));
  Multiplexer #(.enable("false")) multiplexer_33 (
    .in0(in_1[24]), .in1(in_1[9]), .out(multiplexer_33_out), .sel(b2_desloca_16));
  Multiplexer #(.enable("false")) multiplexer_34 (
    .in0(multiplexer_33_out), .in1(multiplexer_147_out), .out(multiplexer_34_out), .sel(b2_desloca_8));
  Multiplexer #(.enable("false")) multiplexer_35 (
    .in0(multiplexer_28_out), .in1(multiplexer_12_out), .out(multiplexer_35_out), .sel(b2_desloca_4));
  Multiplexer #(.enable("false")) multiplexer_36 (
    .in0(multiplexer_34_out), .in1(multiplexer_18_out), .out(multiplexer_36_out), .sel(b2_desloca_4));
  Multiplexer #(.enable("false")) multiplexer_37 (
    .in0(multiplexer_35_out), .in1(multiplexer_20_out), .out(multiplexer_37_out), .sel(b1_desloca_2));
  Multiplexer #(.enable("false")) multiplexer_38 (
    .in0(multiplexer_36_out), .in1(multiplexer_30_out), .out(multiplexer_38_out), .sel(b1_desloca_2));
  Multiplexer #(.enable("false")) multiplexer_39 (
    .in0(multiplexer_37_out), .in1(multiplexer_31_out), .out(out_7[25]), .sel(b0_desloca_1));
  Multiplexer #(.enable("false")) multiplexer_40 (
    .in0(multiplexer_38_out), .in1(multiplexer_37_out), .out(out_7[24]), .sel(b0_desloca_1));
  Multiplexer #(.enable("false")) multiplexer_41 (
    .in0(in_1[22]), .in1(in_1[7]), .out(multiplexer_41_out), .sel(b2_desloca_16));
  Multiplexer #(.enable("false")) multiplexer_42 (
    .in0(in_1[23]), .in1(in_1[8]), .out(multiplexer_42_out), .sel(b2_desloca_16));
  Multiplexer #(.enable("false")) multiplexer_43 (
    .in0(multiplexer_41_out), .in1(multiplexer_2_out), .out(multiplexer_43_out), .sel(b2_desloca_8));
  Multiplexer #(.enable("false")) multiplexer_44 (
    .in0(multiplexer_42_out), .in1(multiplexer_153_out), .out(multiplexer_44_out), .sel(b2_desloca_8));
  Multiplexer #(.enable("false")) multiplexer_45 (
    .in0(multiplexer_43_out), .in1(multiplexer_29_out), .out(multiplexer_45_out), .sel(b2_desloca_4));
  Multiplexer #(.enable("false")) multiplexer_46 (
    .in0(multiplexer_44_out), .in1(multiplexer_19_out), .out(multiplexer_46_out), .sel(b2_desloca_4));
  Multiplexer #(.enable("false")) multiplexer_47 (
    .in0(multiplexer_45_out), .in1(multiplexer_36_out), .out(multiplexer_47_out), .sel(b1_desloca_2));
  Multiplexer #(.enable("false")) multiplexer_48 (
    .in0(multiplexer_46_out), .in1(multiplexer_35_out), .out(multiplexer_48_out), .sel(b1_desloca_2));
  Multiplexer #(.enable("false")) multiplexer_49 (
    .in0(multiplexer_48_out), .in1(multiplexer_38_out), .out(out_7[23]), .sel(b0_desloca_1));
  Multiplexer #(.enable("false")) multiplexer_50 (
    .in0(in_1[20]), .in1(in_1[5]), .out(multiplexer_50_out), .sel(b2_desloca_16));
  Multiplexer #(.enable("false")) multiplexer_51 (
    .in0(in_1[21]), .in1(in_1[6]), .out(multiplexer_51_out), .sel(b2_desloca_16));
  Multiplexer #(.enable("false")) multiplexer_52 (
    .in0(multiplexer_51_out), .in1(multiplexer_11_out), .out(multiplexer_52_out), .sel(b2_desloca_8));
  Multiplexer #(.enable("false")) multiplexer_53 (
    .in0(multiplexer_52_out), .in1(multiplexer_28_out), .out(multiplexer_53_out), .sel(b2_desloca_4));
  Multiplexer #(.enable("false")) multiplexer_54 (
    .in0(multiplexer_53_out), .in1(multiplexer_46_out), .out(multiplexer_54_out), .sel(b1_desloca_2));
  Multiplexer #(.enable("false")) multiplexer_55 (
    .in0(multiplexer_54_out), .in1(multiplexer_47_out), .out(out_7[21]), .sel(b0_desloca_1));
  Multiplexer #(.enable("false")) multiplexer_56 (
    .in0(multiplexer_47_out), .in1(multiplexer_48_out), .out(out_7[22]), .sel(b0_desloca_1));
  Multiplexer #(.enable("false")) multiplexer_57 (
    .in0(in_1[19]), .in1(in_1[4]), .out(multiplexer_57_out), .sel(b2_desloca_16));
  Multiplexer #(.enable("false")) multiplexer_58 (
    .in0(multiplexer_50_out), .in1(multiplexer_10_out), .out(multiplexer_58_out), .sel(b2_desloca_8));
  Multiplexer #(.enable("false")) multiplexer_59 (
    .in0(multiplexer_57_out), .in1(multiplexer_17_out), .out(multiplexer_59_out), .sel(b2_desloca_8));
  Multiplexer #(.enable("false")) multiplexer_60 (
    .in0(multiplexer_59_out), .in1(multiplexer_44_out), .out(multiplexer_60_out), .sel(b2_desloca_4));
  Multiplexer #(.enable("false")) multiplexer_61 (
    .in0(multiplexer_58_out), .in1(multiplexer_34_out), .out(multiplexer_61_out), .sel(b2_desloca_4));
  Multiplexer #(.enable("false")) multiplexer_62 (
    .in0(multiplexer_60_out), .in1(multiplexer_53_out), .out(multiplexer_62_out), .sel(b1_desloca_2));
  Multiplexer #(.enable("false")) multiplexer_63 (
    .in0(multiplexer_61_out), .in1(multiplexer_45_out), .out(multiplexer_63_out), .sel(b1_desloca_2));
  Multiplexer #(.enable("false")) multiplexer_64 (
    .in0(multiplexer_62_out), .in1(multiplexer_63_out), .out(out_7[19]), .sel(b0_desloca_1));
  Multiplexer #(.enable("false")) multiplexer_65 (
    .in0(multiplexer_63_out), .in1(multiplexer_54_out), .out(out_7[20]), .sel(b0_desloca_1));
  Multiplexer #(.enable("false")) multiplexer_66 (
    .in0(in_1[18]), .in1(in_1[3]), .out(multiplexer_66_out), .sel(b2_desloca_16));
  Multiplexer #(.enable("false")) multiplexer_67 (
    .in0(in_1[17]), .in1(in_1[2]), .out(multiplexer_67_out), .sel(b2_desloca_16));
  Multiplexer #(.enable("false")) multiplexer_68 (
    .in0(multiplexer_67_out), .in1(multiplexer_26_out), .out(multiplexer_68_out), .sel(b2_desloca_8));
  Multiplexer #(.enable("false")) multiplexer_69 (
    .in0(multiplexer_66_out), .in1(multiplexer_27_out), .out(multiplexer_69_out), .sel(b2_desloca_8));
  Multiplexer #(.enable("false")) multiplexer_70 (
    .in0(multiplexer_69_out), .in1(multiplexer_43_out), .out(multiplexer_70_out), .sel(b2_desloca_4));
  Multiplexer #(.enable("false")) multiplexer_71 (
    .in0(multiplexer_70_out), .in1(multiplexer_61_out), .out(multiplexer_71_out), .sel(b1_desloca_2));
  Multiplexer #(.enable("false")) multiplexer_72 (
    .in0(multiplexer_71_out), .in1(multiplexer_62_out), .out(out_7[18]), .sel(b0_desloca_1));
  Multiplexer #(.enable("false")) multiplexer_73 (
    .in0(in_1[16]), .in1(in_1[1]), .out(multiplexer_73_out), .sel(b2_desloca_16));
  Multiplexer #(.enable("false")) multiplexer_74 (
    .in0(multiplexer_73_out), .in1(multiplexer_33_out), .out(multiplexer_74_out), .sel(b2_desloca_8));
  Multiplexer #(.enable("false")) multiplexer_75 (
    .in0(multiplexer_68_out), .in1(multiplexer_52_out), .out(multiplexer_75_out), .sel(b2_desloca_4));
  Multiplexer #(.enable("false")) multiplexer_76 (
    .in0(multiplexer_74_out), .in1(multiplexer_58_out), .out(multiplexer_76_out), .sel(b2_desloca_4));
  Multiplexer #(.enable("false")) multiplexer_77 (
    .in0(multiplexer_76_out), .in1(multiplexer_70_out), .out(multiplexer_77_out), .sel(b1_desloca_2));
  Multiplexer #(.enable("false")) multiplexer_78 (
    .in0(multiplexer_75_out), .in1(multiplexer_60_out), .out(multiplexer_78_out), .sel(b1_desloca_2));
  Multiplexer #(.enable("false")) multiplexer_79 (
    .in0(multiplexer_78_out), .in1(multiplexer_71_out), .out(out_7[17]), .sel(b0_desloca_1));
  Multiplexer #(.enable("false")) multiplexer_80 (
    .in0(multiplexer_77_out), .in1(multiplexer_78_out), .out(out_7[16]), .sel(b0_desloca_1));
  Multiplexer #(.enable("false")) multiplexer_81 (
    .in0(in_1[14]), .in1(in_1[30]), .out(multiplexer_81_out), .sel(b2_desloca_16));
  Multiplexer #(.enable("false")) multiplexer_82 (
    .in0(in_1[15]), .in1(in_1[0]), .out(multiplexer_82_out), .sel(b2_desloca_16));
  Multiplexer #(.enable("false")) multiplexer_83 (
    .in0(multiplexer_82_out), .in1(multiplexer_42_out), .out(multiplexer_83_out), .sel(b2_desloca_8));
  Multiplexer #(.enable("false")) multiplexer_84 (
    .in0(multiplexer_81_out), .in1(multiplexer_41_out), .out(multiplexer_84_out), .sel(b2_desloca_8));
  Multiplexer #(.enable("false")) multiplexer_85 (
    .in0(multiplexer_83_out), .in1(multiplexer_59_out), .out(multiplexer_85_out), .sel(b2_desloca_4));
  Multiplexer #(.enable("false")) multiplexer_86 (
    .in0(multiplexer_84_out), .in1(multiplexer_69_out), .out(multiplexer_86_out), .sel(b2_desloca_4));
  Multiplexer #(.enable("false")) multiplexer_87 (
    .in0(multiplexer_85_out), .in1(multiplexer_75_out), .out(multiplexer_87_out), .sel(b1_desloca_2));
  Multiplexer #(.enable("false")) multiplexer_88 (
    .in0(multiplexer_86_out), .in1(multiplexer_76_out), .out(multiplexer_88_out), .sel(b1_desloca_2));
  Multiplexer #(.enable("false")) multiplexer_89 (
    .in0(multiplexer_87_out), .in1(multiplexer_77_out), .out(out_7[15]), .sel(b0_desloca_1));
  Multiplexer #(.enable("false")) multiplexer_90 (
    .in0(in_1[13]), .in1(in_1[29]), .out(multiplexer_90_out), .sel(b2_desloca_16));
  Multiplexer #(.enable("false")) multiplexer_91 (
    .in0(in_1[12]), .in1(in_1[28]), .out(multiplexer_91_out), .sel(b2_desloca_16));
  Multiplexer #(.enable("false")) multiplexer_92 (
    .in0(multiplexer_90_out), .in1(multiplexer_51_out), .out(multiplexer_92_out), .sel(b2_desloca_8));
  Multiplexer #(.enable("false")) multiplexer_93 (
    .in0(multiplexer_92_out), .in1(multiplexer_68_out), .out(multiplexer_93_out), .sel(b2_desloca_4));
  Multiplexer #(.enable("false")) multiplexer_94 (
    .in0(multiplexer_93_out), .in1(multiplexer_85_out), .out(multiplexer_94_out), .sel(b1_desloca_2));
  Multiplexer #(.enable("false")) multiplexer_95 (
    .in0(multiplexer_88_out), .in1(multiplexer_87_out), .out(out_7[14]), .sel(b0_desloca_1));
  Multiplexer #(.enable("false")) multiplexer_96 (
    .in0(multiplexer_94_out), .in1(multiplexer_88_out), .out(out_7[13]), .sel(b0_desloca_1));
  Multiplexer #(.enable("false")) multiplexer_97 (
    .in0(in_1[11]), .in1(in_1[27]), .out(multiplexer_97_out), .sel(b2_desloca_16));
  Multiplexer #(.enable("false")) multiplexer_98 (
    .in0(multiplexer_91_out), .in1(multiplexer_50_out), .out(multiplexer_98_out), .sel(b2_desloca_8));
  Multiplexer #(.enable("false")) multiplexer_99 (
    .in0(multiplexer_97_out), .in1(multiplexer_57_out), .out(multiplexer_99_out), .sel(b2_desloca_8));
  Multiplexer #(.enable("false")) multiplexer_100 (
    .in0(multiplexer_99_out), .in1(multiplexer_83_out), .out(multiplexer_100_out), .sel(b2_desloca_4));
  Multiplexer #(.enable("false")) multiplexer_101 (
    .in0(multiplexer_98_out), .in1(multiplexer_74_out), .out(multiplexer_101_out), .sel(b2_desloca_4));
  Multiplexer #(.enable("false")) multiplexer_102 (
    .in0(multiplexer_101_out), .in1(multiplexer_86_out), .out(multiplexer_102_out), .sel(b1_desloca_2));
  Multiplexer #(.enable("false")) multiplexer_103 (
    .in0(multiplexer_100_out), .in1(multiplexer_93_out), .out(multiplexer_103_out), .sel(b1_desloca_2));
  Multiplexer #(.enable("false")) multiplexer_104 (
    .in0(multiplexer_102_out), .in1(multiplexer_94_out), .out(out_7[12]), .sel(b0_desloca_1));
  Multiplexer #(.enable("false")) multiplexer_105 (
    .in0(multiplexer_103_out), .in1(multiplexer_102_out), .out(out_7[11]), .sel(b0_desloca_1));
  Multiplexer #(.enable("false")) multiplexer_106 (
    .in0(in_1[10]), .in1(in_1[26]), .out(multiplexer_106_out), .sel(b2_desloca_16));
  Multiplexer #(.enable("false")) multiplexer_107 (
    .in0(in_1[9]), .in1(in_1[25]), .out(multiplexer_107_out), .sel(b2_desloca_16));
  Multiplexer #(.enable("false")) multiplexer_108 (
    .in0(multiplexer_107_out), .in1(multiplexer_67_out), .out(multiplexer_108_out), .sel(b2_desloca_8));
  Multiplexer #(.enable("false")) multiplexer_109 (
    .in0(multiplexer_106_out), .in1(multiplexer_66_out), .out(multiplexer_109_out), .sel(b2_desloca_8));
  Multiplexer #(.enable("false")) multiplexer_110 (
    .in0(multiplexer_109_out), .in1(multiplexer_84_out), .out(multiplexer_110_out), .sel(b2_desloca_4));
  Multiplexer #(.enable("false")) multiplexer_111 (
    .in0(multiplexer_110_out), .in1(multiplexer_101_out), .out(multiplexer_111_out), .sel(b1_desloca_2));
  Multiplexer #(.enable("false")) multiplexer_112 (
    .in0(multiplexer_111_out), .in1(multiplexer_103_out), .out(out_7[10]), .sel(b0_desloca_1));
  Multiplexer #(.enable("false")) multiplexer_113 (
    .in0(in_1[8]), .in1(in_1[24]), .out(multiplexer_113_out), .sel(b2_desloca_16));
  Multiplexer #(.enable("false")) multiplexer_114 (
    .in0(multiplexer_113_out), .in1(multiplexer_73_out), .out(multiplexer_114_out), .sel(b2_desloca_8));
  Multiplexer #(.enable("false")) multiplexer_115 (
    .in0(multiplexer_108_out), .in1(multiplexer_92_out), .out(multiplexer_115_out), .sel(b2_desloca_4));
  Multiplexer #(.enable("false")) multiplexer_116 (
    .in0(multiplexer_114_out), .in1(multiplexer_98_out), .out(multiplexer_116_out), .sel(b2_desloca_4));
  Multiplexer #(.enable("false")) multiplexer_117 (
    .in0(multiplexer_115_out), .in1(multiplexer_100_out), .out(multiplexer_117_out), .sel(b1_desloca_2));
  Multiplexer #(.enable("false")) multiplexer_118 (
    .in0(multiplexer_116_out), .in1(multiplexer_110_out), .out(multiplexer_118_out), .sel(b1_desloca_2));
  Multiplexer #(.enable("false")) multiplexer_119 (
    .in0(multiplexer_118_out), .in1(multiplexer_117_out), .out(out_7[8]), .sel(b0_desloca_1));
  Multiplexer #(.enable("false")) multiplexer_120 (
    .in0(multiplexer_117_out), .in1(multiplexer_111_out), .out(out_7[9]), .sel(b0_desloca_1));
  Multiplexer #(.enable("false")) multiplexer_121 (
    .in0(in_1[7]), .in1(in_1[23]), .out(multiplexer_121_out), .sel(b2_desloca_16));
  Multiplexer #(.enable("false")) multiplexer_122 (
    .in0(in_1[6]), .in1(in_1[22]), .out(multiplexer_122_out), .sel(b2_desloca_16));
  Multiplexer #(.enable("false")) multiplexer_123 (
    .in0(multiplexer_121_out), .in1(multiplexer_82_out), .out(multiplexer_123_out), .sel(b2_desloca_8));
  Multiplexer #(.enable("false")) multiplexer_124 (
    .in0(multiplexer_122_out), .in1(multiplexer_81_out), .out(multiplexer_124_out), .sel(b2_desloca_8));
  Multiplexer #(.enable("false")) multiplexer_125 (
    .in0(multiplexer_123_out), .in1(multiplexer_99_out), .out(multiplexer_125_out), .sel(b2_desloca_4));
  Multiplexer #(.enable("false")) multiplexer_126 (
    .in0(multiplexer_124_out), .in1(multiplexer_109_out), .out(multiplexer_126_out), .sel(b2_desloca_4));
  Multiplexer #(.enable("false")) multiplexer_127 (
    .in0(multiplexer_126_out), .in1(multiplexer_116_out), .out(multiplexer_127_out), .sel(b1_desloca_2));
  Multiplexer #(.enable("false")) multiplexer_128 (
    .in0(multiplexer_125_out), .in1(multiplexer_115_out), .out(multiplexer_128_out), .sel(b1_desloca_2));
  Multiplexer #(.enable("false")) multiplexer_129 (
    .in0(multiplexer_128_out), .in1(multiplexer_118_out), .out(out_7[7]), .sel(b0_desloca_1));
  Multiplexer #(.enable("false")) multiplexer_130 (
    .in0(in_1[5]), .in1(in_1[21]), .out(multiplexer_130_out), .sel(b2_desloca_16));
  Multiplexer #(.enable("false")) multiplexer_131 (
    .in0(in_1[4]), .in1(in_1[20]), .out(multiplexer_131_out), .sel(b2_desloca_16));
  Multiplexer #(.enable("false")) multiplexer_132 (
    .in0(multiplexer_130_out), .in1(multiplexer_90_out), .out(multiplexer_132_out), .sel(b2_desloca_8));
  Multiplexer #(.enable("false")) multiplexer_133 (
    .in0(multiplexer_132_out), .in1(multiplexer_108_out), .out(multiplexer_133_out), .sel(b2_desloca_4));
  Multiplexer #(.enable("false")) multiplexer_134 (
    .in0(multiplexer_133_out), .in1(multiplexer_125_out), .out(multiplexer_134_out), .sel(b1_desloca_2));
  Multiplexer #(.enable("false")) multiplexer_135 (
    .in0(multiplexer_134_out), .in1(multiplexer_127_out), .out(out_7[5]), .sel(b0_desloca_1));
  Multiplexer #(.enable("false")) multiplexer_136 (
    .in0(multiplexer_127_out), .in1(multiplexer_128_out), .out(out_7[6]), .sel(b0_desloca_1));
  Multiplexer #(.enable("false")) multiplexer_137 (
    .in0(in_1[3]), .in1(in_1[19]), .out(multiplexer_137_out), .sel(b2_desloca_16));
  Multiplexer #(.enable("false")) multiplexer_138 (
    .in0(multiplexer_137_out), .in1(multiplexer_97_out), .out(multiplexer_138_out), .sel(b2_desloca_8));
  Multiplexer #(.enable("false")) multiplexer_139 (
    .in0(multiplexer_131_out), .in1(multiplexer_91_out), .out(multiplexer_139_out), .sel(b2_desloca_8));
  Multiplexer #(.enable("false")) multiplexer_140 (
    .in0(multiplexer_139_out), .in1(multiplexer_114_out), .out(multiplexer_140_out), .sel(b2_desloca_4));
  Multiplexer #(.enable("false")) multiplexer_141 (
    .in0(multiplexer_138_out), .in1(multiplexer_123_out), .out(multiplexer_141_out), .sel(b2_desloca_4));
  Multiplexer #(.enable("false")) multiplexer_142 (
    .in0(multiplexer_141_out), .in1(multiplexer_133_out), .out(multiplexer_142_out), .sel(b1_desloca_2));
  Multiplexer #(.enable("false")) multiplexer_143 (
    .in0(multiplexer_140_out), .in1(multiplexer_126_out), .out(multiplexer_143_out), .sel(b1_desloca_2));
  Multiplexer #(.enable("false")) multiplexer_144 (
    .in0(multiplexer_142_out), .in1(multiplexer_143_out), .out(out_7[3]), .sel(b0_desloca_1));
  Multiplexer #(.enable("false")) multiplexer_145 (
    .in0(multiplexer_143_out), .in1(multiplexer_134_out), .out(out_7[4]), .sel(b0_desloca_1));
  Multiplexer #(.enable("false")) multiplexer_146 (
    .in0(in_1[2]), .in1(in_1[18]), .out(multiplexer_146_out), .sel(b2_desloca_16));
  Multiplexer #(.enable("false")) multiplexer_147 (
    .in0(in_1[1]), .in1(in_1[17]), .out(multiplexer_147_out), .sel(b2_desloca_16));
  Multiplexer #(.enable("false")) multiplexer_148 (
    .in0(multiplexer_147_out), .in1(multiplexer_107_out), .out(multiplexer_148_out), .sel(b2_desloca_8));
  Multiplexer #(.enable("false")) multiplexer_149 (
    .in0(multiplexer_146_out), .in1(multiplexer_106_out), .out(multiplexer_149_out), .sel(b2_desloca_8));
  Multiplexer #(.enable("false")) multiplexer_150 (
    .in0(multiplexer_149_out), .in1(multiplexer_124_out), .out(multiplexer_150_out), .sel(b2_desloca_4));
  Multiplexer #(.enable("false")) multiplexer_151 (
    .in0(multiplexer_150_out), .in1(multiplexer_140_out), .out(multiplexer_151_out), .sel(b1_desloca_2));
  Multiplexer #(.enable("false")) multiplexer_152 (
    .in0(multiplexer_151_out), .in1(multiplexer_142_out), .out(out_7[2]), .sel(b0_desloca_1));
  Multiplexer #(.enable("false")) multiplexer_153 (
    .in0(in_1[0]), .in1(in_1[16]), .out(multiplexer_153_out), .sel(b2_desloca_16));
  Multiplexer #(.enable("false")) multiplexer_154 (
    .in0(multiplexer_153_out), .in1(multiplexer_113_out), .out(multiplexer_154_out), .sel(b2_desloca_8));
  Multiplexer #(.enable("false")) multiplexer_155 (
    .in0(multiplexer_148_out), .in1(multiplexer_132_out), .out(multiplexer_155_out), .sel(b2_desloca_4));
  Multiplexer #(.enable("false")) multiplexer_156 (
    .in0(multiplexer_154_out), .in1(multiplexer_139_out), .out(multiplexer_156_out), .sel(b2_desloca_4));
  Multiplexer #(.enable("false")) multiplexer_157 (
    .in0(multiplexer_156_out), .in1(multiplexer_150_out), .out(multiplexer_157_out), .sel(b1_desloca_2));
  Multiplexer #(.enable("false")) multiplexer_158 (
    .in0(multiplexer_155_out), .in1(multiplexer_141_out), .out(multiplexer_158_out), .sel(b1_desloca_2));
  Multiplexer #(.enable("false")) multiplexer_159 (
    .in0(multiplexer_158_out), .in1(multiplexer_151_out), .out(out_7[1]), .sel(b0_desloca_1));
  Multiplexer #(.enable("false")) multiplexer_160 (
    .in0(multiplexer_157_out), .in1(multiplexer_158_out), .out(out_7[0]), .sel(b0_desloca_1));
endmodule
